// Logisim project cpu28going版.circ as structural Verilog: 26 circuits, main circuit ◇重定向流水线
module \单周期MIPS  (
);

  wire and_1_out, and_2_out, and_3_out, and_4_out, Beq, BGTZ, Bne, branch, CLK, eq, eq34, Go, JAL, JMP, JR,
       LBU, les, not_1_out, or_2_out, RegDst, RST, Run, SignedExt, SRLV, Sys, \硬布线控制器_1_alu_src ,
       \硬布线控制器_1_memtoreg , \硬布线控制器_1_memwrite , \硬布线控制器_1_regwrite ;
  wire [3:0] \硬布线控制器_1_alu_op ;
  wire [4:0] multiplexer_4_out, multiplexer_5_out, multiplexer_6_out, multiplexer_7_out, multiplexer_12_out,
       Shamt;
  wire [7:0] ByteEx;
  wire [15:0] \总周期数 , \无条件分支数 , \条件分支成功数 ;
  wire [27:0] nextPC;
  wire [31:0] bit_extender_1_out, bit_extender_2_out, branchPC, Din, Jaddr, LedData, mips_probe_1_p2,
       mips_ram_1_p7, multiplexer_1_out, multiplexer_2_out, multiplexer_3_out, multiplexer_8_out,
       multiplexer_9_out, multiplexer_10_out, multiplexer_11_out, PC_q, R1, R2, shifter_2_out;
  wire [31:1] Result;

  Button \u_总复位  (.out(RST));
  Button \u_继续运行  (.out(Go));
  Clock clock_1 (.out(CLK));
  Multiplexer #(.width(32), .disabled(0), .enable("false")) multiplexer_1 (
    .in0({Jaddr[31:28], nextPC}), .in1(branchPC), .out(multiplexer_1_out), .sel(branch));
  Multiplexer #(.width(32), .disabled(0), .enable("false")) multiplexer_2 (
    .in0(multiplexer_1_out), .in1(Jaddr), .out(multiplexer_2_out), .sel(JMP));
  Hex_Digit_Display hex_digit_display_1 (.value(LedData[31:28]));  // open: dp
  Hex_Digit_Display hex_digit_display_2 (.value(LedData[27:24]));  // open: dp
  not not_1 (not_1_out, Sys);
  or or_1 (Run, Go, not_1_out, eq34);
  Register #(.width(32)) PC (.D(multiplexer_3_out), .en(Run), .Q(PC_q), .clk(CLK), .clr(RST));
  Multiplexer #(.width(32), .disabled(0), .enable("false")) multiplexer_3 (
    .in0(multiplexer_2_out), .in1(R1), .out(multiplexer_3_out), .sel(JR));
  Hex_Digit_Display hex_digit_display_3 (.value(LedData[23:20]));  // open: dp
  Hex_Digit_Display hex_digit_display_4 (.value(LedData[19:16]));  // open: dp
  Register #(.width(32)) register_1 (.D(R2), .en(eq34), .Q(LedData), .clk(CLK));  // open: clr
  Hex_Digit_Display hex_digit_display_5 (.value(LedData[15:12]));  // open: dp
  Hex_Digit_Display hex_digit_display_6 (.value(LedData[11:8]));  // open: dp
  Adder #(.width(32)) adder_1 (.a(PC_q), .b(32'h4), .out({Jaddr[31:28], nextPC}), .cin(1'b0));  // open: cout
  // Mips_Probe mips_probe_1: pin names not known; wires that end beside it: 32'h4, {mips_probe_1_p2[31:11], Shamt, mips_probe_1_p2[5:0]}
  Hex_Digit_Display hex_digit_display_7 (.value(LedData[3:0]));  // open: dp
  Hex_Digit_Display hex_digit_display_8 (.value(LedData[7:4]));  // open: dp
  ROM #(.addrWidth(10), .dataWidth(32)) rom_1 (
    .addr(PC_q[11:2]), .data({mips_probe_1_p2[31:11], Shamt, mips_probe_1_p2[5:0]}));  // open: sel
  \硬布线控制器  \u_硬布线控制器_1  (
    .Func(mips_probe_1_p2[5:0]), .OP(mips_probe_1_p2[31:26]), .ALU_OP(\硬布线控制器_1_alu_op ),
    .MemToReg(\硬布线控制器_1_memtoreg ), .MemWrite(\硬布线控制器_1_memwrite ), .ALU_SRC(\硬布线控制器_1_alu_src ),
    .RegWrite(\硬布线控制器_1_regwrite ), .SysCALL(Sys), .SignedExt(SignedExt), .RegDst(RegDst), .JR(JR),
    .JMP(JMP), .Beq(Beq), .JAL(JAL), .Bne(Bne), .SRLV(SRLV), .LBU(LBU), .BGTZ(BGTZ));
  Multiplexer #(.width(5), .disabled(0), .enable("false")) multiplexer_4 (
    .in0(mips_probe_1_p2[25:21]), .in1(5'b00010), .out(multiplexer_4_out), .sel(Sys));
  Multiplexer #(.width(5), .disabled(0), .enable("false")) multiplexer_5 (
    .in0(mips_probe_1_p2[20:16]), .in1(5'b00100), .out(multiplexer_5_out), .sel(Sys));
  Multiplexer #(.width(5), .disabled(0), .enable("false")) multiplexer_6 (
    .in0(mips_probe_1_p2[20:16]), .in1(mips_probe_1_p2[15:11]), .out(multiplexer_6_out), .sel(RegDst));
  assign bit_extender_1_out = {{16{mips_probe_1_p2[15]}}, {mips_probe_1_p2[15:11], Shamt, mips_probe_1_p2[5:0]}};  // Bit_Extender bit_extender_1
  // Probe on \总周期数 
  // Probe on \无条件分支数 
  // Probe on \条件分支成功数 
  Multiplexer #(.width(5), .disabled(0), .enable("false")) multiplexer_7 (
    .in0(multiplexer_6_out), .in1({5{1'b1}}), .out(multiplexer_7_out), .sel(JAL));
  Multiplexer #(.width(32), .disabled(0), .enable("false")) multiplexer_8 (
    .in0(Din), .in1({Jaddr[31:28], nextPC}), .out(multiplexer_8_out), .sel(JAL));
  assign bit_extender_2_out = {{16{1'b0}}, {mips_probe_1_p2[15:11], Shamt, mips_probe_1_p2[5:0]}};  // Bit_Extender bit_extender_2
  Shifter #(.width(28)) shifter_1 (
    .in({2'b00, mips_probe_1_p2[25:11], Shamt, mips_probe_1_p2[5:0]}), .\dist (5'b00010), .out(Jaddr[27:0]));
  Multiplexer #(.width(32), .disabled(0), .enable("false")) multiplexer_9 (
    .in0(multiplexer_8_out), .in1({{24{1'b0}}, ByteEx}), .out(multiplexer_9_out), .sel(LBU));
  Multiplexer #(.width(32), .disabled(0), .enable("false")) multiplexer_10 (
    .in0(bit_extender_2_out), .in1(bit_extender_1_out), .out(multiplexer_10_out), .sel(SignedExt));
  MIPS_Regifile mips_regifile_1 (
    .Din(multiplexer_9_out), .Clk(CLK), .R1(R1), .R2(R2), .WE(\硬布线控制器_1_regwrite ),
    .W_num(multiplexer_7_out), .R1_num(multiplexer_4_out), .R2_num(multiplexer_5_out));
  Shifter #(.width(32)) shifter_2 (.in(bit_extender_1_out), .\dist (5'b00010), .out(shifter_2_out));
  or or_2 (or_2_out, JAL, JMP, JR);
  Comparator #(.width(32)) comparator_1 (.a(32'h22), .b(R1), .eq(eq34));  // open: gt, lt
  Adder #(.width(32)) adder_2 (.a(shifter_2_out), .b({Jaddr[31:28], nextPC}), .out(branchPC));  // open: cin, cout
  Counter #(.width(16), .max('hffff)) counter_1 (
    .count(Run), .Q(\总周期数 ), .clk(CLK), .clr(RST));  // open: load, D, carry
  Counter #(.width(16), .max('hffff)) counter_2 (
    .count(or_2_out), .Q(\无条件分支数 ), .clk(CLK), .clr(RST));  // open: load, D, carry
  Multiplexer #(.width(32), .disabled(0), .enable("false")) multiplexer_11 (
    .in0(R2), .in1(multiplexer_10_out), .out(multiplexer_11_out), .sel(\硬布线控制器_1_alu_src ));
  // Probe on multiplexer_10_out
  Multiplexer #(.width(5), .disabled(0), .enable("false")) multiplexer_12 (
    .in0(Shamt), .in1(R1[4:0]), .out(multiplexer_12_out), .sel(SRLV));
  MIPS_ALU mips_alu_1 (
    .X(R1), .Y(multiplexer_11_out), .AluOP(\硬布线控制器_1_alu_op ), .Equal(eq), .Result({Result, les}),
    .shamt(multiplexer_12_out));  // open: Result_2
  Multiplexer #(.select(2), .width(8), .disabled(0), .enable("false")) multiplexer_13 (
    .in0(Din[7:0]), .in1(Din[15:8]), .in2(Din[23:16]), .in3(Din[31:24]), .out(ByteEx), .sel({Result[1], les}));
  and and_1 (and_1_out, BGTZ, and_2_out);
  and and_2 (and_2_out, ~eq, ~les);  // AND_Gate
  // Probe on Result[21:2]
  and and_3 (and_3_out, ~eq, Bne);  // AND_Gate
  // MIPS_RAM mips_ram_1: pin names not known; wires that end beside it: Result[21:2], R2, \硬布线控制器_1_memwrite , CLK, \硬布线控制器_1_memtoreg , RST, mips_ram_1_p7
  and and_4 (and_4_out, eq, Beq);
  or or_3 (branch, and_4_out, and_1_out, and_3_out);
  Multiplexer #(.width(32), .disabled(0), .enable("false")) multiplexer_14 (
    .in0({Result, les}), .in1(mips_ram_1_p7), .out(Din), .sel(\硬布线控制器_1_memtoreg ));
  Counter #(.width(16), .max('hffff)) counter_3 (
    .count(branch), .Q(\条件分支成功数 ), .clk(CLK), .clr(RST));  // open: load, D, carry

  // Other names for the same wires on the sheet: nextPC[31:28] = Jaddr[31:28]; Result[0] = les

  // Notes on the sheet:
  //   数码管输出应该用寄存器锁存，否则显示数据只能一闪而过
  //   可以通过项目增加Logisim库的方式将前几次实验完成的电路作为子电路引入到本电路中使用
  //   指令存储器
  //   数码管输出
  //   contents of rom_1 (hex, n*v repeats v):
  //   2011000f 112020 20020022 c 2231ffff 1e20fffb 2002000a c
  //   总复位信号应将除ROM以外所有存储组件全部清零
  //   rs
  //   rt
  //   rd
  //   Beq
  //   JMP
  //   JR
  //   Bne
  //   OP
  //   JAL
  //   Func
  //   Syscall
  //   MemToReg
  //   MemWrite
  //   AluOP
  //   AluSrcB
  //   RegWrite
  //   RegDst
endmodule

// 单周期硬布线控制器
module \硬布线控制器  (
  input  [5:0] OP,
  input  [5:0] Func,
  output [3:0] ALU_OP,
  output MemToReg,
  output MemWrite,
  output ALU_SRC,
  output RegWrite,
  output SysCALL,
  output SignedExt,
  output RegDst,
  output Beq,
  output Bne,
  output JR,
  output JMP,
  output JAL,
  output SRLV,
  output LBU,
  output BGTZ
);

  \运算控制器  \u_运算控制器_1  (
    .OP0(OP[0]), .OP1(OP[1]), .OP2(OP[2]), .OP3(OP[3]), .OP4(OP[4]), .OP5(OP[5]), .F0(Func[0]), .F1(Func[1]),
    .F2(Func[2]), .F3(Func[3]), .F4(Func[4]), .F5(Func[5]), .S0(ALU_OP[0]), .S1(ALU_OP[1]), .S2(ALU_OP[2]),
    .S3(ALU_OP[3]));
  \控制信号生成  \u_控制信号生成_1  (
    .OP0(OP[0]), .OP1(OP[1]), .OP2(OP[2]), .OP3(OP[3]), .OP4(OP[4]), .OP5(OP[5]), .F0(Func[0]), .F1(Func[1]),
    .F2(Func[2]), .F3(Func[3]), .F4(Func[4]), .F5(Func[5]), .MemToReg(MemToReg), .MemWrite(MemWrite),
    .ALU_SRC(ALU_SRC), .RegWrite(RegWrite), .SysCALL(SysCALL), .SignedExt(SignedExt), .RegDst(RegDst),
    .BEQ(Beq), .BNE(Bne), .JR(JR), .JMP(JMP), .JAL(JAL));
  \控制信号生成2  \u_控制信号生成2_1  (
    .OP0(OP[0]), .OP1(OP[1]), .OP2(OP[2]), .OP3(OP[3]), .SRLV(SRLV), .OP4(OP[4]), .OP5(OP[5]), .F0(Func[0]),
    .F1(Func[1]), .LBU(LBU), .F2(Func[2]), .F3(Func[3]), .F4(Func[4]), .BGTZ(BGTZ), .F5(Func[5]));

  // Other names for the same wires on the sheet: OP_CODE[5:0] = OP

  // Notes on the sheet:
  //   运算器控制器，根据指令生成运算器功能选择信号
  //   控制信号生成，产生数据通路需要的其他控制信号
endmodule

// 运算器控制器
module \运算控制器  (
  input  OP0,
  input  OP1,
  input  OP2,
  input  OP3,
  input  OP4,
  input  OP5,
  input  F0,
  input  F1,
  input  F2,
  input  F3,
  input  F4,
  input  F5,
  output S0,
  output S1,
  output S2,
  output S3
);

  wire and_1_out, and_2_out, and_3_out, and_4_out, and_5_out, and_6_out, and_7_out, and_8_out, and_9_out,
       and_10_out, and_11_out, and_12_out, and_13_out, and_14_out, and_15_out, and_16_out, and_17_out,
       and_18_out, and_19_out, and_20_out, and_21_out, and_22_out, and_23_out, and_24_out, and_25_out,
       and_26_out, and_27_out, and_28_out, and_29_out, and_30_out, and_31_out, and_32_out, and_33_out,
       and_34_out, and_35_out, and_36_out, and_37_out, and_38_out, and_39_out, and_40_out, and_41_out,
       and_42_out, not_1_out, not_2_out, not_3_out, not_4_out, not_5_out, not_6_out, not_7_out, not_8_out,
       not_9_out, not_10_out, not_11_out, not_12_out, not_13_out, not_14_out, not_15_out, not_16_out,
       not_17_out, not_18_out, not_19_out, not_20_out, not_21_out, not_22_out, not_23_out, not_24_out,
       not_25_out, not_26_out, not_27_out, not_28_out, not_29_out, not_30_out, not_31_out, not_32_out,
       not_33_out, not_34_out, not_35_out, not_36_out, not_37_out, not_38_out, not_39_out, not_40_out,
       not_41_out, not_42_out, not_43_out, not_44_out, not_45_out, not_46_out, not_47_out, not_48_out,
       not_49_out, not_50_out, not_51_out, not_52_out, not_53_out, not_54_out, not_55_out, not_56_out,
       not_57_out, not_58_out, not_59_out, not_60_out, not_61_out, not_62_out, not_63_out, not_64_out,
       not_65_out, not_66_out, not_67_out, not_68_out, not_69_out, not_70_out, not_71_out, not_72_out,
       not_73_out, not_74_out, not_75_out, not_76_out, not_77_out, not_78_out, not_79_out, not_80_out,
       not_81_out, not_82_out, not_83_out, not_84_out, not_85_out, not_86_out, not_87_out, not_88_out,
       not_89_out, not_90_out, not_91_out, not_92_out, not_93_out, not_94_out, not_95_out, not_96_out,
       not_97_out, not_98_out, not_99_out, not_100_out, not_101_out, not_102_out, not_103_out, not_104_out,
       not_105_out, not_106_out, not_107_out, not_108_out, not_109_out, not_110_out, not_111_out,
       not_112_out, not_113_out, not_114_out, not_115_out, not_116_out, not_117_out, not_118_out,
       not_119_out, not_120_out, not_121_out, not_122_out, not_123_out, not_124_out, not_125_out,
       not_126_out, not_127_out, not_128_out, not_129_out, not_130_out, not_131_out, not_132_out,
       not_133_out, not_134_out, not_135_out, not_136_out, not_137_out, not_138_out, not_139_out,
       not_140_out, not_141_out, not_142_out, not_143_out, not_144_out, not_145_out, not_146_out,
       not_147_out, not_148_out, not_149_out, not_150_out, not_151_out, not_152_out, not_153_out,
       not_154_out, not_155_out, not_156_out, not_157_out, not_158_out, not_159_out, not_160_out,
       not_161_out, not_162_out, not_163_out, not_164_out, not_165_out, not_166_out, not_167_out,
       not_168_out, not_169_out, not_170_out, not_171_out, not_172_out, not_173_out, not_174_out,
       not_175_out, not_176_out, not_177_out, not_178_out, not_179_out, not_180_out, not_181_out,
       not_182_out, not_183_out, not_184_out, not_185_out, not_186_out, not_187_out, not_188_out,
       not_189_out, not_190_out, not_191_out, not_192_out, not_193_out, not_194_out, not_195_out,
       not_196_out, not_197_out, not_198_out, not_199_out, not_200_out, not_201_out, not_202_out,
       not_203_out, not_204_out, not_205_out, not_206_out, not_207_out, not_208_out, not_209_out,
       not_210_out, not_211_out, not_212_out, not_213_out, not_214_out, not_215_out, not_216_out,
       not_217_out, not_218_out, not_219_out, not_220_out, not_221_out, not_222_out, not_223_out,
       not_224_out, not_225_out, not_226_out, not_227_out, not_228_out, not_229_out, not_230_out,
       not_231_out, not_232_out, not_233_out, not_234_out, not_235_out, not_236_out, not_237_out,
       not_238_out, not_239_out, not_240_out, not_241_out, not_242_out, not_243_out, not_244_out,
       not_245_out, not_246_out, not_247_out, not_248_out, not_249_out, not_250_out, not_251_out,
       not_252_out, not_253_out, not_254_out, not_255_out, not_256_out, not_257_out, not_258_out,
       not_259_out, not_260_out, not_261_out, not_262_out, not_263_out, not_264_out, not_265_out,
       not_266_out, not_267_out, not_268_out, not_269_out, not_270_out, not_271_out, not_272_out,
       not_273_out, not_274_out, not_275_out, not_276_out, not_277_out, not_278_out, not_279_out,
       not_280_out, not_281_out;

  not not_1 (not_1_out, OP5);
  not not_2 (not_2_out, OP4);
  not not_3 (not_3_out, OP3);
  not not_4 (not_4_out, OP2);
  not not_5 (not_5_out, OP1);
  not not_6 (not_6_out, OP0);
  not not_7 (not_7_out, F5);
  not not_8 (not_8_out, F4);
  not not_9 (not_9_out, F3);
  not not_10 (not_10_out, F2);
  not not_11 (not_11_out, OP5);
  not not_12 (not_12_out, OP4);
  not not_13 (not_13_out, OP3);
  not not_14 (not_14_out, OP2);
  not not_15 (not_15_out, OP1);
  not not_16 (not_16_out, OP0);
  not not_17 (not_17_out, F4);
  not not_18 (not_18_out, F3);
  not not_19 (not_19_out, F2);
  not not_20 (not_20_out, F1);
  not not_21 (not_21_out, F0);
  not not_22 (not_22_out, OP5);
  not not_23 (not_23_out, OP4);
  not not_24 (not_24_out, OP3);
  not not_25 (not_25_out, OP2);
  not not_26 (not_26_out, OP1);
  not not_27 (not_27_out, OP0);
  not not_28 (not_28_out, F4);
  not not_29 (not_29_out, F3);
  not not_30 (not_30_out, F2);
  not not_31 (not_31_out, F1);
  not not_32 (not_32_out, OP5);
  not not_33 (not_33_out, OP4);
  not not_34 (not_34_out, OP3);
  not not_35 (not_35_out, OP2);
  not not_36 (not_36_out, OP1);
  not not_37 (not_37_out, OP0);
  not not_38 (not_38_out, F4);
  not not_39 (not_39_out, F3);
  not not_40 (not_40_out, F1);
  not not_41 (not_41_out, F0);
  not not_42 (not_42_out, OP5);
  not not_43 (not_43_out, OP4);
  not not_44 (not_44_out, OP3);
  not not_45 (not_45_out, OP2);
  not not_46 (not_46_out, OP1);
  not not_47 (not_47_out, OP0);
  not not_48 (not_48_out, F4);
  not not_49 (not_49_out, F2);
  not not_50 (not_50_out, F0);
  not not_51 (not_51_out, OP5);
  not not_52 (not_52_out, OP4);
  not not_53 (not_53_out, OP2);
  not not_54 (not_54_out, OP1);
  not not_55 (not_55_out, OP0);
  not not_56 (not_56_out, OP5);
  not not_57 (not_57_out, OP4);
  not not_58 (not_58_out, OP1);
  not not_59 (not_59_out, OP0);
  not not_60 (not_60_out, OP5);
  not not_61 (not_61_out, OP4);
  not not_62 (not_62_out, OP2);
  not not_63 (not_63_out, OP1);
  not not_64 (not_64_out, OP5);
  not not_65 (not_65_out, OP4);
  not not_66 (not_66_out, OP2);
  not not_67 (not_67_out, OP0);
  not not_68 (not_68_out, OP4);
  not not_69 (not_69_out, OP3);
  not not_70 (not_70_out, OP2);
  not not_71 (not_71_out, OP4);
  not not_72 (not_72_out, OP2);
  not not_73 (not_73_out, OP5);
  not not_74 (not_74_out, OP4);
  not not_75 (not_75_out, OP3);
  not not_76 (not_76_out, OP2);
  not not_77 (not_77_out, OP1);
  not not_78 (not_78_out, OP0);
  not not_79 (not_79_out, F4);
  not not_80 (not_80_out, F3);
  not not_81 (not_81_out, F0);
  not not_82 (not_82_out, OP4);
  not not_83 (not_83_out, OP3);
  not not_84 (not_84_out, OP1);
  not not_85 (not_85_out, OP0);
  not not_86 (not_86_out, OP5);
  not not_87 (not_87_out, OP4);
  not not_88 (not_88_out, OP3);
  not not_89 (not_89_out, OP5);
  not not_90 (not_90_out, OP4);
  not not_91 (not_91_out, OP3);
  not not_92 (not_92_out, OP2);
  not not_93 (not_93_out, OP1);
  not not_94 (not_94_out, OP0);
  not not_95 (not_95_out, F5);
  not not_96 (not_96_out, F4);
  not not_97 (not_97_out, F3);
  not not_98 (not_98_out, F2);
  not not_99 (not_99_out, F0);
  not not_100 (not_100_out, OP5);
  not not_101 (not_101_out, OP4);
  not not_102 (not_102_out, OP3);
  not not_103 (not_103_out, OP2);
  not not_104 (not_104_out, OP1);
  not not_105 (not_105_out, OP0);
  not not_106 (not_106_out, F4);
  not not_107 (not_107_out, F3);
  not not_108 (not_108_out, F2);
  not not_109 (not_109_out, F0);
  not not_110 (not_110_out, OP5);
  not not_111 (not_111_out, OP4);
  not not_112 (not_112_out, OP3);
  not not_113 (not_113_out, OP2);
  not not_114 (not_114_out, OP1);
  not not_115 (not_115_out, OP0);
  not not_116 (not_116_out, F4);
  not not_117 (not_117_out, F3);
  not not_118 (not_118_out, F1);
  not not_119 (not_119_out, F0);
  not not_120 (not_120_out, OP5);
  not not_121 (not_121_out, OP4);
  not not_122 (not_122_out, OP3);
  not not_123 (not_123_out, OP2);
  not not_124 (not_124_out, OP1);
  not not_125 (not_125_out, OP0);
  not not_126 (not_126_out, F4);
  not not_127 (not_127_out, F3);
  not not_128 (not_128_out, OP5);
  not not_129 (not_129_out, OP4);
  not not_130 (not_130_out, OP3);
  not not_131 (not_131_out, OP2);
  not not_132 (not_132_out, OP1);
  not not_133 (not_133_out, OP0);
  not not_134 (not_134_out, F4);
  not not_135 (not_135_out, F2);
  not not_136 (not_136_out, F0);
  not not_137 (not_137_out, OP5);
  not not_138 (not_138_out, OP4);
  not not_139 (not_139_out, OP1);
  not not_140 (not_140_out, OP0);
  not not_141 (not_141_out, OP5);
  not not_142 (not_142_out, OP4);
  not not_143 (not_143_out, OP2);
  not not_144 (not_144_out, OP0);
  not not_145 (not_145_out, OP5);
  not not_146 (not_146_out, OP4);
  not not_147 (not_147_out, OP3);
  not not_148 (not_148_out, OP2);
  not not_149 (not_149_out, OP1);
  not not_150 (not_150_out, OP0);
  not not_151 (not_151_out, F5);
  not not_152 (not_152_out, F4);
  not not_153 (not_153_out, F3);
  not not_154 (not_154_out, F0);
  not not_155 (not_155_out, OP5);
  not not_156 (not_156_out, OP4);
  not not_157 (not_157_out, OP3);
  not not_158 (not_158_out, OP5);
  not not_159 (not_159_out, OP4);
  not not_160 (not_160_out, OP3);
  not not_161 (not_161_out, OP2);
  not not_162 (not_162_out, OP1);
  not not_163 (not_163_out, OP0);
  not not_164 (not_164_out, F4);
  not not_165 (not_165_out, F3);
  not not_166 (not_166_out, F2);
  not not_167 (not_167_out, F1);
  not not_168 (not_168_out, F0);
  not not_169 (not_169_out, OP5);
  not not_170 (not_170_out, OP4);
  not not_171 (not_171_out, OP3);
  not not_172 (not_172_out, OP2);
  not not_173 (not_173_out, OP1);
  not not_174 (not_174_out, OP0);
  not not_175 (not_175_out, F4);
  not not_176 (not_176_out, F3);
  not not_177 (not_177_out, F2);
  not not_178 (not_178_out, F1);
  not not_179 (not_179_out, OP5);
  not not_180 (not_180_out, OP4);
  not not_181 (not_181_out, OP3);
  not not_182 (not_182_out, OP2);
  not not_183 (not_183_out, OP1);
  not not_184 (not_184_out, OP0);
  not not_185 (not_185_out, F4);
  not not_186 (not_186_out, F3);
  not not_187 (not_187_out, F2);
  not not_188 (not_188_out, F0);
  not not_189 (not_189_out, OP5);
  not not_190 (not_190_out, OP4);
  not not_191 (not_191_out, OP3);
  not not_192 (not_192_out, OP2);
  not not_193 (not_193_out, OP1);
  not not_194 (not_194_out, OP0);
  not not_195 (not_195_out, F4);
  not not_196 (not_196_out, F3);
  not not_197 (not_197_out, F1);
  not not_198 (not_198_out, F0);
  not not_199 (not_199_out, OP5);
  not not_200 (not_200_out, OP4);
  not not_201 (not_201_out, OP3);
  not not_202 (not_202_out, OP2);
  not not_203 (not_203_out, OP1);
  not not_204 (not_204_out, OP0);
  not not_205 (not_205_out, F4);
  not not_206 (not_206_out, F2);
  not not_207 (not_207_out, OP5);
  not not_208 (not_208_out, OP4);
  not not_209 (not_209_out, OP2);
  not not_210 (not_210_out, OP1);
  not not_211 (not_211_out, OP0);
  not not_212 (not_212_out, OP5);
  not not_213 (not_213_out, OP4);
  not not_214 (not_214_out, OP1);
  not not_215 (not_215_out, OP0);
  not not_216 (not_216_out, OP5);
  not not_217 (not_217_out, OP4);
  not not_218 (not_218_out, OP2);
  not not_219 (not_219_out, OP1);
  not not_220 (not_220_out, OP4);
  not not_221 (not_221_out, OP3);
  not not_222 (not_222_out, OP2);
  not not_223 (not_223_out, OP4);
  not not_224 (not_224_out, OP2);
  not not_225 (not_225_out, OP4);
  not not_226 (not_226_out, OP3);
  not not_227 (not_227_out, OP1);
  not not_228 (not_228_out, OP0);
  not not_229 (not_229_out, OP5);
  not not_230 (not_230_out, OP4);
  not not_231 (not_231_out, OP3);
  not not_232 (not_232_out, OP2);
  not not_233 (not_233_out, OP1);
  not not_234 (not_234_out, OP0);
  not not_235 (not_235_out, F4);
  not not_236 (not_236_out, F3);
  not not_237 (not_237_out, F1);
  not not_238 (not_238_out, OP5);
  not not_239 (not_239_out, OP4);
  not not_240 (not_240_out, OP3);
  not not_241 (not_241_out, OP2);
  not not_242 (not_242_out, OP1);
  not not_243 (not_243_out, OP0);
  not not_244 (not_244_out, F4);
  not not_245 (not_245_out, F3);
  not not_246 (not_246_out, OP5);
  not not_247 (not_247_out, OP4);
  not not_248 (not_248_out, OP3);
  not not_249 (not_249_out, OP2);
  not not_250 (not_250_out, OP1);
  not not_251 (not_251_out, OP0);
  not not_252 (not_252_out, F4);
  not not_253 (not_253_out, F2);
  not not_254 (not_254_out, F0);
  not not_255 (not_255_out, OP5);
  not not_256 (not_256_out, OP4);
  not not_257 (not_257_out, OP3);
  not not_258 (not_258_out, OP2);
  not not_259 (not_259_out, OP1);
  not not_260 (not_260_out, OP0);
  not not_261 (not_261_out, F4);
  not not_262 (not_262_out, F2);
  not not_263 (not_263_out, OP5);
  not not_264 (not_264_out, OP4);
  not not_265 (not_265_out, OP2);
  not not_266 (not_266_out, OP0);
  not not_267 (not_267_out, OP5);
  not not_268 (not_268_out, OP4);
  not not_269 (not_269_out, OP1);
  not not_270 (not_270_out, OP5);
  not not_271 (not_271_out, OP4);
  not not_272 (not_272_out, OP3);
  not not_273 (not_273_out, OP2);
  not not_274 (not_274_out, OP1);
  not not_275 (not_275_out, OP0);
  not not_276 (not_276_out, F4);
  not not_277 (not_277_out, F3);
  not not_278 (not_278_out, F0);
  not not_279 (not_279_out, OP5);
  not not_280 (not_280_out, OP4);
  not not_281 (not_281_out, OP3);
  and and_1 (and_1_out, not_1_out, not_2_out, not_3_out, not_4_out, not_5_out, not_6_out, not_7_out, not_8_out, not_9_out, not_10_out, F1, F0);
  and and_2 (and_2_out, not_11_out, not_12_out, not_13_out, not_14_out, not_15_out, not_16_out, F5, not_17_out, not_18_out, not_19_out, not_20_out, not_21_out);
  and and_3 (and_3_out, not_22_out, not_23_out, not_24_out, not_25_out, not_26_out, not_27_out, F5, not_28_out, not_29_out, not_30_out, not_31_out, F0);
  and and_4 (and_4_out, not_32_out, not_33_out, not_34_out, not_35_out, not_36_out, not_37_out, F5, not_38_out, not_39_out, F2, not_40_out, not_41_out);
  and and_5 (and_5_out, not_42_out, not_43_out, not_44_out, not_45_out, not_46_out, not_47_out, F5, not_48_out, F3, not_49_out, F1, not_50_out);
  and and_6 (and_6_out, not_51_out, not_52_out, OP3, not_53_out, not_54_out, not_55_out);
  and and_7 (and_7_out, not_56_out, not_57_out, OP3, OP2, not_58_out, not_59_out);
  and and_8 (and_8_out, not_60_out, not_61_out, OP3, not_62_out, not_63_out, OP0);
  and and_9 (and_9_out, not_64_out, not_65_out, OP3, not_66_out, OP1, not_67_out);
  and and_10 (and_10_out, OP5, not_68_out, not_69_out, not_70_out, OP1, OP0);
  and and_11 (and_11_out, OP5, not_71_out, OP3, not_72_out, OP1, OP0);
  and and_12 (and_12_out, not_73_out, not_74_out, not_75_out, not_76_out, not_77_out, not_78_out, F5, not_79_out, not_80_out, F2, F1, not_81_out);
  and and_13 (and_13_out, OP5, not_82_out, not_83_out, OP2, not_84_out, not_85_out);
  and and_14 (and_14_out, not_86_out, not_87_out, not_88_out, OP2, OP1, OP0);
  and and_15 (and_15_out, not_89_out, not_90_out, not_91_out, not_92_out, not_93_out, not_94_out, not_95_out, not_96_out, not_97_out, not_98_out, F1, not_99_out);
  and and_16 (and_16_out, not_100_out, not_101_out, not_102_out, not_103_out, not_104_out, not_105_out, F5, not_106_out, not_107_out, not_108_out, F1, not_109_out);
  and and_17 (and_17_out, not_110_out, not_111_out, not_112_out, not_113_out, not_114_out, not_115_out, F5, not_116_out, not_117_out, F2, not_118_out, not_119_out);
  and and_18 (and_18_out, not_120_out, not_121_out, not_122_out, not_123_out, not_124_out, not_125_out, F5, not_126_out, not_127_out, F2, F1, F0);
  and and_19 (and_19_out, not_128_out, not_129_out, not_130_out, not_131_out, not_132_out, not_133_out, F5, not_134_out, F3, not_135_out, F1, not_136_out);
  and and_20 (and_20_out, not_137_out, not_138_out, OP3, OP2, not_139_out, not_140_out);
  and and_21 (and_21_out, not_141_out, not_142_out, OP3, not_143_out, OP1, not_144_out);
  and and_22 (and_22_out, not_145_out, not_146_out, not_147_out, not_148_out, not_149_out, not_150_out, not_151_out, not_152_out, not_153_out, F2, F1, not_154_out);
  and and_23 (and_23_out, not_155_out, not_156_out, not_157_out, OP2, OP1, OP0);
  and and_24 (and_24_out, not_158_out, not_159_out, not_160_out, not_161_out, not_162_out, not_163_out, F5, not_164_out, not_165_out, not_166_out, not_167_out, not_168_out);
  and and_25 (and_25_out, not_169_out, not_170_out, not_171_out, not_172_out, not_173_out, not_174_out, F5, not_175_out, not_176_out, not_177_out, not_178_out, F0);
  and and_26 (and_26_out, not_179_out, not_180_out, not_181_out, not_182_out, not_183_out, not_184_out, F5, not_185_out, not_186_out, not_187_out, F1, not_188_out);
  and and_27 (and_27_out, not_189_out, not_190_out, not_191_out, not_192_out, not_193_out, not_194_out, F5, not_195_out, not_196_out, F2, not_197_out, not_198_out);
  and and_28 (and_28_out, not_199_out, not_200_out, not_201_out, not_202_out, not_203_out, not_204_out, F5, not_205_out, F3, not_206_out, F1, F0);
  and and_29 (and_29_out, not_207_out, not_208_out, OP3, not_209_out, not_210_out, not_211_out);
  and and_30 (and_30_out, not_212_out, not_213_out, OP3, OP2, not_214_out, not_215_out);
  and and_31 (and_31_out, not_216_out, not_217_out, OP3, not_218_out, not_219_out, OP0);
  and and_32 (and_32_out, OP5, not_220_out, not_221_out, not_222_out, OP1, OP0);
  and and_33 (and_33_out, OP5, not_223_out, OP3, not_224_out, OP1, OP0);
  and and_34 (and_34_out, OP5, not_225_out, not_226_out, OP2, not_227_out, not_228_out);
  and and_35 (and_35_out, not_229_out, not_230_out, not_231_out, not_232_out, not_233_out, not_234_out, F5, not_235_out, not_236_out, F2, not_237_out, F0);
  and and_36 (and_36_out, not_238_out, not_239_out, not_240_out, not_241_out, not_242_out, not_243_out, F5, not_244_out, not_245_out, F2, F1, F0);
  and and_37 (and_37_out, not_246_out, not_247_out, not_248_out, not_249_out, not_250_out, not_251_out, F5, not_252_out, F3, not_253_out, F1, not_254_out);
  and and_38 (and_38_out, not_255_out, not_256_out, not_257_out, not_258_out, not_259_out, not_260_out, F5, not_261_out, F3, not_262_out, F1, F0);
  and and_39 (and_39_out, not_263_out, not_264_out, OP3, not_265_out, OP1, not_266_out);
  and and_40 (and_40_out, not_267_out, not_268_out, OP3, OP2, not_269_out, OP0);
  and and_41 (and_41_out, not_270_out, not_271_out, not_272_out, not_273_out, not_274_out, not_275_out, F5, not_276_out, not_277_out, F2, F1, not_278_out);
  and and_42 (and_42_out, not_279_out, not_280_out, not_281_out, OP2, OP1, OP0);
  or or_1 (S1, and_15_out, and_16_out, and_17_out, and_18_out, and_19_out, and_20_out, and_21_out, and_22_out, and_23_out);
  or or_2 (S2, and_24_out, and_25_out, and_26_out, and_27_out, and_28_out, and_29_out, and_30_out, and_31_out, and_32_out, and_33_out, and_34_out);
  or or_3 (S3, and_35_out, and_36_out, and_37_out, and_38_out, and_39_out, and_40_out, and_41_out, and_42_out);
  or or_4 (S0, and_1_out, and_2_out, and_3_out, and_4_out, and_5_out, and_6_out, and_7_out, and_8_out, and_9_out, and_10_out, and_11_out, and_12_out, and_13_out, and_14_out);
endmodule

// 控制信号生成
module \控制信号生成  (
  input  OP0,
  input  OP1,
  input  OP2,
  input  OP3,
  input  OP4,
  input  OP5,
  input  F0,
  input  F1,
  input  F2,
  input  F3,
  input  F4,
  input  F5,
  output MemToReg,
  output MemWrite,
  output ALU_SRC,
  output RegWrite,
  output SysCALL,
  output SignedExt,
  output RegDst,
  output BEQ,
  output BNE,
  output JR,
  output JMP,
  output JAL
);

  wire and_1_out, and_2_out, and_4_out, and_5_out, and_6_out, and_7_out, and_8_out, and_9_out, and_10_out,
       and_11_out, and_12_out, and_13_out, and_14_out, and_15_out, and_16_out, and_17_out, and_18_out,
       and_19_out, and_20_out, and_21_out, and_22_out, and_23_out, and_24_out, and_25_out, and_26_out,
       and_27_out, and_28_out, and_29_out, and_30_out, and_31_out, and_32_out, and_34_out, and_35_out,
       and_36_out, and_37_out, and_38_out, and_39_out, and_40_out, and_41_out, and_42_out, and_43_out,
       and_44_out, and_45_out, and_46_out, and_47_out, and_48_out, and_49_out, and_50_out, and_51_out,
       and_52_out, and_53_out, and_57_out, and_58_out, and_59_out, not_1_out, not_2_out, not_3_out,
       not_4_out, not_5_out, not_6_out, not_7_out, not_8_out, not_9_out, not_10_out, not_11_out, not_12_out,
       not_13_out, not_14_out, not_15_out, not_16_out, not_17_out, not_18_out, not_19_out, not_20_out,
       not_21_out, not_22_out, not_23_out, not_24_out, not_25_out, not_26_out, not_27_out, not_28_out,
       not_29_out, not_30_out, not_31_out, not_32_out, not_33_out, not_34_out, not_35_out, not_36_out,
       not_37_out, not_38_out, not_39_out, not_40_out, not_41_out, not_42_out, not_43_out, not_44_out,
       not_45_out, not_46_out, not_47_out, not_48_out, not_49_out, not_50_out, not_51_out, not_52_out,
       not_53_out, not_54_out, not_55_out, not_56_out, not_57_out, not_58_out, not_59_out, not_60_out,
       not_61_out, not_62_out, not_63_out, not_64_out, not_65_out, not_66_out, not_67_out, not_68_out,
       not_69_out, not_70_out, not_71_out, not_72_out, not_73_out, not_74_out, not_75_out, not_76_out,
       not_77_out, not_78_out, not_79_out, not_80_out, not_81_out, not_82_out, not_83_out, not_84_out,
       not_85_out, not_86_out, not_87_out, not_88_out, not_89_out, not_90_out, not_91_out, not_92_out,
       not_93_out, not_94_out, not_95_out, not_96_out, not_97_out, not_98_out, not_99_out, not_100_out,
       not_101_out, not_102_out, not_103_out, not_104_out, not_105_out, not_106_out, not_107_out,
       not_108_out, not_109_out, not_110_out, not_111_out, not_112_out, not_113_out, not_114_out,
       not_115_out, not_116_out, not_117_out, not_118_out, not_119_out, not_120_out, not_121_out,
       not_122_out, not_123_out, not_124_out, not_125_out, not_126_out, not_127_out, not_128_out,
       not_129_out, not_130_out, not_131_out, not_132_out, not_133_out, not_134_out, not_135_out,
       not_136_out, not_137_out, not_138_out, not_139_out, not_140_out, not_141_out, not_142_out,
       not_143_out, not_144_out, not_145_out, not_146_out, not_147_out, not_148_out, not_149_out,
       not_150_out, not_151_out, not_152_out, not_153_out, not_154_out, not_155_out, not_156_out,
       not_157_out, not_158_out, not_159_out, not_160_out, not_161_out, not_162_out, not_163_out,
       not_164_out, not_165_out, not_166_out, not_167_out, not_168_out, not_169_out, not_170_out,
       not_171_out, not_172_out, not_173_out, not_174_out, not_175_out, not_176_out, not_177_out,
       not_178_out, not_179_out, not_180_out, not_181_out, not_182_out, not_183_out, not_184_out,
       not_185_out, not_186_out, not_187_out, not_188_out, not_189_out, not_190_out, not_191_out,
       not_192_out, not_193_out, not_194_out, not_195_out, not_196_out, not_197_out, not_198_out,
       not_199_out, not_200_out, not_201_out, not_202_out, not_203_out, not_204_out, not_205_out,
       not_206_out, not_207_out, not_208_out, not_209_out, not_210_out, not_211_out, not_212_out,
       not_213_out, not_214_out, not_215_out, not_216_out, not_217_out, not_218_out, not_219_out,
       not_220_out, not_221_out, not_222_out, not_223_out, not_224_out, not_225_out, not_226_out,
       not_227_out, not_228_out, not_229_out, not_230_out, not_231_out, not_232_out, not_233_out,
       not_234_out, not_235_out, not_236_out, not_237_out, not_238_out, not_239_out, not_240_out,
       not_241_out, not_242_out, not_243_out, not_244_out, not_245_out, not_246_out, not_247_out,
       not_248_out, not_249_out, not_250_out, not_251_out, not_252_out, not_253_out, not_254_out,
       not_255_out, not_256_out, not_257_out, not_258_out, not_259_out, not_260_out, not_261_out,
       not_262_out, not_263_out, not_264_out, not_265_out, not_266_out, not_267_out, not_268_out,
       not_269_out, not_270_out, not_271_out, not_272_out, not_273_out, not_274_out, not_275_out,
       not_276_out, not_277_out, not_278_out, not_279_out, not_280_out, not_281_out, not_282_out,
       not_283_out, not_284_out, not_285_out, not_286_out, not_287_out, not_288_out, not_289_out,
       not_290_out, not_291_out, not_292_out, not_293_out, not_294_out, not_295_out, not_296_out,
       not_297_out, not_298_out, not_299_out, not_300_out, not_301_out, not_302_out, not_303_out,
       not_304_out, not_305_out, not_306_out, not_307_out, not_308_out, not_309_out, not_310_out,
       not_311_out, not_312_out, not_313_out, not_314_out, not_315_out, not_316_out, not_317_out,
       not_318_out, not_319_out, not_320_out, not_321_out, not_322_out, not_323_out, not_324_out,
       not_325_out, not_326_out, not_327_out, not_328_out, not_329_out, not_330_out, not_331_out,
       not_332_out, not_333_out, not_334_out, not_335_out, not_336_out, not_337_out, not_338_out,
       not_339_out, not_340_out, not_341_out, not_342_out, not_343_out, not_344_out, not_345_out,
       not_346_out, not_347_out, not_348_out, not_349_out, not_350_out, not_351_out, not_352_out,
       not_353_out, not_354_out, not_355_out, not_356_out, not_357_out, not_358_out, not_359_out,
       not_360_out, not_361_out, not_362_out, not_363_out, not_364_out, not_365_out, not_366_out,
       not_367_out, not_368_out, not_369_out, not_370_out, not_371_out, not_372_out, not_373_out,
       not_374_out, not_375_out, not_376_out, not_377_out, not_378_out, not_379_out, not_380_out,
       not_381_out, not_382_out, not_383_out, not_384_out, not_385_out, not_386_out, not_387_out,
       not_388_out, not_389_out, not_390_out, not_391_out, not_392_out, not_393_out, not_394_out,
       not_395_out, not_396_out, not_397_out, not_398_out, not_399_out, not_400_out, not_401_out,
       not_402_out, not_403_out;

  not not_1 (not_1_out, OP4);
  not not_2 (not_2_out, OP3);
  not not_3 (not_3_out, OP2);
  not not_4 (not_4_out, OP4);
  not not_5 (not_5_out, OP3);
  not not_6 (not_6_out, OP1);
  not not_7 (not_7_out, OP0);
  not not_8 (not_8_out, OP4);
  not not_9 (not_9_out, OP2);
  not not_10 (not_10_out, OP5);
  not not_11 (not_11_out, OP4);
  not not_12 (not_12_out, OP2);
  not not_13 (not_13_out, OP1);
  not not_14 (not_14_out, OP0);
  not not_15 (not_15_out, OP5);
  not not_16 (not_16_out, OP4);
  not not_17 (not_17_out, OP1);
  not not_18 (not_18_out, OP0);
  not not_19 (not_19_out, OP5);
  not not_20 (not_20_out, OP4);
  not not_21 (not_21_out, OP2);
  not not_22 (not_22_out, OP1);
  not not_23 (not_23_out, OP5);
  not not_24 (not_24_out, OP4);
  not not_25 (not_25_out, OP2);
  not not_26 (not_26_out, OP0);
  not not_27 (not_27_out, OP5);
  not not_28 (not_28_out, OP4);
  not not_29 (not_29_out, OP1);
  not not_30 (not_30_out, OP4);
  not not_31 (not_31_out, OP3);
  not not_32 (not_32_out, OP2);
  not not_33 (not_33_out, OP4);
  not not_34 (not_34_out, OP2);
  not not_35 (not_35_out, OP4);
  not not_36 (not_36_out, OP3);
  not not_37 (not_37_out, OP1);
  not not_38 (not_38_out, OP0);
  not not_39 (not_39_out, OP5);
  not not_40 (not_40_out, OP4);
  not not_41 (not_41_out, OP3);
  not not_42 (not_42_out, OP2);
  not not_43 (not_43_out, OP1);
  not not_44 (not_44_out, OP0);
  not not_45 (not_45_out, F5);
  not not_46 (not_46_out, F4);
  not not_47 (not_47_out, F3);
  not not_48 (not_48_out, F2);
  not not_49 (not_49_out, F1);
  not not_50 (not_50_out, F0);
  not not_51 (not_51_out, OP5);
  not not_52 (not_52_out, OP4);
  not not_53 (not_53_out, OP3);
  not not_54 (not_54_out, OP2);
  not not_55 (not_55_out, OP1);
  not not_56 (not_56_out, OP0);
  not not_57 (not_57_out, F5);
  not not_58 (not_58_out, F4);
  not not_59 (not_59_out, F3);
  not not_60 (not_60_out, F2);
  not not_61 (not_61_out, OP5);
  not not_62 (not_62_out, OP4);
  not not_63 (not_63_out, OP3);
  not not_64 (not_64_out, OP2);
  not not_65 (not_65_out, OP1);
  not not_66 (not_66_out, OP0);
  not not_67 (not_67_out, F5);
  not not_68 (not_68_out, F4);
  not not_69 (not_69_out, F3);
  not not_70 (not_70_out, F2);
  not not_71 (not_71_out, F0);
  not not_72 (not_72_out, OP5);
  not not_73 (not_73_out, OP4);
  not not_74 (not_74_out, OP3);
  not not_75 (not_75_out, OP2);
  not not_76 (not_76_out, OP1);
  not not_77 (not_77_out, OP0);
  not not_78 (not_78_out, F4);
  not not_79 (not_79_out, F3);
  not not_80 (not_80_out, F2);
  not not_81 (not_81_out, F1);
  not not_82 (not_82_out, F0);
  not not_83 (not_83_out, OP5);
  not not_84 (not_84_out, OP4);
  not not_85 (not_85_out, OP3);
  not not_86 (not_86_out, OP2);
  not not_87 (not_87_out, OP1);
  not not_88 (not_88_out, OP0);
  not not_89 (not_89_out, F4);
  not not_90 (not_90_out, F3);
  not not_91 (not_91_out, F2);
  not not_92 (not_92_out, F1);
  not not_93 (not_93_out, OP5);
  not not_94 (not_94_out, OP4);
  not not_95 (not_95_out, OP3);
  not not_96 (not_96_out, OP2);
  not not_97 (not_97_out, OP1);
  not not_98 (not_98_out, OP0);
  not not_99 (not_99_out, F4);
  not not_100 (not_100_out, F3);
  not not_101 (not_101_out, F2);
  not not_102 (not_102_out, F0);
  not not_103 (not_103_out, OP5);
  not not_104 (not_104_out, OP4);
  not not_105 (not_105_out, OP3);
  not not_106 (not_106_out, OP2);
  not not_107 (not_107_out, OP1);
  not not_108 (not_108_out, OP0);
  not not_109 (not_109_out, F4);
  not not_110 (not_110_out, F3);
  not not_111 (not_111_out, F1);
  not not_112 (not_112_out, F0);
  not not_113 (not_113_out, OP5);
  not not_114 (not_114_out, OP4);
  not not_115 (not_115_out, OP3);
  not not_116 (not_116_out, OP2);
  not not_117 (not_117_out, OP1);
  not not_118 (not_118_out, OP0);
  not not_119 (not_119_out, F4);
  not not_120 (not_120_out, F3);
  not not_121 (not_121_out, F1);
  not not_122 (not_122_out, OP5);
  not not_123 (not_123_out, OP4);
  not not_124 (not_124_out, OP3);
  not not_125 (not_125_out, OP2);
  not not_126 (not_126_out, OP1);
  not not_127 (not_127_out, OP0);
  not not_128 (not_128_out, F4);
  not not_129 (not_129_out, F3);
  not not_130 (not_130_out, OP5);
  not not_131 (not_131_out, OP4);
  not not_132 (not_132_out, OP3);
  not not_133 (not_133_out, OP2);
  not not_134 (not_134_out, OP1);
  not not_135 (not_135_out, OP0);
  not not_136 (not_136_out, F4);
  not not_137 (not_137_out, F2);
  not not_138 (not_138_out, F0);
  not not_139 (not_139_out, OP5);
  not not_140 (not_140_out, OP4);
  not not_141 (not_141_out, OP3);
  not not_142 (not_142_out, OP2);
  not not_143 (not_143_out, OP1);
  not not_144 (not_144_out, OP0);
  not not_145 (not_145_out, F4);
  not not_146 (not_146_out, F2);
  not not_147 (not_147_out, OP5);
  not not_148 (not_148_out, OP4);
  not not_149 (not_149_out, OP3);
  not not_150 (not_150_out, OP2);
  not not_151 (not_151_out, OP5);
  not not_152 (not_152_out, OP4);
  not not_153 (not_153_out, OP2);
  not not_154 (not_154_out, OP1);
  not not_155 (not_155_out, OP0);
  not not_156 (not_156_out, OP5);
  not not_157 (not_157_out, OP4);
  not not_158 (not_158_out, OP1);
  not not_159 (not_159_out, OP0);
  not not_160 (not_160_out, OP5);
  not not_161 (not_161_out, OP4);
  not not_162 (not_162_out, OP2);
  not not_163 (not_163_out, OP1);
  not not_164 (not_164_out, OP5);
  not not_165 (not_165_out, OP4);
  not not_166 (not_166_out, OP2);
  not not_167 (not_167_out, OP0);
  not not_168 (not_168_out, OP5);
  not not_169 (not_169_out, OP4);
  not not_170 (not_170_out, OP1);
  not not_171 (not_171_out, OP4);
  not not_172 (not_172_out, OP3);
  not not_173 (not_173_out, OP2);
  not not_174 (not_174_out, OP5);
  not not_175 (not_175_out, OP4);
  not not_176 (not_176_out, OP3);
  not not_177 (not_177_out, OP2);
  not not_178 (not_178_out, OP1);
  not not_179 (not_179_out, OP0);
  not not_180 (not_180_out, F5);
  not not_181 (not_181_out, F4);
  not not_182 (not_182_out, F3);
  not not_183 (not_183_out, F0);
  not not_184 (not_184_out, OP5);
  not not_185 (not_185_out, OP4);
  not not_186 (not_186_out, OP3);
  not not_187 (not_187_out, OP2);
  not not_188 (not_188_out, OP1);
  not not_189 (not_189_out, OP0);
  not not_190 (not_190_out, F4);
  not not_191 (not_191_out, F3);
  not not_192 (not_192_out, F0);
  not not_193 (not_193_out, OP4);
  not not_194 (not_194_out, OP3);
  not not_195 (not_195_out, OP1);
  not not_196 (not_196_out, OP0);
  not not_197 (not_197_out, OP5);
  not not_198 (not_198_out, OP4);
  not not_199 (not_199_out, OP3);
  not not_200 (not_200_out, OP2);
  not not_201 (not_201_out, OP1);
  not not_202 (not_202_out, OP0);
  not not_203 (not_203_out, F5);
  not not_204 (not_204_out, F4);
  not not_205 (not_205_out, F1);
  not not_206 (not_206_out, F0);
  not not_207 (not_207_out, OP5);
  not not_208 (not_208_out, OP4);
  not not_209 (not_209_out, OP2);
  not not_210 (not_210_out, OP1);
  not not_211 (not_211_out, OP0);
  not not_212 (not_212_out, OP5);
  not not_213 (not_213_out, OP4);
  not not_214 (not_214_out, OP1);
  not not_215 (not_215_out, OP0);
  not not_216 (not_216_out, OP5);
  not not_217 (not_217_out, OP4);
  not not_218 (not_218_out, OP2);
  not not_219 (not_219_out, OP1);
  not not_220 (not_220_out, OP5);
  not not_221 (not_221_out, OP4);
  not not_222 (not_222_out, OP2);
  not not_223 (not_223_out, OP0);
  not not_224 (not_224_out, OP4);
  not not_225 (not_225_out, OP3);
  not not_226 (not_226_out, OP2);
  not not_227 (not_227_out, OP4);
  not not_228 (not_228_out, OP2);
  not not_229 (not_229_out, OP4);
  not not_230 (not_230_out, OP3);
  not not_231 (not_231_out, OP1);
  not not_232 (not_232_out, OP0);
  not not_233 (not_233_out, OP5);
  not not_234 (not_234_out, OP4);
  not not_235 (not_235_out, OP3);
  not not_236 (not_236_out, OP2);
  not not_237 (not_237_out, OP1);
  not not_238 (not_238_out, OP0);
  not not_239 (not_239_out, F5);
  not not_240 (not_240_out, F4);
  not not_241 (not_241_out, F3);
  not not_242 (not_242_out, F2);
  not not_243 (not_243_out, F1);
  not not_244 (not_244_out, F0);
  not not_245 (not_245_out, OP5);
  not not_246 (not_246_out, OP4);
  not not_247 (not_247_out, OP3);
  not not_248 (not_248_out, OP2);
  not not_249 (not_249_out, OP1);
  not not_250 (not_250_out, OP0);
  not not_251 (not_251_out, F5);
  not not_252 (not_252_out, F4);
  not not_253 (not_253_out, F3);
  not not_254 (not_254_out, F2);
  not not_255 (not_255_out, OP5);
  not not_256 (not_256_out, OP4);
  not not_257 (not_257_out, OP3);
  not not_258 (not_258_out, OP2);
  not not_259 (not_259_out, OP1);
  not not_260 (not_260_out, OP0);
  not not_261 (not_261_out, F5);
  not not_262 (not_262_out, F4);
  not not_263 (not_263_out, F3);
  not not_264 (not_264_out, F2);
  not not_265 (not_265_out, F0);
  not not_266 (not_266_out, OP5);
  not not_267 (not_267_out, OP4);
  not not_268 (not_268_out, OP3);
  not not_269 (not_269_out, OP2);
  not not_270 (not_270_out, OP1);
  not not_271 (not_271_out, OP0);
  not not_272 (not_272_out, F4);
  not not_273 (not_273_out, F3);
  not not_274 (not_274_out, F2);
  not not_275 (not_275_out, F1);
  not not_276 (not_276_out, F0);
  not not_277 (not_277_out, OP5);
  not not_278 (not_278_out, OP4);
  not not_279 (not_279_out, OP3);
  not not_280 (not_280_out, OP2);
  not not_281 (not_281_out, OP1);
  not not_282 (not_282_out, OP0);
  not not_283 (not_283_out, F4);
  not not_284 (not_284_out, F3);
  not not_285 (not_285_out, F2);
  not not_286 (not_286_out, F1);
  not not_287 (not_287_out, OP5);
  not not_288 (not_288_out, OP4);
  not not_289 (not_289_out, OP3);
  not not_290 (not_290_out, OP2);
  not not_291 (not_291_out, OP1);
  not not_292 (not_292_out, OP0);
  not not_293 (not_293_out, F4);
  not not_294 (not_294_out, F3);
  not not_295 (not_295_out, F2);
  not not_296 (not_296_out, F0);
  not not_297 (not_297_out, OP5);
  not not_298 (not_298_out, OP4);
  not not_299 (not_299_out, OP3);
  not not_300 (not_300_out, OP2);
  not not_301 (not_301_out, OP1);
  not not_302 (not_302_out, OP0);
  not not_303 (not_303_out, F4);
  not not_304 (not_304_out, F3);
  not not_305 (not_305_out, F1);
  not not_306 (not_306_out, F0);
  not not_307 (not_307_out, OP5);
  not not_308 (not_308_out, OP4);
  not not_309 (not_309_out, OP3);
  not not_310 (not_310_out, OP2);
  not not_311 (not_311_out, OP1);
  not not_312 (not_312_out, OP0);
  not not_313 (not_313_out, F4);
  not not_314 (not_314_out, F3);
  not not_315 (not_315_out, F1);
  not not_316 (not_316_out, OP5);
  not not_317 (not_317_out, OP4);
  not not_318 (not_318_out, OP3);
  not not_319 (not_319_out, OP2);
  not not_320 (not_320_out, OP1);
  not not_321 (not_321_out, OP0);
  not not_322 (not_322_out, F4);
  not not_323 (not_323_out, F3);
  not not_324 (not_324_out, OP5);
  not not_325 (not_325_out, OP4);
  not not_326 (not_326_out, OP3);
  not not_327 (not_327_out, OP2);
  not not_328 (not_328_out, OP1);
  not not_329 (not_329_out, OP0);
  not not_330 (not_330_out, F4);
  not not_331 (not_331_out, F2);
  not not_332 (not_332_out, F0);
  not not_333 (not_333_out, OP5);
  not not_334 (not_334_out, OP4);
  not not_335 (not_335_out, OP3);
  not not_336 (not_336_out, OP2);
  not not_337 (not_337_out, OP1);
  not not_338 (not_338_out, OP0);
  not not_339 (not_339_out, F4);
  not not_340 (not_340_out, F2);
  not not_341 (not_341_out, OP5);
  not not_342 (not_342_out, OP4);
  not not_343 (not_343_out, OP3);
  not not_344 (not_344_out, OP2);
  not not_345 (not_345_out, OP1);
  not not_346 (not_346_out, OP0);
  not not_347 (not_347_out, F5);
  not not_348 (not_348_out, F4);
  not not_349 (not_349_out, F3);
  not not_350 (not_350_out, F0);
  not not_351 (not_351_out, OP5);
  not not_352 (not_352_out, OP4);
  not not_353 (not_353_out, OP3);
  not not_354 (not_354_out, OP2);
  not not_355 (not_355_out, OP1);
  not not_356 (not_356_out, OP0);
  not not_357 (not_357_out, F4);
  not not_358 (not_358_out, F3);
  not not_359 (not_359_out, F0);
  not not_360 (not_360_out, OP5);
  not not_361 (not_361_out, OP4);
  not not_362 (not_362_out, OP3);
  not not_363 (not_363_out, OP1);
  not not_364 (not_364_out, OP0);
  not not_365 (not_365_out, OP5);
  not not_366 (not_366_out, OP4);
  not not_367 (not_367_out, OP3);
  not not_368 (not_368_out, OP1);
  not not_369 (not_369_out, OP5);
  not not_370 (not_370_out, OP4);
  not not_371 (not_371_out, OP3);
  not not_372 (not_372_out, OP2);
  not not_373 (not_373_out, OP1);
  not not_374 (not_374_out, OP0);
  not not_375 (not_375_out, F5);
  not not_376 (not_376_out, F4);
  not not_377 (not_377_out, F2);
  not not_378 (not_378_out, F1);
  not not_379 (not_379_out, F0);
  not not_380 (not_380_out, OP5);
  not not_381 (not_381_out, OP4);
  not not_382 (not_382_out, OP3);
  not not_383 (not_383_out, OP2);
  not not_384 (not_384_out, OP1);
  not not_385 (not_385_out, OP0);
  not not_386 (not_386_out, F5);
  not not_387 (not_387_out, F4);
  not not_388 (not_388_out, F2);
  not not_389 (not_389_out, F1);
  not not_390 (not_390_out, F0);
  not not_391 (not_391_out, OP5);
  not not_392 (not_392_out, OP4);
  not not_393 (not_393_out, OP3);
  not not_394 (not_394_out, OP2);
  not not_395 (not_395_out, OP0);
  not not_396 (not_396_out, OP5);
  not not_397 (not_397_out, OP4);
  not not_398 (not_398_out, OP3);
  not not_399 (not_399_out, OP2);
  not not_400 (not_400_out, OP5);
  not not_401 (not_401_out, OP4);
  not not_402 (not_402_out, OP3);
  not not_403 (not_403_out, OP2);
  and and_1 (and_1_out, OP5, not_1_out, not_2_out, not_3_out, OP1, OP0);
  and and_2 (and_2_out, OP5, not_4_out, not_5_out, OP2, not_6_out, not_7_out);
  and and_3 (MemWrite, OP5, not_8_out, OP3, not_9_out, OP1, OP0);
  and and_4 (and_4_out, not_10_out, not_11_out, OP3, not_12_out, not_13_out, not_14_out);
  and and_5 (and_5_out, not_15_out, not_16_out, OP3, OP2, not_17_out, not_18_out);
  and and_6 (and_6_out, not_19_out, not_20_out, OP3, not_21_out, not_22_out, OP0);
  and and_7 (and_7_out, not_23_out, not_24_out, OP3, not_25_out, OP1, not_26_out);
  and and_8 (and_8_out, not_27_out, not_28_out, OP3, OP2, not_29_out, OP0);
  and and_9 (and_9_out, OP5, not_30_out, not_31_out, not_32_out, OP1, OP0);
  and and_10 (and_10_out, OP5, not_33_out, OP3, not_34_out, OP1, OP0);
  and and_11 (and_11_out, OP5, not_35_out, not_36_out, OP2, not_37_out, not_38_out);
  and and_12 (and_12_out, not_39_out, not_40_out, not_41_out, not_42_out, not_43_out, not_44_out, not_45_out, not_46_out, not_47_out, not_48_out, not_49_out, not_50_out);
  and and_13 (and_13_out, not_51_out, not_52_out, not_53_out, not_54_out, not_55_out, not_56_out, not_57_out, not_58_out, not_59_out, not_60_out, F1, F0);
  and and_14 (and_14_out, not_61_out, not_62_out, not_63_out, not_64_out, not_65_out, not_66_out, not_67_out, not_68_out, not_69_out, not_70_out, F1, not_71_out);
  and and_15 (and_15_out, not_72_out, not_73_out, not_74_out, not_75_out, not_76_out, not_77_out, F5, not_78_out, not_79_out, not_80_out, not_81_out, not_82_out);
  and and_16 (and_16_out, not_83_out, not_84_out, not_85_out, not_86_out, not_87_out, not_88_out, F5, not_89_out, not_90_out, not_91_out, not_92_out, F0);
  and and_17 (and_17_out, not_93_out, not_94_out, not_95_out, not_96_out, not_97_out, not_98_out, F5, not_99_out, not_100_out, not_101_out, F1, not_102_out);
  and and_18 (and_18_out, not_103_out, not_104_out, not_105_out, not_106_out, not_107_out, not_108_out, F5, not_109_out, not_110_out, F2, not_111_out, not_112_out);
  and and_19 (and_19_out, not_113_out, not_114_out, not_115_out, not_116_out, not_117_out, not_118_out, F5, not_119_out, not_120_out, F2, not_121_out, F0);
  and and_20 (and_20_out, not_122_out, not_123_out, not_124_out, not_125_out, not_126_out, not_127_out, F5, not_128_out, not_129_out, F2, F1, F0);
  and and_21 (and_21_out, not_130_out, not_131_out, not_132_out, not_133_out, not_134_out, not_135_out, F5, not_136_out, F3, not_137_out, F1, not_138_out);
  and and_22 (and_22_out, not_139_out, not_140_out, not_141_out, not_142_out, not_143_out, not_144_out, F5, not_145_out, F3, not_146_out, F1, F0);
  and and_23 (and_23_out, not_147_out, not_148_out, not_149_out, not_150_out, OP1, OP0);
  and and_24 (and_24_out, not_151_out, not_152_out, OP3, not_153_out, not_154_out, not_155_out);
  and and_25 (and_25_out, not_156_out, not_157_out, OP3, OP2, not_158_out, not_159_out);
  and and_26 (and_26_out, not_160_out, not_161_out, OP3, not_162_out, not_163_out, OP0);
  and and_27 (and_27_out, not_164_out, not_165_out, OP3, not_166_out, OP1, not_167_out);
  and and_28 (and_28_out, not_168_out, not_169_out, OP3, OP2, not_170_out, OP0);
  and and_29 (and_29_out, OP5, not_171_out, not_172_out, not_173_out, OP1, OP0);
  and and_30 (and_30_out, not_174_out, not_175_out, not_176_out, not_177_out, not_178_out, not_179_out, not_180_out, not_181_out, not_182_out, F2, F1, not_183_out);
  and and_31 (and_31_out, not_184_out, not_185_out, not_186_out, not_187_out, not_188_out, not_189_out, F5, not_190_out, not_191_out, F2, F1, not_192_out);
  and and_32 (and_32_out, OP5, not_193_out, not_194_out, OP2, not_195_out, not_196_out);
  and and_33 (SysCALL, not_197_out, not_198_out, not_199_out, not_200_out, not_201_out, not_202_out, not_203_out, not_204_out, F3, F2, not_205_out, not_206_out);
  and and_34 (and_34_out, not_207_out, not_208_out, OP3, not_209_out, not_210_out, not_211_out);
  and and_35 (and_35_out, not_212_out, not_213_out, OP3, OP2, not_214_out, not_215_out);
  and and_36 (and_36_out, not_216_out, not_217_out, OP3, not_218_out, not_219_out, OP0);
  and and_37 (and_37_out, not_220_out, not_221_out, OP3, not_222_out, OP1, not_223_out);
  and and_38 (and_38_out, OP5, not_224_out, not_225_out, not_226_out, OP1, OP0);
  and and_39 (and_39_out, OP5, not_227_out, OP3, not_228_out, OP1, OP0);
  and and_40 (and_40_out, OP5, not_229_out, not_230_out, OP2, not_231_out, not_232_out);
  and and_41 (and_41_out, not_233_out, not_234_out, not_235_out, not_236_out, not_237_out, not_238_out, not_239_out, not_240_out, not_241_out, not_242_out, not_243_out, not_244_out);
  and and_42 (and_42_out, not_245_out, not_246_out, not_247_out, not_248_out, not_249_out, not_250_out, not_251_out, not_252_out, not_253_out, not_254_out, F1, F0);
  and and_43 (and_43_out, not_255_out, not_256_out, not_257_out, not_258_out, not_259_out, not_260_out, not_261_out, not_262_out, not_263_out, not_264_out, F1, not_265_out);
  and and_44 (and_44_out, not_266_out, not_267_out, not_268_out, not_269_out, not_270_out, not_271_out, F5, not_272_out, not_273_out, not_274_out, not_275_out, not_276_out);
  and and_45 (and_45_out, not_277_out, not_278_out, not_279_out, not_280_out, not_281_out, not_282_out, F5, not_283_out, not_284_out, not_285_out, not_286_out, F0);
  and and_46 (and_46_out, not_287_out, not_288_out, not_289_out, not_290_out, not_291_out, not_292_out, F5, not_293_out, not_294_out, not_295_out, F1, not_296_out);
  and and_47 (and_47_out, not_297_out, not_298_out, not_299_out, not_300_out, not_301_out, not_302_out, F5, not_303_out, not_304_out, F2, not_305_out, not_306_out);
  and and_48 (and_48_out, not_307_out, not_308_out, not_309_out, not_310_out, not_311_out, not_312_out, F5, not_313_out, not_314_out, F2, not_315_out, F0);
  and and_49 (and_49_out, not_316_out, not_317_out, not_318_out, not_319_out, not_320_out, not_321_out, F5, not_322_out, not_323_out, F2, F1, F0);
  and and_50 (and_50_out, not_324_out, not_325_out, not_326_out, not_327_out, not_328_out, not_329_out, F5, not_330_out, F3, not_331_out, F1, not_332_out);
  and and_51 (and_51_out, not_333_out, not_334_out, not_335_out, not_336_out, not_337_out, not_338_out, F5, not_339_out, F3, not_340_out, F1, F0);
  and and_52 (and_52_out, not_341_out, not_342_out, not_343_out, not_344_out, not_345_out, not_346_out, not_347_out, not_348_out, not_349_out, F2, F1, not_350_out);
  and and_53 (and_53_out, not_351_out, not_352_out, not_353_out, not_354_out, not_355_out, not_356_out, F5, not_357_out, not_358_out, F2, F1, not_359_out);
  and and_54 (BEQ, not_360_out, not_361_out, not_362_out, OP2, not_363_out, not_364_out);
  and and_55 (BNE, not_365_out, not_366_out, not_367_out, OP2, not_368_out, OP0);
  and and_56 (JR, not_369_out, not_370_out, not_371_out, not_372_out, not_373_out, not_374_out, not_375_out, not_376_out, F3, not_377_out, not_378_out, not_379_out);
  and and_57 (and_57_out, not_380_out, not_381_out, not_382_out, not_383_out, not_384_out, not_385_out, not_386_out, not_387_out, F3, not_388_out, not_389_out, not_390_out);
  and and_58 (and_58_out, not_391_out, not_392_out, not_393_out, not_394_out, OP1, not_395_out);
  and and_59 (and_59_out, not_396_out, not_397_out, not_398_out, not_399_out, OP1, OP0);
  and and_60 (JAL, not_400_out, not_401_out, not_402_out, not_403_out, OP1, OP0);
  or or_1 (MemToReg, and_1_out, and_2_out);
  or or_2 (ALU_SRC, and_4_out, and_5_out, and_6_out, and_7_out, and_8_out, and_9_out, and_10_out, and_11_out);
  or or_3 (SignedExt, and_34_out, and_35_out, and_36_out, and_37_out, and_38_out, and_39_out, and_40_out);
  or or_4 (JMP, and_57_out, and_58_out, and_59_out);
  or or_5 (RegWrite, and_12_out, and_13_out, and_14_out, and_15_out, and_16_out, and_17_out, and_18_out, and_19_out, and_20_out, and_21_out, and_22_out, and_23_out, and_24_out, and_25_out, and_26_out, and_27_out, and_28_out, and_29_out, and_30_out, and_31_out, and_32_out);
  or or_6 (RegDst, and_41_out, and_42_out, and_43_out, and_44_out, and_45_out, and_46_out, and_47_out, and_48_out, and_49_out, and_50_out, and_51_out, and_52_out, and_53_out);
endmodule

// ALU
module MIPS_ALU (
  input  [4:0] shamt,
  input  [31:0] X,
  input  [31:0] Y,
  input  [3:0] AluOP,
  output Equal,
  output [31:0] Result,
  output [31:0] Result_2
);

  wire [0:0] comparator_1_lt, comparator_2_lt;
  wire [31:0] adder_1_out, AND_out, divider_1_out, divider_1_rem, multiplier_1_cout, multiplier_1_out,
       NOR_out, OR_out, shifter_1_out, shifter_2_out, shifter_3_out, subtractor_1_out, XOR_out;

  assign AND_out = X & Y;  // AND_Gate AND, 32 bits wide
  assign OR_out = X | Y;  // OR_Gate OR, 32 bits wide
  Shifter #(.width(32)) shifter_1 (.in(Y), .\dist (shamt), .out(shifter_1_out));
  Shifter #(.width(32), .shift("ar")) shifter_2 (.in(Y), .\dist (shamt), .out(shifter_2_out));
  Shifter #(.width(32), .shift("lr")) shifter_3 (.in(Y), .\dist (shamt), .out(shifter_3_out));
  Multiplier #(.width(32)) multiplier_1 (.a(X), .b(Y), .out(multiplier_1_out), .cout(multiplier_1_cout));  // open: cin
  Divider #(.width(32)) divider_1 (.a(X), .b(Y), .out(divider_1_out), .rem(divider_1_rem));  // open: upper
  Adder #(.width(32)) adder_1 (.a(X), .b(Y), .out(adder_1_out));  // open: cin, cout
  Subtractor #(.width(32)) subtractor_1 (.a(X), .b(Y), .out(subtractor_1_out));  // open: bin, bout
  assign XOR_out = X ^ Y;  // XOR_Gate XOR, 32 bits wide
  assign NOR_out = ~(X | Y);  // NOR_Gate NOR, 32 bits wide
  Comparator #(.width(32)) comparator_1 (.a(X), .b(Y), .eq(Equal), .lt(comparator_1_lt[0]));  // open: gt
  Comparator #(.width(32), .mode("unsigned")) comparator_2 (.a(X), .b(Y), .lt(comparator_2_lt[0]));  // open: gt, eq
  Multiplexer #(.select(4), .width(32), .enable("false")) multiplexer_1 (
    .in0(shifter_1_out), .in1(shifter_2_out), .in2(shifter_3_out), .in3(multiplier_1_out),
    .in4(divider_1_out), .in5(adder_1_out), .in6(subtractor_1_out), .in7(AND_out), .in8(OR_out),
    .in9(XOR_out), .in10(NOR_out), .in11({{31{1'b0}}, comparator_1_lt[0]}),
    .in12({{31{1'b0}}, comparator_2_lt[0]}), .in13({32{1'b0}}), .in14({32{1'b0}}), .in15({32{1'b0}}),
    .out(Result), .sel(AluOP));
  Multiplexer #(.select(4), .width(32), .enable("false")) multiplexer_2 (
    .in0({32{1'b0}}), .in1({32{1'b0}}), .in2({32{1'b0}}), .in3(multiplier_1_cout), .in4(divider_1_rem),
    .in5({32{1'b0}}), .in6({32{1'b0}}), .in7({32{1'b0}}), .in8({32{1'b0}}), .in9({32{1'b0}}),
    .in10({32{1'b0}}), .in11({32{1'b0}}), .in12({32{1'b0}}), .in13({32{1'b0}}), .in14({32{1'b0}}),
    .in15({32{1'b0}}), .out(Result_2), .sel(AluOP));

  // Other names for the same wires on the sheet: Result2[31:0] = Result_2; S[3:0] = AluOP

  // Notes on the sheet:
  //   不要改变此引脚区域内容，也不要改变ALU封装形式
  //   输入引脚
  //   输出引脚
endmodule

module MIPS_Regifile (
  input  [31:0] Din,
  input  Clk,
  input  WE,
  input  [4:0] R1_num,
  input  [4:0] W_num,
  input  [4:0] R2_num,
  output [31:0] R1,
  output [31:0] R2
);

  // RegisterFile registerfile_1: pin names not known; wires that end beside it: Din, Clk, WE, W_num, R1_num, R2_num, R1, R2
endmodule

module \理想流水线  (
);

  wire CLK, EN, eq34, ex_mem_1_memtoreg_2, ex_mem_1_memwrite_2, ex_mem_1_reg_write_2, ex_mem_1_regdst_2,
       ex_mem_1_syscall_2, Go, id_ex_1_alu_src_2, id_ex_1_memtoreg_2, id_ex_1_memwrite_2,
       id_ex_1_reg_write_2, id_ex_1_regdst_2, id_ex_1_syscall_2, IR1, IR2, IR3, mem_wb_1_memtoreg_2,
       mem_wb_1_regdst_2, mem_wb_1_syscall_2, registerfile_1_p7, registerfile_1_p8, RST, SignedExt, TEN, W1,
       W2, W3, \硬布线控制器_1_alu_src , \硬布线控制器_1_memtoreg , \硬布线控制器_1_memwrite , \硬布线控制器_1_regdst ,
       \硬布线控制器_1_regwrite , \硬布线控制器_1_syscall ;
  wire [3:0] id_ex_1_alu_op_2, \硬布线控制器_1_alu_op ;
  wire [4:0] RW1, RW2, RW3;
  wire [15:0] \LoadUse次数 , \总周期数 , \插入气泡数 , \无条件分支数 , \条件分支成功数 ;
  wire [31:0] adder_1_out, bit_extender_1_out, bit_extender_2_out, din, ex_mem_1_alu_2, ex_mem_1_ir_2,
       ex_mem_1_r2_2, EX_PC, id_ex_1_imm_2, id_ex_1_ir_2, id_ex_1_r1_2, id_ex_1_r2_2, ID_PC, if_id_1_instr_2,
       IF_PC, Ins, LedData, MEM_PC, mem_wb_1_alu_2, mem_wb_1_dm_2, mem_wb_1_ir_2, mips_alu_1_result,
       mips_probe_2_p1, mips_ram_1_p7, mips_regifile_1_r1, mips_regifile_1_r2, multiplexer_4_out,
       multiplexer_5_out, R2, rom_2_data, rom_3_data, WB_PC;

  Button \u_总复位  (.out(RST));
  Button _1 (.out(IR1));
  Button _2 (.out(IR2));
  Button _3 (.out(IR3));
  Button \u_继续运行  (.out(Go));
  LED led_1 (.in(W1));
  LED led_2 (.in(W2));
  LED led_3 (.in(W3));
  Register #(.width(32)) register_1 (.D(R2), .en(eq34), .Q(LedData), .clk(CLK));  // open: clr
  not not_1 (EN, mem_wb_1_syscall_2);
  // Probe on IF_PC
  Hex_Digit_Display hex_digit_display_1 (.value(LedData[31:28]));  // open: dp
  Register #(.width(32)) PC (.D(adder_1_out), .en(EN), .Q(IF_PC), .clk(CLK), .clr(RST));
  // Probe on Ins
  // Probe on ID_PC
  // Probe on Ins
  Hex_Digit_Display hex_digit_display_2 (.value(LedData[23:20]));  // open: dp
  Hex_Digit_Display hex_digit_display_3 (.value(LedData[27:24]));  // open: dp
  // Mips_Probe mips_probe_1: pin names not known; wires that end beside it: Ins
  Hex_Digit_Display hex_digit_display_4 (.value(LedData[19:16]));  // open: dp
  Hex_Digit_Display hex_digit_display_5 (.value(LedData[15:12]));  // open: dp
  // Mips_Probe mips_probe_2: pin names not known; wires that end beside it: mips_probe_2_p1
  // Probe on if_id_1_instr_2
  // Probe on EX_PC
  // Probe on WB_PC
  Hex_Digit_Display hex_digit_display_6 (.value(LedData[11:8]));  // open: dp
  Hex_Digit_Display hex_digit_display_7 (.value(LedData[7:4]));  // open: dp
  Clock clock_1 (.out(CLK));
  Adder #(.width(32)) adder_1 (.a(IF_PC), .b(32'h4), .out(adder_1_out), .cin(1'b0));  // open: cout
  ROM #(.addrWidth(10), .dataWidth(32)) rom_1 (.addr(IF_PC[11:2]), .data(mips_probe_2_p1));  // open: sel
  // Probe on MEM_PC
  Hex_Digit_Display hex_digit_display_8 (.value(LedData[3:0]));  // open: dp
  IF_ID if_id_1 (
    .nextPC(IF_PC), .Instr(mips_probe_2_p1), .RST(RST), .CLK(CLK), .EN(EN), .nextPC_2(ID_PC),
    .Instr_2(if_id_1_instr_2));  // open: pre, pre_2
  ROM #(.addrWidth(10), .dataWidth(32)) rom_2 (.addr(WB_PC[11:2]), .data(rom_2_data));  // open: sel
  ROM #(.addrWidth(10), .dataWidth(32)) rom_3 (.addr(ID_PC[11:2]), .data(rom_3_data));  // open: sel
  // Probe on \总周期数 
  // Probe on \无条件分支数 
  // Probe on \条件分支成功数 
  // Probe on \插入气泡数 
  // Probe on \LoadUse次数 
  // Probe on if_id_1_instr_2[5:0]
  // Probe on if_id_1_instr_2[31:26]
  // Mips_Probe mips_probe_3: pin names not known; wires that end beside it: rom_2_data, rom_3_data
  // Probe on IF_PC[11:0]
  \硬布线控制器  \u_硬布线控制器_1  (
    .Func(if_id_1_instr_2[5:0]), .OP(if_id_1_instr_2[31:26]), .ALU_OP(\硬布线控制器_1_alu_op ),
    .MemToReg(\硬布线控制器_1_memtoreg ), .MemWrite(\硬布线控制器_1_memwrite ), .ALU_SRC(\硬布线控制器_1_alu_src ),
    .RegWrite(\硬布线控制器_1_regwrite ), .SysCALL(\硬布线控制器_1_syscall ), .SignedExt(SignedExt),
    .RegDst(\硬布线控制器_1_regdst ));  // open: JR, JMP, Beq, JAL, Bne, SRLV, LBU, BGTZ
  Multiplexer #(.width(5), .disabled(0), .enable("false")) multiplexer_1 (
    .in0(if_id_1_instr_2[25:21]), .in1(5'b00010), .out(RW1), .sel(\硬布线控制器_1_syscall ));
  Multiplexer #(.width(5), .disabled(0), .enable("false")) multiplexer_2 (
    .in0(if_id_1_instr_2[20:16]), .in1(5'b00100), .out(RW2), .sel(\硬布线控制器_1_syscall ));
  Multiplexer #(.width(5), .disabled(0), .enable("false")) multiplexer_3 (
    .in0(mem_wb_1_ir_2[20:16]), .in1(mem_wb_1_ir_2[15:11]), .out(RW3), .sel(mem_wb_1_regdst_2));
  assign bit_extender_1_out = {{16{1'b0}}, if_id_1_instr_2[15:0]};  // Bit_Extender bit_extender_1
  assign bit_extender_2_out = {{16{if_id_1_instr_2[15]}}, if_id_1_instr_2[15:0]};  // Bit_Extender bit_extender_2
  // Probe on ID_PC[11:0]
  // Probe on RW2
  Multiplexer #(.width(32), .disabled(0), .enable("false")) multiplexer_4 (
    .in0(bit_extender_1_out), .in1(bit_extender_2_out), .out(multiplexer_4_out), .sel(SignedExt));
  // RegisterFile registerfile_1: pin names not known; wires that end beside it: din, CLK, TEN, RW3, RW1, RW2, registerfile_1_p7, registerfile_1_p8
  // Probe on MEM_PC[11:0]
  // Probe on EX_PC[11:0]
  // Probe on registerfile_1_p7
  // Probe on registerfile_1_p8
  // Probe on RW1
  // Probe on RW2
  // Probe on RW3
  // Probe on WB_PC[11:0]
  MIPS_Regifile mips_regifile_1 (
    .Din(din), .Clk(CLK), .R1(mips_regifile_1_r1), .R2(mips_regifile_1_r2), .WE(TEN), .W_num(RW3),
    .R1_num(RW1), .R2_num(RW2));
  // Probe on mips_regifile_1_r2
  // Probe on multiplexer_4_out
  // Probe on din
  Counter #(.width(16), .max('hffff)) counter_1 (.count(EN), .Q(\总周期数 ), .clk(CLK), .clr(RST));  // open: load, D, carry
  ID_EX id_ex_1 (
    .nextPC(ID_PC), .ALU_SRC(\硬布线控制器_1_alu_src ), .R1(mips_regifile_1_r1), .MemToReg(\硬布线控制器_1_memtoreg ),
    .R2(mips_regifile_1_r2), .MemWrite(\硬布线控制器_1_memwrite ), .IMM(multiplexer_4_out),
    .SysCALL(\硬布线控制器_1_syscall ), .ALU_OP(\硬布线控制器_1_alu_op ), .nextPC_2(EX_PC),
    .ALU_SRC_2(id_ex_1_alu_src_2), .R1_2(id_ex_1_r1_2), .MemToReg_2(id_ex_1_memtoreg_2), .R2_2(id_ex_1_r2_2),
    .MemWrite_2(id_ex_1_memwrite_2), .IMM_2(id_ex_1_imm_2), .SysCALL_2(id_ex_1_syscall_2),
    .ALU_OP_2(id_ex_1_alu_op_2), .EN(EN), .IR(if_id_1_instr_2), .IR_2(id_ex_1_ir_2), .RST(RST), .CLK(CLK),
    .RegDst(\硬布线控制器_1_regdst ), .RegDst_2(id_ex_1_regdst_2), .Reg_Write(\硬布线控制器_1_regwrite ),
    .Reg_Write_2(id_ex_1_reg_write_2));  // open: BNE, BNE_2, BEQ, BEQ_2, J, J_2, BGTZ, BGTZ_2, fwd1, fwd1_2, fwd2, fwd2_2, eq34, eq34_2, SRLV, SRLV_2, LBU, LBU_2, Pre, Pre_2, simm, simm_2
  // Probe on mips_regifile_1_r1
  Comparator #(.width(32)) comparator_1 (.a(32'h22), .b(id_ex_1_r1_2), .eq(eq34));  // open: gt, lt
  MIPS_ALU mips_alu_1 (
    .X(id_ex_1_r1_2), .Y(multiplexer_5_out), .AluOP(id_ex_1_alu_op_2), .Result(mips_alu_1_result),
    .shamt(id_ex_1_ir_2[10:6]));  // open: Equal, Result_2
  Multiplexer #(.width(32), .disabled(0), .enable("false")) multiplexer_5 (
    .in0(id_ex_1_r2_2), .in1(id_ex_1_imm_2), .out(multiplexer_5_out), .sel(id_ex_1_alu_src_2));
  // Probe on mips_alu_1_result
  EX_MEM ex_mem_1 (
    .nextPC(EX_PC), .Reg_Write(id_ex_1_reg_write_2), .MemToReg(id_ex_1_memtoreg_2), .R2(id_ex_1_r2_2),
    .MemWrite(id_ex_1_memwrite_2), .RegDst(id_ex_1_regdst_2), .ALU(mips_alu_1_result), .RST(RST), .CLK(CLK),
    .IR(id_ex_1_ir_2), .SysCALL(id_ex_1_syscall_2), .nextPC_2(MEM_PC), .Reg_Write_2(ex_mem_1_reg_write_2),
    .MemToReg_2(ex_mem_1_memtoreg_2), .R2_2(ex_mem_1_r2_2), .MemWrite_2(ex_mem_1_memwrite_2),
    .RegDst_2(ex_mem_1_regdst_2), .ALU_2(ex_mem_1_alu_2), .IR_2(ex_mem_1_ir_2),
    .SysCALL_2(ex_mem_1_syscall_2), .EN(EN));  // open: BNE, BNE_2, BEQ, BEQ_2, J, EXJ, BGTZ, EXBGTZ, eq34, eq34_2, R1, R1_2, LBU, LBU_2
  // Probe on ex_mem_1_r2_2
  // MIPS_RAM mips_ram_1: pin names not known; wires that end beside it: ex_mem_1_alu_2[21:2], ex_mem_1_r2_2, ex_mem_1_memwrite_2, CLK, ex_mem_1_memtoreg_2, RST, mips_ram_1_p7
  MEM_WB mem_wb_1 (
    .nextPC(MEM_PC), .Reg_Write(ex_mem_1_reg_write_2), .MemToReg(ex_mem_1_memtoreg_2), .DM(mips_ram_1_p7),
    .RegDst(ex_mem_1_regdst_2), .ALU(ex_mem_1_alu_2), .RST(RST), .CLK(CLK), .IR(ex_mem_1_ir_2),
    .SysCALL(ex_mem_1_syscall_2), .nextPC_2(WB_PC), .Reg_Write_2(TEN), .MemToReg_2(mem_wb_1_memtoreg_2),
    .DM_2(mem_wb_1_dm_2), .RegDst_2(mem_wb_1_regdst_2), .ALU_2(mem_wb_1_alu_2), .IR_2(mem_wb_1_ir_2),
    .SysCALL_2(mem_wb_1_syscall_2), .EN(EN));  // open: EXJ, WBJ, LedData, LedData_2, R1_2, R1, eq34, eq34_2, LBU, WB_LBU
  Multiplexer #(.width(32), .disabled(0), .enable("false")) multiplexer_6 (
    .in0(mem_wb_1_alu_2), .in1(mem_wb_1_dm_2), .out(din), .sel(mem_wb_1_memtoreg_2));

  // Notes on the sheet:
  //   中断源
  //   中断等待指示
  //   数码管输出
  //   指令存储器
  //   contents of rom_1 (hex, n*v repeats v):
  //   20100000 20110000 20120000 20130000 36100000 36310001 36520002 36730003 ae100000 ae110004 ae120008
  //   ae13000c 2002000a 20110000 20120000 20130000 c
  //   contents of rom_2 (hex, n*v repeats v):
  //   20100000 20110000 20120000 20130000 36100000 36310001 36520002 36730003 ae100000 ae110004 ae120008
  //   ae13000c 2002000a 20110000 20120000 20130000 c
  //   rs
  //   rt
  //   rd
  //   contents of rom_3 (hex, n*v repeats v):
  //   20100000 20110000 20120000 20130000 36100000 36310001 36520002 36730003 ae100000 ae110004 ae120008
  //   ae13000c 2002000a 20110000 20120000 20130000 c
  //   OP
  //   Func
  //   Syscall
  //   MemToReg
  //   MemWrite
  //   AluOP
  //   AluSrcB
  //   RegWrite
  //   RegDst
  //   流水调试日志用
endmodule

// 源寄存器使用情况
module \源寄存器使用情况  (
  input  OP0,
  input  OP1,
  input  OP2,
  input  OP3,
  input  OP4,
  input  OP5,
  input  F0,
  input  F1,
  input  F2,
  input  F3,
  input  F4,
  input  F5,
  output R1_Used,
  output R2_Used
);

  wire and_1_out, and_2_out, and_3_out, and_4_out, and_5_out, and_6_out, and_7_out, and_8_out, and_9_out,
       and_10_out, and_11_out, and_12_out, and_13_out, and_14_out, and_15_out, and_16_out, and_17_out,
       and_18_out, and_19_out, and_20_out, and_21_out, and_22_out, and_23_out, and_24_out, and_25_out,
       and_26_out, and_27_out, and_28_out, and_29_out, and_30_out, and_31_out, and_32_out, and_33_out,
       and_34_out, and_35_out, and_36_out, and_37_out, and_38_out, and_39_out, and_40_out, and_41_out,
       not_1_out, not_2_out, not_3_out, not_4_out, not_5_out, not_6_out, not_7_out, not_8_out, not_9_out,
       not_10_out, not_11_out, not_12_out, not_13_out, not_14_out, not_15_out, not_16_out, not_17_out,
       not_18_out, not_19_out, not_20_out, not_21_out, not_22_out, not_23_out, not_24_out, not_25_out,
       not_26_out, not_27_out, not_28_out, not_29_out, not_30_out, not_31_out, not_32_out, not_33_out,
       not_34_out, not_35_out, not_36_out, not_37_out, not_38_out, not_39_out, not_40_out, not_41_out,
       not_42_out, not_43_out, not_44_out, not_45_out, not_46_out, not_47_out, not_48_out, not_49_out,
       not_50_out, not_51_out, not_52_out, not_53_out, not_54_out, not_55_out, not_56_out, not_57_out,
       not_58_out, not_59_out, not_60_out, not_61_out, not_62_out, not_63_out, not_64_out, not_65_out,
       not_66_out, not_67_out, not_68_out, not_69_out, not_70_out, not_71_out, not_72_out, not_73_out,
       not_74_out, not_75_out, not_76_out, not_77_out, not_78_out, not_79_out, not_80_out, not_81_out,
       not_82_out, not_83_out, not_84_out, not_85_out, not_86_out, not_87_out, not_88_out, not_89_out,
       not_90_out, not_91_out, not_92_out, not_93_out, not_94_out, not_95_out, not_96_out, not_97_out,
       not_98_out, not_99_out, not_100_out, not_101_out, not_102_out, not_103_out, not_104_out, not_105_out,
       not_106_out, not_107_out, not_108_out, not_109_out, not_110_out, not_111_out, not_112_out,
       not_113_out, not_114_out, not_115_out, not_116_out, not_117_out, not_118_out, not_119_out,
       not_120_out, not_121_out, not_122_out, not_123_out, not_124_out, not_125_out, not_126_out,
       not_127_out, not_128_out, not_129_out, not_130_out, not_131_out, not_132_out, not_133_out,
       not_134_out, not_135_out, not_136_out, not_137_out, not_138_out, not_139_out, not_140_out,
       not_141_out, not_142_out, not_143_out, not_144_out, not_145_out, not_146_out, not_147_out,
       not_148_out, not_149_out, not_150_out, not_151_out, not_152_out, not_153_out, not_154_out,
       not_155_out, not_156_out, not_157_out, not_158_out, not_159_out, not_160_out, not_161_out,
       not_162_out, not_163_out, not_164_out, not_165_out, not_166_out, not_167_out, not_168_out,
       not_169_out, not_170_out, not_171_out, not_172_out, not_173_out, not_174_out, not_175_out,
       not_176_out, not_177_out, not_178_out, not_179_out, not_180_out, not_181_out, not_182_out,
       not_183_out, not_184_out, not_185_out, not_186_out, not_187_out, not_188_out, not_189_out,
       not_190_out, not_191_out, not_192_out, not_193_out, not_194_out, not_195_out, not_196_out,
       not_197_out, not_198_out, not_199_out, not_200_out, not_201_out, not_202_out, not_203_out,
       not_204_out, not_205_out, not_206_out, not_207_out, not_208_out, not_209_out, not_210_out,
       not_211_out, not_212_out, not_213_out, not_214_out, not_215_out, not_216_out, not_217_out,
       not_218_out, not_219_out, not_220_out, not_221_out, not_222_out, not_223_out, not_224_out,
       not_225_out, not_226_out, not_227_out, not_228_out, not_229_out, not_230_out, not_231_out,
       not_232_out, not_233_out, not_234_out, not_235_out, not_236_out, not_237_out, not_238_out,
       not_239_out, not_240_out, not_241_out, not_242_out, not_243_out, not_244_out, not_245_out,
       not_246_out, not_247_out, not_248_out, not_249_out, not_250_out, not_251_out, not_252_out,
       not_253_out, not_254_out, not_255_out, not_256_out, not_257_out, not_258_out, not_259_out,
       not_260_out, not_261_out, not_262_out, not_263_out, not_264_out, not_265_out, not_266_out,
       not_267_out, not_268_out, not_269_out, not_270_out, not_271_out, not_272_out, not_273_out,
       not_274_out, not_275_out, not_276_out, not_277_out, not_278_out, not_279_out, not_280_out,
       not_281_out, not_282_out, not_283_out, not_284_out, not_285_out, not_286_out, not_287_out,
       not_288_out, not_289_out, not_290_out, not_291_out, not_292_out, not_293_out, not_294_out,
       not_295_out, not_296_out, not_297_out, not_298_out, not_299_out, not_300_out, not_301_out,
       not_302_out, not_303_out, not_304_out, not_305_out, not_306_out, not_307_out, not_308_out;

  not not_1 (not_1_out, OP5);
  not not_2 (not_2_out, OP4);
  not not_3 (not_3_out, OP3);
  not not_4 (not_4_out, OP2);
  not not_5 (not_5_out, OP1);
  not not_6 (not_6_out, OP0);
  not not_7 (not_7_out, F4);
  not not_8 (not_8_out, F3);
  not not_9 (not_9_out, F2);
  not not_10 (not_10_out, F1);
  not not_11 (not_11_out, F0);
  not not_12 (not_12_out, OP5);
  not not_13 (not_13_out, OP4);
  not not_14 (not_14_out, OP3);
  not not_15 (not_15_out, OP2);
  not not_16 (not_16_out, OP1);
  not not_17 (not_17_out, OP0);
  not not_18 (not_18_out, F4);
  not not_19 (not_19_out, F3);
  not not_20 (not_20_out, F2);
  not not_21 (not_21_out, F1);
  not not_22 (not_22_out, OP5);
  not not_23 (not_23_out, OP4);
  not not_24 (not_24_out, OP3);
  not not_25 (not_25_out, OP2);
  not not_26 (not_26_out, OP1);
  not not_27 (not_27_out, OP0);
  not not_28 (not_28_out, F4);
  not not_29 (not_29_out, F3);
  not not_30 (not_30_out, F2);
  not not_31 (not_31_out, F0);
  not not_32 (not_32_out, OP5);
  not not_33 (not_33_out, OP4);
  not not_34 (not_34_out, OP3);
  not not_35 (not_35_out, OP2);
  not not_36 (not_36_out, OP1);
  not not_37 (not_37_out, OP0);
  not not_38 (not_38_out, F4);
  not not_39 (not_39_out, F3);
  not not_40 (not_40_out, F1);
  not not_41 (not_41_out, F0);
  not not_42 (not_42_out, OP5);
  not not_43 (not_43_out, OP4);
  not not_44 (not_44_out, OP3);
  not not_45 (not_45_out, OP2);
  not not_46 (not_46_out, OP1);
  not not_47 (not_47_out, OP0);
  not not_48 (not_48_out, F4);
  not not_49 (not_49_out, F3);
  not not_50 (not_50_out, F1);
  not not_51 (not_51_out, OP5);
  not not_52 (not_52_out, OP4);
  not not_53 (not_53_out, OP3);
  not not_54 (not_54_out, OP2);
  not not_55 (not_55_out, OP1);
  not not_56 (not_56_out, OP0);
  not not_57 (not_57_out, F4);
  not not_58 (not_58_out, F3);
  not not_59 (not_59_out, OP5);
  not not_60 (not_60_out, OP4);
  not not_61 (not_61_out, OP3);
  not not_62 (not_62_out, OP2);
  not not_63 (not_63_out, OP1);
  not not_64 (not_64_out, OP0);
  not not_65 (not_65_out, F4);
  not not_66 (not_66_out, F2);
  not not_67 (not_67_out, F0);
  not not_68 (not_68_out, OP5);
  not not_69 (not_69_out, OP4);
  not not_70 (not_70_out, OP3);
  not not_71 (not_71_out, OP2);
  not not_72 (not_72_out, OP1);
  not not_73 (not_73_out, OP0);
  not not_74 (not_74_out, F4);
  not not_75 (not_75_out, F2);
  not not_76 (not_76_out, OP5);
  not not_77 (not_77_out, OP4);
  not not_78 (not_78_out, OP3);
  not not_79 (not_79_out, OP2);
  not not_80 (not_80_out, OP1);
  not not_81 (not_81_out, OP0);
  not not_82 (not_82_out, F5);
  not not_83 (not_83_out, F4);
  not not_84 (not_84_out, F2);
  not not_85 (not_85_out, F1);
  not not_86 (not_86_out, F0);
  not not_87 (not_87_out, OP5);
  not not_88 (not_88_out, OP4);
  not not_89 (not_89_out, OP3);
  not not_90 (not_90_out, OP2);
  not not_91 (not_91_out, OP1);
  not not_92 (not_92_out, OP0);
  not not_93 (not_93_out, F5);
  not not_94 (not_94_out, F4);
  not not_95 (not_95_out, F1);
  not not_96 (not_96_out, F0);
  not not_97 (not_97_out, OP5);
  not not_98 (not_98_out, OP4);
  not not_99 (not_99_out, OP3);
  not not_100 (not_100_out, OP1);
  not not_101 (not_101_out, OP0);
  not not_102 (not_102_out, OP5);
  not not_103 (not_103_out, OP4);
  not not_104 (not_104_out, OP3);
  not not_105 (not_105_out, OP1);
  not not_106 (not_106_out, OP5);
  not not_107 (not_107_out, OP4);
  not not_108 (not_108_out, OP2);
  not not_109 (not_109_out, OP1);
  not not_110 (not_110_out, OP0);
  not not_111 (not_111_out, OP5);
  not not_112 (not_112_out, OP4);
  not not_113 (not_113_out, OP1);
  not not_114 (not_114_out, OP0);
  not not_115 (not_115_out, OP5);
  not not_116 (not_116_out, OP4);
  not not_117 (not_117_out, OP2);
  not not_118 (not_118_out, OP1);
  not not_119 (not_119_out, OP5);
  not not_120 (not_120_out, OP4);
  not not_121 (not_121_out, OP2);
  not not_122 (not_122_out, OP0);
  not not_123 (not_123_out, OP5);
  not not_124 (not_124_out, OP4);
  not not_125 (not_125_out, OP1);
  not not_126 (not_126_out, OP4);
  not not_127 (not_127_out, OP3);
  not not_128 (not_128_out, OP2);
  not not_129 (not_129_out, OP4);
  not not_130 (not_130_out, OP2);
  not not_131 (not_131_out, OP5);
  not not_132 (not_132_out, OP4);
  not not_133 (not_133_out, OP3);
  not not_134 (not_134_out, OP2);
  not not_135 (not_135_out, OP1);
  not not_136 (not_136_out, OP0);
  not not_137 (not_137_out, F5);
  not not_138 (not_138_out, F4);
  not not_139 (not_139_out, F3);
  not not_140 (not_140_out, F0);
  not not_141 (not_141_out, OP5);
  not not_142 (not_142_out, OP4);
  not not_143 (not_143_out, OP3);
  not not_144 (not_144_out, OP2);
  not not_145 (not_145_out, OP1);
  not not_146 (not_146_out, OP0);
  not not_147 (not_147_out, F4);
  not not_148 (not_148_out, F3);
  not not_149 (not_149_out, F0);
  not not_150 (not_150_out, OP4);
  not not_151 (not_151_out, OP3);
  not not_152 (not_152_out, OP1);
  not not_153 (not_153_out, OP0);
  not not_154 (not_154_out, OP5);
  not not_155 (not_155_out, OP4);
  not not_156 (not_156_out, OP3);
  not not_157 (not_157_out, OP5);
  not not_158 (not_158_out, OP4);
  not not_159 (not_159_out, OP3);
  not not_160 (not_160_out, OP2);
  not not_161 (not_161_out, OP1);
  not not_162 (not_162_out, OP0);
  not not_163 (not_163_out, F5);
  not not_164 (not_164_out, F4);
  not not_165 (not_165_out, F3);
  not not_166 (not_166_out, F2);
  not not_167 (not_167_out, F1);
  not not_168 (not_168_out, F0);
  not not_169 (not_169_out, OP5);
  not not_170 (not_170_out, OP4);
  not not_171 (not_171_out, OP3);
  not not_172 (not_172_out, OP2);
  not not_173 (not_173_out, OP1);
  not not_174 (not_174_out, OP0);
  not not_175 (not_175_out, F5);
  not not_176 (not_176_out, F4);
  not not_177 (not_177_out, F3);
  not not_178 (not_178_out, F2);
  not not_179 (not_179_out, OP5);
  not not_180 (not_180_out, OP4);
  not not_181 (not_181_out, OP3);
  not not_182 (not_182_out, OP2);
  not not_183 (not_183_out, OP1);
  not not_184 (not_184_out, OP0);
  not not_185 (not_185_out, F5);
  not not_186 (not_186_out, F4);
  not not_187 (not_187_out, F3);
  not not_188 (not_188_out, F2);
  not not_189 (not_189_out, F0);
  not not_190 (not_190_out, OP5);
  not not_191 (not_191_out, OP4);
  not not_192 (not_192_out, OP3);
  not not_193 (not_193_out, OP2);
  not not_194 (not_194_out, OP1);
  not not_195 (not_195_out, OP0);
  not not_196 (not_196_out, F4);
  not not_197 (not_197_out, F3);
  not not_198 (not_198_out, F2);
  not not_199 (not_199_out, F1);
  not not_200 (not_200_out, F0);
  not not_201 (not_201_out, OP5);
  not not_202 (not_202_out, OP4);
  not not_203 (not_203_out, OP3);
  not not_204 (not_204_out, OP2);
  not not_205 (not_205_out, OP1);
  not not_206 (not_206_out, OP0);
  not not_207 (not_207_out, F4);
  not not_208 (not_208_out, F3);
  not not_209 (not_209_out, F2);
  not not_210 (not_210_out, F1);
  not not_211 (not_211_out, OP5);
  not not_212 (not_212_out, OP4);
  not not_213 (not_213_out, OP3);
  not not_214 (not_214_out, OP2);
  not not_215 (not_215_out, OP1);
  not not_216 (not_216_out, OP0);
  not not_217 (not_217_out, F4);
  not not_218 (not_218_out, F3);
  not not_219 (not_219_out, F2);
  not not_220 (not_220_out, F0);
  not not_221 (not_221_out, OP5);
  not not_222 (not_222_out, OP4);
  not not_223 (not_223_out, OP3);
  not not_224 (not_224_out, OP2);
  not not_225 (not_225_out, OP1);
  not not_226 (not_226_out, OP0);
  not not_227 (not_227_out, F4);
  not not_228 (not_228_out, F3);
  not not_229 (not_229_out, F1);
  not not_230 (not_230_out, F0);
  not not_231 (not_231_out, OP5);
  not not_232 (not_232_out, OP4);
  not not_233 (not_233_out, OP3);
  not not_234 (not_234_out, OP2);
  not not_235 (not_235_out, OP1);
  not not_236 (not_236_out, OP0);
  not not_237 (not_237_out, F4);
  not not_238 (not_238_out, F3);
  not not_239 (not_239_out, F1);
  not not_240 (not_240_out, OP5);
  not not_241 (not_241_out, OP4);
  not not_242 (not_242_out, OP3);
  not not_243 (not_243_out, OP2);
  not not_244 (not_244_out, OP1);
  not not_245 (not_245_out, OP0);
  not not_246 (not_246_out, F4);
  not not_247 (not_247_out, F3);
  not not_248 (not_248_out, OP5);
  not not_249 (not_249_out, OP4);
  not not_250 (not_250_out, OP3);
  not not_251 (not_251_out, OP2);
  not not_252 (not_252_out, OP1);
  not not_253 (not_253_out, OP0);
  not not_254 (not_254_out, F4);
  not not_255 (not_255_out, F2);
  not not_256 (not_256_out, F0);
  not not_257 (not_257_out, OP5);
  not not_258 (not_258_out, OP4);
  not not_259 (not_259_out, OP3);
  not not_260 (not_260_out, OP2);
  not not_261 (not_261_out, OP1);
  not not_262 (not_262_out, OP0);
  not not_263 (not_263_out, F4);
  not not_264 (not_264_out, F2);
  not not_265 (not_265_out, OP5);
  not not_266 (not_266_out, OP4);
  not not_267 (not_267_out, OP3);
  not not_268 (not_268_out, OP2);
  not not_269 (not_269_out, OP1);
  not not_270 (not_270_out, OP0);
  not not_271 (not_271_out, F5);
  not not_272 (not_272_out, F4);
  not not_273 (not_273_out, F1);
  not not_274 (not_274_out, F0);
  not not_275 (not_275_out, OP5);
  not not_276 (not_276_out, OP4);
  not not_277 (not_277_out, OP3);
  not not_278 (not_278_out, OP1);
  not not_279 (not_279_out, OP0);
  not not_280 (not_280_out, OP5);
  not not_281 (not_281_out, OP4);
  not not_282 (not_282_out, OP3);
  not not_283 (not_283_out, OP1);
  not not_284 (not_284_out, OP4);
  not not_285 (not_285_out, OP2);
  not not_286 (not_286_out, OP5);
  not not_287 (not_287_out, OP4);
  not not_288 (not_288_out, OP3);
  not not_289 (not_289_out, OP2);
  not not_290 (not_290_out, OP1);
  not not_291 (not_291_out, OP0);
  not not_292 (not_292_out, F5);
  not not_293 (not_293_out, F4);
  not not_294 (not_294_out, F3);
  not not_295 (not_295_out, F0);
  not not_296 (not_296_out, OP5);
  not not_297 (not_297_out, OP4);
  not not_298 (not_298_out, OP3);
  not not_299 (not_299_out, OP2);
  not not_300 (not_300_out, OP1);
  not not_301 (not_301_out, OP0);
  not not_302 (not_302_out, F4);
  not not_303 (not_303_out, F3);
  not not_304 (not_304_out, F0);
  not not_305 (not_305_out, OP4);
  not not_306 (not_306_out, OP3);
  not not_307 (not_307_out, OP1);
  not not_308 (not_308_out, OP0);
  and and_1 (and_1_out, not_1_out, not_2_out, not_3_out, not_4_out, not_5_out, not_6_out, F5, not_7_out, not_8_out, not_9_out, not_10_out, not_11_out);
  and and_2 (and_2_out, not_12_out, not_13_out, not_14_out, not_15_out, not_16_out, not_17_out, F5, not_18_out, not_19_out, not_20_out, not_21_out, F0);
  and and_3 (and_3_out, not_22_out, not_23_out, not_24_out, not_25_out, not_26_out, not_27_out, F5, not_28_out, not_29_out, not_30_out, F1, not_31_out);
  and and_4 (and_4_out, not_32_out, not_33_out, not_34_out, not_35_out, not_36_out, not_37_out, F5, not_38_out, not_39_out, F2, not_40_out, not_41_out);
  and and_5 (and_5_out, not_42_out, not_43_out, not_44_out, not_45_out, not_46_out, not_47_out, F5, not_48_out, not_49_out, F2, not_50_out, F0);
  and and_6 (and_6_out, not_51_out, not_52_out, not_53_out, not_54_out, not_55_out, not_56_out, F5, not_57_out, not_58_out, F2, F1, F0);
  and and_7 (and_7_out, not_59_out, not_60_out, not_61_out, not_62_out, not_63_out, not_64_out, F5, not_65_out, F3, not_66_out, F1, not_67_out);
  and and_8 (and_8_out, not_68_out, not_69_out, not_70_out, not_71_out, not_72_out, not_73_out, F5, not_74_out, F3, not_75_out, F1, F0);
  and and_9 (and_9_out, not_76_out, not_77_out, not_78_out, not_79_out, not_80_out, not_81_out, not_82_out, not_83_out, F3, not_84_out, not_85_out, not_86_out);
  and and_10 (and_10_out, not_87_out, not_88_out, not_89_out, not_90_out, not_91_out, not_92_out, not_93_out, not_94_out, F3, F2, not_95_out, not_96_out);
  and and_11 (and_11_out, not_97_out, not_98_out, not_99_out, OP2, not_100_out, not_101_out);
  and and_12 (and_12_out, not_102_out, not_103_out, not_104_out, OP2, not_105_out, OP0);
  and and_13 (and_13_out, not_106_out, not_107_out, OP3, not_108_out, not_109_out, not_110_out);
  and and_14 (and_14_out, not_111_out, not_112_out, OP3, OP2, not_113_out, not_114_out);
  and and_15 (and_15_out, not_115_out, not_116_out, OP3, not_117_out, not_118_out, OP0);
  and and_16 (and_16_out, not_119_out, not_120_out, OP3, not_121_out, OP1, not_122_out);
  and and_17 (and_17_out, not_123_out, not_124_out, OP3, OP2, not_125_out, OP0);
  and and_18 (and_18_out, OP5, not_126_out, not_127_out, not_128_out, OP1, OP0);
  and and_19 (and_19_out, OP5, not_129_out, OP3, not_130_out, OP1, OP0);
  and and_20 (and_20_out, not_131_out, not_132_out, not_133_out, not_134_out, not_135_out, not_136_out, not_137_out, not_138_out, not_139_out, F2, F1, not_140_out);
  and and_21 (and_21_out, not_141_out, not_142_out, not_143_out, not_144_out, not_145_out, not_146_out, F5, not_147_out, not_148_out, F2, F1, not_149_out);
  and and_22 (and_22_out, OP5, not_150_out, not_151_out, OP2, not_152_out, not_153_out);
  and and_23 (and_23_out, not_154_out, not_155_out, not_156_out, OP2, OP1, OP0);
  and and_24 (and_24_out, not_157_out, not_158_out, not_159_out, not_160_out, not_161_out, not_162_out, not_163_out, not_164_out, not_165_out, not_166_out, not_167_out, not_168_out);
  and and_25 (and_25_out, not_169_out, not_170_out, not_171_out, not_172_out, not_173_out, not_174_out, not_175_out, not_176_out, not_177_out, not_178_out, F1, F0);
  and and_26 (and_26_out, not_179_out, not_180_out, not_181_out, not_182_out, not_183_out, not_184_out, not_185_out, not_186_out, not_187_out, not_188_out, F1, not_189_out);
  and and_27 (and_27_out, not_190_out, not_191_out, not_192_out, not_193_out, not_194_out, not_195_out, F5, not_196_out, not_197_out, not_198_out, not_199_out, not_200_out);
  and and_28 (and_28_out, not_201_out, not_202_out, not_203_out, not_204_out, not_205_out, not_206_out, F5, not_207_out, not_208_out, not_209_out, not_210_out, F0);
  and and_29 (and_29_out, not_211_out, not_212_out, not_213_out, not_214_out, not_215_out, not_216_out, F5, not_217_out, not_218_out, not_219_out, F1, not_220_out);
  and and_30 (and_30_out, not_221_out, not_222_out, not_223_out, not_224_out, not_225_out, not_226_out, F5, not_227_out, not_228_out, F2, not_229_out, not_230_out);
  and and_31 (and_31_out, not_231_out, not_232_out, not_233_out, not_234_out, not_235_out, not_236_out, F5, not_237_out, not_238_out, F2, not_239_out, F0);
  and and_32 (and_32_out, not_240_out, not_241_out, not_242_out, not_243_out, not_244_out, not_245_out, F5, not_246_out, not_247_out, F2, F1, F0);
  and and_33 (and_33_out, not_248_out, not_249_out, not_250_out, not_251_out, not_252_out, not_253_out, F5, not_254_out, F3, not_255_out, F1, not_256_out);
  and and_34 (and_34_out, not_257_out, not_258_out, not_259_out, not_260_out, not_261_out, not_262_out, F5, not_263_out, F3, not_264_out, F1, F0);
  and and_35 (and_35_out, not_265_out, not_266_out, not_267_out, not_268_out, not_269_out, not_270_out, not_271_out, not_272_out, F3, F2, not_273_out, not_274_out);
  and and_36 (and_36_out, not_275_out, not_276_out, not_277_out, OP2, not_278_out, not_279_out);
  and and_37 (and_37_out, not_280_out, not_281_out, not_282_out, OP2, not_283_out, OP0);
  and and_38 (and_38_out, OP5, not_284_out, OP3, not_285_out, OP1, OP0);
  and and_39 (and_39_out, not_286_out, not_287_out, not_288_out, not_289_out, not_290_out, not_291_out, not_292_out, not_293_out, not_294_out, F2, F1, not_295_out);
  and and_40 (and_40_out, not_296_out, not_297_out, not_298_out, not_299_out, not_300_out, not_301_out, F5, not_302_out, not_303_out, F2, F1, not_304_out);
  and and_41 (and_41_out, OP5, not_305_out, not_306_out, OP2, not_307_out, not_308_out);
  or or_1 (R1_Used, and_1_out, and_2_out, and_3_out, and_4_out, and_5_out, and_6_out, and_7_out, and_8_out, and_9_out, and_10_out, and_11_out, and_12_out, and_13_out, and_14_out, and_15_out, and_16_out, and_17_out, and_18_out, and_19_out, and_20_out, and_21_out, and_22_out, and_23_out);
  or or_2 (R2_Used, and_24_out, and_25_out, and_26_out, and_27_out, and_28_out, and_29_out, and_30_out, and_31_out, and_32_out, and_33_out, and_34_out, and_35_out, and_36_out, and_37_out, and_38_out, and_39_out, and_40_out, and_41_out);
endmodule

module \数据相关检测  (
  input  [5:0] OP,
  input  [4:0] EX_WriteReg_num,
  input  EX_RegWrite,
  input  [4:0] MEM_WriteReg_num,
  input  MEM_RegWrite,
  input  [5:0] Func,
  input  [4:0] ID_R1_num,
  input  [4:0] ID_R2_num,
  output \数据相关 
);

  wire and_1_out, and_2_out, and_3_out, and_4_out, and_5_out, and_6_out, comparator_1_eq, comparator_2_eq,
       comparator_3_eq, comparator_4_eq, comparator_5_eq, comparator_6_eq, not_1_out, not_2_out, or_1_out,
       or_2_out, \源寄存器使用情况_1_r1_used , \源寄存器使用情况_1_r2_used ;

  \源寄存器使用情况  \u_源寄存器使用情况_1  (
    .OP0(OP[0]), .OP1(OP[1]), .OP2(OP[2]), .OP3(OP[3]), .OP4(OP[4]), .OP5(OP[5]), .F0(Func[0]), .F1(Func[1]),
    .F2(Func[2]), .F3(Func[3]), .F4(Func[4]), .F5(Func[5]), .R1_Used(\源寄存器使用情况_1_r1_used ),
    .R2_Used(\源寄存器使用情况_1_r2_used ));
  Comparator #(.width(5)) comparator_1 (.a(ID_R1_num), .b({5{1'b0}}), .eq(comparator_1_eq));  // open: gt, lt
  Comparator #(.width(5)) comparator_2 (.a(ID_R2_num), .b({5{1'b0}}), .eq(comparator_2_eq));  // open: gt, lt
  Comparator #(.width(5)) comparator_3 (.a(ID_R1_num), .b(MEM_WriteReg_num), .eq(comparator_3_eq));  // open: gt, lt
  Comparator #(.width(5)) comparator_4 (.a(ID_R2_num), .b(MEM_WriteReg_num), .eq(comparator_4_eq));  // open: gt, lt
  not not_1 (not_1_out, comparator_1_eq);
  Comparator #(.width(5)) comparator_5 (.a(ID_R2_num), .b(EX_WriteReg_num), .eq(comparator_5_eq));  // open: gt, lt
  Comparator #(.width(5)) comparator_6 (.a(ID_R1_num), .b(EX_WriteReg_num), .eq(comparator_6_eq));  // open: gt, lt
  not not_2 (not_2_out, comparator_2_eq);
  and and_1 (and_1_out, \源寄存器使用情况_1_r2_used , comparator_5_eq, not_2_out);
  and and_2 (and_2_out, \源寄存器使用情况_1_r1_used , comparator_6_eq, not_1_out);
  and and_3 (and_3_out, \源寄存器使用情况_1_r1_used , comparator_3_eq, not_1_out);
  and and_4 (and_4_out, not_2_out, comparator_4_eq, \源寄存器使用情况_1_r2_used );
  and and_5 (and_5_out, EX_RegWrite, or_1_out);
  or or_1 (or_1_out, and_1_out, and_2_out);
  and and_6 (and_6_out, MEM_RegWrite, or_2_out);
  or or_2 (or_2_out, and_3_out, and_4_out);
  or or_3 (\数据相关 , and_5_out, and_6_out);

  // Other names for the same wires on the sheet: OP_CODE[5:0] = OP
endmodule

module IF_ID (
  input  [31:0] nextPC,
  input  [31:0] Instr,
  input  pre,
  input  RST,
  input  EN,
  input  CLK,
  output [31:0] nextPC_2,
  output [31:0] Instr_2,
  output pre_2
);

  wire multiplexer_3_out;
  wire [31:0] multiplexer_1_out, multiplexer_2_out;

  Multiplexer #(.width(32), .enable("false")) multiplexer_1 (
    .in0(nextPC), .in1({32{1'b0}}), .out(multiplexer_1_out), .sel(RST));
  Multiplexer #(.width(32), .enable("false")) multiplexer_2 (
    .in0(Instr), .in1({32{1'b0}}), .out(multiplexer_2_out), .sel(RST));
  Multiplexer #(.enable("false")) multiplexer_3 (.in0(pre), .in1(1'b0), .out(multiplexer_3_out), .sel(RST));
  Register #(.width(32)) register_1 (.D(multiplexer_1_out), .en(EN), .Q(nextPC_2), .clk(CLK));  // open: clr
  Register #(.width(32)) register_2 (.D(multiplexer_2_out), .en(EN), .Q(Instr_2), .clk(CLK));  // open: clr
  Register #(.width(1)) register_3 (.D(multiplexer_3_out), .en(EN), .Q(pre_2), .clk(CLK));  // open: clr
endmodule
module ID_EX (
  input  [31:0] nextPC,
  input  RST,
  input  CLK,
  input  ALU_SRC,
  input  [31:0] R1,
  input  MemToReg,
  input  [31:0] R2,
  input  MemWrite,
  input  RegDst,
  input  [31:0] IMM,
  input  SRLV,
  input  [31:0] IR,
  input  SysCALL,
  input  [3:0] ALU_OP,
  input  BNE,
  input  BEQ,
  input  Reg_Write,
  input  [2:0] J,
  input  BGTZ,
  input  [1:0] fwd2,
  input  [1:0] fwd1,
  input  eq34,
  input  LBU,
  input  [31:0] simm,
  input  Pre,
  input  EN,
  output [31:0] nextPC_2,
  output ALU_SRC_2,
  output [31:0] R1_2,
  output MemToReg_2,
  output [31:0] R2_2,
  output MemWrite_2,
  output RegDst_2,
  output [31:0] IMM_2,
  output SRLV_2,
  output [31:0] IR_2,
  output SysCALL_2,
  output [3:0] ALU_OP_2,
  output BNE_2,
  output BEQ_2,
  output Reg_Write_2,
  output [2:0] J_2,
  output BGTZ_2,
  output [1:0] fwd2_2,
  output [1:0] fwd1_2,
  output eq34_2,
  output LBU_2,
  output [31:0] simm_2,
  output Pre_2
);

  wire multiplexer_2_out, multiplexer_3_out, multiplexer_4_out, multiplexer_5_out, multiplexer_6_out,
       multiplexer_7_out, multiplexer_9_out, multiplexer_10_out, multiplexer_12_out, multiplexer_13_out,
       multiplexer_18_out, multiplexer_19_out, multiplexer_22_out;
  wire [1:0] multiplexer_11_out, multiplexer_21_out;
  wire [2:0] multiplexer_20_out;
  wire [3:0] multiplexer_8_out;
  wire [31:0] multiplexer_1_out, multiplexer_14_out, multiplexer_15_out, multiplexer_16_out,
       multiplexer_17_out, multiplexer_23_out;

  Multiplexer #(.width(32), .enable("false")) multiplexer_1 (
    .in0(nextPC), .in1({32{1'b0}}), .out(multiplexer_1_out), .sel(RST));
  Multiplexer #(.enable("false")) multiplexer_2 (.in0(ALU_SRC), .in1(1'b0), .out(multiplexer_2_out), .sel(RST));
  Multiplexer #(.enable("false")) multiplexer_3 (.in0(MemToReg), .in1(1'b0), .out(multiplexer_3_out), .sel(RST));
  Multiplexer #(.enable("false")) multiplexer_4 (.in0(MemWrite), .in1(1'b0), .out(multiplexer_4_out), .sel(RST));
  Multiplexer #(.enable("false")) multiplexer_5 (.in0(RegDst), .in1(1'b0), .out(multiplexer_5_out), .sel(RST));
  Multiplexer #(.enable("false")) multiplexer_6 (.in0(SRLV), .in1(1'b0), .out(multiplexer_6_out), .sel(RST));
  Multiplexer #(.enable("false")) multiplexer_7 (.in0(SysCALL), .in1(1'b0), .out(multiplexer_7_out), .sel(RST));
  Multiplexer #(.width(4), .enable("false")) multiplexer_8 (
    .in0(ALU_OP), .in1(4'b0000), .out(multiplexer_8_out), .sel(RST));
  Multiplexer #(.enable("false")) multiplexer_9 (.in0(Reg_Write), .in1(1'b0), .out(multiplexer_9_out), .sel(RST));
  Multiplexer #(.enable("false")) multiplexer_10 (.in0(BGTZ), .in1(1'b0), .out(multiplexer_10_out), .sel(RST));
  Multiplexer #(.width(2), .enable("false")) multiplexer_11 (
    .in0(fwd1), .in1(2'b00), .out(multiplexer_11_out), .sel(RST));
  Multiplexer #(.enable("false")) multiplexer_12 (.in0(LBU), .in1(1'b0), .out(multiplexer_12_out), .sel(RST));
  Multiplexer #(.enable("false")) multiplexer_13 (.in0(Pre), .in1(1'b0), .out(multiplexer_13_out), .sel(RST));
  Register #(.width(32)) register_1 (.D(multiplexer_1_out), .en(EN), .Q(nextPC_2), .clk(CLK));  // open: clr
  Register #(.width(1)) register_2 (.D(multiplexer_2_out), .en(EN), .Q(ALU_SRC_2), .clk(CLK));  // open: clr
  Register #(.width(1)) register_3 (.D(multiplexer_3_out), .en(EN), .Q(MemToReg_2), .clk(CLK));  // open: clr
  Register #(.width(1)) register_4 (.D(multiplexer_4_out), .en(EN), .Q(MemWrite_2), .clk(CLK));  // open: clr
  Register #(.width(1)) register_5 (.D(multiplexer_5_out), .en(EN), .Q(RegDst_2), .clk(CLK));  // open: clr
  Register #(.width(1)) register_6 (.D(multiplexer_6_out), .en(EN), .Q(SRLV_2), .clk(CLK));  // open: clr
  Register #(.width(1)) register_7 (.D(multiplexer_7_out), .en(EN), .Q(SysCALL_2), .clk(CLK));  // open: clr
  Register #(.width(4)) register_8 (.D(multiplexer_8_out), .en(EN), .Q(ALU_OP_2), .clk(CLK));  // open: clr
  Register #(.width(1)) register_9 (.D(multiplexer_9_out), .en(EN), .Q(Reg_Write_2), .clk(CLK));  // open: clr
  Register #(.width(1)) register_10 (.D(multiplexer_10_out), .en(EN), .Q(BGTZ_2), .clk(CLK));  // open: clr
  Register #(.width(2)) register_11 (.D(multiplexer_11_out), .en(EN), .Q(fwd1_2), .clk(CLK));  // open: clr
  Register #(.width(1)) register_12 (.D(multiplexer_12_out), .en(EN), .Q(LBU_2), .clk(CLK));  // open: clr
  Register #(.width(1)) register_13 (.D(multiplexer_13_out), .en(EN), .Q(Pre_2), .clk(CLK));  // open: clr
  Multiplexer #(.width(32), .enable("false")) multiplexer_14 (
    .in0(R1), .in1({32{1'b0}}), .out(multiplexer_14_out), .sel(RST));
  Multiplexer #(.width(32), .enable("false")) multiplexer_15 (
    .in0(R2), .in1({32{1'b0}}), .out(multiplexer_15_out), .sel(RST));
  Multiplexer #(.width(32), .enable("false")) multiplexer_16 (
    .in0(IMM), .in1({32{1'b0}}), .out(multiplexer_16_out), .sel(RST));
  Multiplexer #(.width(32), .enable("false")) multiplexer_17 (
    .in0(IR), .in1({32{1'b0}}), .out(multiplexer_17_out), .sel(RST));
  Multiplexer #(.enable("false")) multiplexer_18 (.in0(BNE), .in1(1'b0), .out(multiplexer_18_out), .sel(RST));
  Multiplexer #(.enable("false")) multiplexer_19 (.in0(BEQ), .in1(1'b0), .out(multiplexer_19_out), .sel(RST));
  Multiplexer #(.width(3), .enable("false")) multiplexer_20 (
    .in0(J), .in1(3'b000), .out(multiplexer_20_out), .sel(RST));
  Multiplexer #(.width(2), .enable("false")) multiplexer_21 (
    .in0(fwd2), .in1(2'b00), .out(multiplexer_21_out), .sel(RST));
  Multiplexer #(.enable("false")) multiplexer_22 (.in0(eq34), .in1(1'b0), .out(multiplexer_22_out), .sel(RST));
  Multiplexer #(.width(32), .enable("false")) multiplexer_23 (
    .in0(simm), .in1({32{1'b0}}), .out(multiplexer_23_out), .sel(RST));
  Register #(.width(32)) register_14 (.D(multiplexer_14_out), .en(EN), .Q(R1_2), .clk(CLK));  // open: clr
  Register #(.width(32)) register_15 (.D(multiplexer_15_out), .en(EN), .Q(R2_2), .clk(CLK));  // open: clr
  Register #(.width(32)) register_16 (.D(multiplexer_16_out), .en(EN), .Q(IMM_2), .clk(CLK));  // open: clr
  Register #(.width(32)) register_17 (.D(multiplexer_17_out), .en(EN), .Q(IR_2), .clk(CLK));  // open: clr
  Register #(.width(1)) register_18 (.D(multiplexer_18_out), .en(EN), .Q(BNE_2), .clk(CLK));  // open: clr
  Register #(.width(1)) register_19 (.D(multiplexer_19_out), .en(EN), .Q(BEQ_2), .clk(CLK));  // open: clr
  Register #(.width(3)) register_20 (.D(multiplexer_20_out), .en(EN), .Q(J_2), .clk(CLK));  // open: clr
  Register #(.width(2)) register_21 (.D(multiplexer_21_out), .en(EN), .Q(fwd2_2), .clk(CLK));  // open: clr
  Register #(.width(1)) register_22 (.D(multiplexer_22_out), .en(EN), .Q(eq34_2), .clk(CLK));  // open: clr
  Register #(.width(32)) register_23 (.D(multiplexer_23_out), .en(EN), .Q(simm_2), .clk(CLK));  // open: clr

  // Other names for the same wires on the sheet: RF_A[31:0] = R1
endmodule

module EX_MEM (
  input  [31:0] nextPC,
  input  Reg_Write,
  input  MemToReg,
  input  [31:0] R2,
  input  MemWrite,
  input  RegDst,
  input  [31:0] ALU,
  input  RST,
  input  CLK,
  input  [31:0] IR,
  input  SysCALL,
  input  BNE,
  input  [2:0] J,
  input  BEQ,
  input  [31:0] R1,
  input  eq34,
  input  BGTZ,
  input  LBU,
  input  EN,
  output [31:0] nextPC_2,
  output Reg_Write_2,
  output MemToReg_2,
  output [31:0] R2_2,
  output MemWrite_2,
  output RegDst_2,
  output [31:0] ALU_2,
  output [31:0] IR_2,
  output SysCALL_2,
  output BNE_2,
  output [2:0] EXJ,
  output BEQ_2,
  output [31:0] R1_2,
  output eq34_2,
  output EXBGTZ,
  output LBU_2
);

  wire multiplexer_2_out, multiplexer_3_out, multiplexer_4_out, multiplexer_5_out, multiplexer_6_out,
       multiplexer_9_out, multiplexer_10_out, multiplexer_14_out, multiplexer_15_out, multiplexer_16_out;
  wire [2:0] multiplexer_7_out;
  wire [31:0] multiplexer_1_out, multiplexer_8_out, multiplexer_11_out, multiplexer_12_out,
       multiplexer_13_out;

  Multiplexer #(.width(32), .enable("false")) multiplexer_1 (
    .in0(nextPC), .in1({32{1'b0}}), .out(multiplexer_1_out), .sel(RST));
  Multiplexer #(.enable("false")) multiplexer_2 (.in0(Reg_Write), .in1(1'b0), .out(multiplexer_2_out), .sel(RST));
  Multiplexer #(.enable("false")) multiplexer_3 (.in0(MemToReg), .in1(1'b0), .out(multiplexer_3_out), .sel(RST));
  Multiplexer #(.enable("false")) multiplexer_4 (.in0(MemWrite), .in1(1'b0), .out(multiplexer_4_out), .sel(RST));
  Multiplexer #(.enable("false")) multiplexer_5 (.in0(RegDst), .in1(1'b0), .out(multiplexer_5_out), .sel(RST));
  Multiplexer #(.enable("false")) multiplexer_6 (.in0(SysCALL), .in1(1'b0), .out(multiplexer_6_out), .sel(RST));
  Multiplexer #(.width(3), .enable("false")) multiplexer_7 (.in0(J), .in1(3'b000), .out(multiplexer_7_out), .sel(RST));
  Multiplexer #(.width(32), .enable("false")) multiplexer_8 (
    .in0(R1), .in1({32{1'b0}}), .out(multiplexer_8_out), .sel(RST));
  Multiplexer #(.enable("false")) multiplexer_9 (.in0(BGTZ), .in1(1'b0), .out(multiplexer_9_out), .sel(RST));
  Multiplexer #(.enable("false")) multiplexer_10 (.in0(LBU), .in1(1'b0), .out(multiplexer_10_out), .sel(RST));
  Register #(.width(32)) register_1 (.D(multiplexer_1_out), .en(EN), .Q(nextPC_2), .clk(CLK));  // open: clr
  Register #(.width(1)) register_2 (.D(multiplexer_2_out), .en(EN), .Q(Reg_Write_2), .clk(CLK));  // open: clr
  Register #(.width(1)) register_3 (.D(multiplexer_3_out), .en(EN), .Q(MemToReg_2), .clk(CLK));  // open: clr
  Register #(.width(1)) register_4 (.D(multiplexer_4_out), .en(EN), .Q(MemWrite_2), .clk(CLK));  // open: clr
  Register #(.width(1)) register_5 (.D(multiplexer_5_out), .en(EN), .Q(RegDst_2), .clk(CLK));  // open: clr
  Register #(.width(1)) register_6 (.D(multiplexer_6_out), .en(EN), .Q(SysCALL_2), .clk(CLK));  // open: clr
  Register #(.width(3)) register_7 (.D(multiplexer_7_out), .en(EN), .Q(EXJ), .clk(CLK));  // open: clr
  Register #(.width(32)) register_8 (.D(multiplexer_8_out), .en(EN), .Q(R1_2), .clk(CLK));  // open: clr
  Register #(.width(1)) register_9 (.D(multiplexer_9_out), .en(EN), .Q(EXBGTZ), .clk(CLK));  // open: clr
  Register #(.width(1)) register_10 (.D(multiplexer_10_out), .en(EN), .Q(LBU_2), .clk(CLK));  // open: clr
  Multiplexer #(.width(32), .enable("false")) multiplexer_11 (
    .in0(R2), .in1({32{1'b0}}), .out(multiplexer_11_out), .sel(RST));
  Multiplexer #(.width(32), .enable("false")) multiplexer_12 (
    .in0(ALU), .in1({32{1'b0}}), .out(multiplexer_12_out), .sel(RST));
  Multiplexer #(.width(32), .enable("false")) multiplexer_13 (
    .in0(IR), .in1({32{1'b0}}), .out(multiplexer_13_out), .sel(RST));
  Multiplexer #(.enable("false")) multiplexer_14 (.in0(BNE), .in1(1'b0), .out(multiplexer_14_out), .sel(RST));
  Multiplexer #(.enable("false")) multiplexer_15 (.in0(BEQ), .in1(1'b0), .out(multiplexer_15_out), .sel(RST));
  Multiplexer #(.enable("false")) multiplexer_16 (.in0(eq34), .in1(1'b0), .out(multiplexer_16_out), .sel(RST));
  Register #(.width(32)) register_11 (.D(multiplexer_11_out), .en(EN), .Q(R2_2), .clk(CLK));  // open: clr
  Register #(.width(32)) register_12 (.D(multiplexer_12_out), .en(EN), .Q(ALU_2), .clk(CLK));  // open: clr
  Register #(.width(32)) register_13 (.D(multiplexer_13_out), .en(EN), .Q(IR_2), .clk(CLK));  // open: clr
  Register #(.width(1)) register_14 (.D(multiplexer_14_out), .en(EN), .Q(BNE_2), .clk(CLK));  // open: clr
  Register #(.width(1)) register_15 (.D(multiplexer_15_out), .en(EN), .Q(BEQ_2), .clk(CLK));  // open: clr
  Register #(.width(1)) register_16 (.D(multiplexer_16_out), .en(EN), .Q(eq34_2), .clk(CLK));  // open: clr
endmodule

module MEM_WB (
  input  [31:0] nextPC,
  input  Reg_Write,
  input  MemToReg,
  input  [31:0] DM,
  input  [31:0] R1,
  input  RegDst,
  input  [31:0] ALU,
  input  RST,
  input  CLK,
  input  [31:0] IR,
  input  SysCALL,
  input  [2:0] EXJ,
  input  [31:0] LedData,
  input  eq34,
  input  LBU,
  input  EN,
  output [31:0] nextPC_2,
  output Reg_Write_2,
  output MemToReg_2,
  output [31:0] DM_2,
  output [31:0] R1_2,
  output RegDst_2,
  output [31:0] ALU_2,
  output [31:0] IR_2,
  output SysCALL_2,
  output [2:0] WBJ,
  output [31:0] LedData_2,
  output eq34_2,
  output WB_LBU
);

  wire multiplexer_2_out, multiplexer_3_out, multiplexer_5_out, multiplexer_6_out, multiplexer_8_out,
       multiplexer_9_out;
  wire [2:0] multiplexer_7_out;
  wire [31:0] multiplexer_1_out, multiplexer_4_out, multiplexer_10_out, multiplexer_11_out,
       multiplexer_12_out, multiplexer_13_out;

  Multiplexer #(.width(32), .enable("false")) multiplexer_1 (
    .in0(nextPC), .in1({32{1'b0}}), .out(multiplexer_1_out), .sel(RST));
  Multiplexer #(.enable("false")) multiplexer_2 (.in0(Reg_Write), .in1(1'b0), .out(multiplexer_2_out), .sel(RST));
  Multiplexer #(.enable("false")) multiplexer_3 (.in0(MemToReg), .in1(1'b0), .out(multiplexer_3_out), .sel(RST));
  Multiplexer #(.width(32), .enable("false")) multiplexer_4 (
    .in0(R1), .in1({32{1'b0}}), .out(multiplexer_4_out), .sel(RST));
  Multiplexer #(.enable("false")) multiplexer_5 (.in0(RegDst), .in1(1'b0), .out(multiplexer_5_out), .sel(RST));
  Multiplexer #(.enable("false")) multiplexer_6 (.in0(SysCALL), .in1(1'b0), .out(multiplexer_6_out), .sel(RST));
  Multiplexer #(.width(3), .enable("false")) multiplexer_7 (
    .in0(EXJ), .in1(3'b000), .out(multiplexer_7_out), .sel(RST));
  Multiplexer #(.enable("false")) multiplexer_8 (.in0(eq34), .in1(1'b0), .out(multiplexer_8_out), .sel(RST));
  Multiplexer #(.enable("false")) multiplexer_9 (.in0(LBU), .in1(1'b0), .out(multiplexer_9_out), .sel(RST));
  Register #(.width(32)) register_1 (.D(multiplexer_1_out), .en(EN), .Q(nextPC_2), .clk(CLK));  // open: clr
  Register #(.width(1)) register_2 (.D(multiplexer_2_out), .en(EN), .Q(Reg_Write_2), .clk(CLK));  // open: clr
  Register #(.width(1)) register_3 (.D(multiplexer_3_out), .en(EN), .Q(MemToReg_2), .clk(CLK));  // open: clr
  Register #(.width(32)) register_4 (.D(multiplexer_4_out), .en(EN), .Q(R1_2), .clk(CLK));  // open: clr
  Register #(.width(1)) register_5 (.D(multiplexer_5_out), .en(EN), .Q(RegDst_2), .clk(CLK));  // open: clr
  Register #(.width(1)) register_6 (.D(multiplexer_6_out), .en(EN), .Q(SysCALL_2), .clk(CLK));  // open: clr
  Register #(.width(3)) register_7 (.D(multiplexer_7_out), .en(EN), .Q(WBJ), .clk(CLK));  // open: clr
  Register #(.width(1)) register_8 (.D(multiplexer_8_out), .en(EN), .Q(eq34_2), .clk(CLK));  // open: clr
  Register #(.width(1)) register_9 (.D(multiplexer_9_out), .en(EN), .Q(WB_LBU), .clk(CLK));  // open: clr
  Multiplexer #(.width(32), .enable("false")) multiplexer_10 (
    .in0(DM), .in1({32{1'b0}}), .out(multiplexer_10_out), .sel(RST));
  Multiplexer #(.width(32), .enable("false")) multiplexer_11 (
    .in0(ALU), .in1({32{1'b0}}), .out(multiplexer_11_out), .sel(RST));
  Multiplexer #(.width(32), .enable("false")) multiplexer_12 (
    .in0(IR), .in1({32{1'b0}}), .out(multiplexer_12_out), .sel(RST));
  Multiplexer #(.width(32), .enable("false")) multiplexer_13 (
    .in0(LedData), .in1({32{1'b0}}), .out(multiplexer_13_out), .sel(RST));
  Register #(.width(32)) register_10 (.D(multiplexer_10_out), .en(EN), .Q(DM_2), .clk(CLK));  // open: clr
  Register #(.width(32)) register_11 (.D(multiplexer_11_out), .en(EN), .Q(ALU_2), .clk(CLK));  // open: clr
  Register #(.width(32)) register_12 (.D(multiplexer_12_out), .en(EN), .Q(IR_2), .clk(CLK));  // open: clr
  Register #(.width(32)) register_13 (.D(multiplexer_13_out), .en(EN), .Q(LedData_2), .clk(CLK));  // open: clr
endmodule

module \分支相关流水线  (
  output out_1,
  output out_2
);

  wire and_1_out, and_2_out, and_3_out, and_4_out, BGTZ, branch, CLK, EN, eq34, ex_mem_1_p19, ex_mem_1_p20,
       ex_mem_1_p21, ex_mem_1_p22, ex_mem_1_p23, ex_mem_1_p24, ex_mem_1_p25, ex_mem_1_p26, ex_mem_1_p27,
       ex_mem_1_p28, ex_mem_1_p29, ex_mem_1_p31, EXBEQ, EXBGTZ, EXBNE, EXEQ, EXles, Go, id_ex_1_alu_src_2,
       id_ex_1_memtoreg_2, id_ex_1_memwrite_2, id_ex_1_reg_write_2, id_ex_1_regdst_2, id_ex_1_syscall_2, IR1,
       IR2, IR3, mem_wb_1_p17, mem_wb_1_p19, mips_ram_1_p10, not_1_out, or_2_out, or_3_out,
       registerfile_1_p7, registerfile_1_p8, RST, SignedExt, TEN, W1, W2, W3, \硬布线控制器_1_alu_src ,
       \硬布线控制器_1_beq , \硬布线控制器_1_bne , \硬布线控制器_1_memtoreg , \硬布线控制器_1_memwrite , \硬布线控制器_1_regdst ,
       \硬布线控制器_1_regwrite , \硬布线控制器_1_syscall ;
  wire [2:0] EXJ, J, WBJ;
  wire [3:0] id_ex_1_alu_op_2, \硬布线控制器_1_alu_op ;
  wire [4:0] multiplexer_7_out, RW1, RW2, RW3;
  wire [15:0] \LoadUse次数 , \总周期数 , \插入气泡数 , \无条件分支数 , \条件分支成功数 ;
  wire [27:0] Jaddr;
  wire [31:0] adder_1_out, bit_extender_1_out, bit_extender_2_out, branchPC, din, ex_mem_1_p30, EX_PC,
       EXnextPC, id_ex_1_imm_2, id_ex_1_ir_2, ID_PC, IF_PC, Ins, LedData, MEM_PC, mem_wb_1_p15, mem_wb_1_p22,
       mem_wb_1_p23, mips_probe_1_p1, mips_regifile_1_r1, mips_regifile_1_r2, multiplexer_1_out,
       multiplexer_2_out, multiplexer_3_out, multiplexer_8_out, multiplexer_9_out, multiplexer_10_out, R1,
       R2, rom_2_data, rom_3_data, shifter_1_out, WB_PC, WBnextPC;
  wire [31:1] mips_alu_1_result;

  Button \u_总复位  (.out(RST));
  Button _1 (.out(IR1));
  Button _2 (.out(IR2));
  Button _3 (.out(IR3));
  Multiplexer #(.width(32), .disabled(0), .enable("false")) multiplexer_1 (
    .in0(adder_1_out), .in1(branchPC), .out(multiplexer_1_out), .sel(branch));
  or or_1 (EN, out_1, not_1_out);
  not not_1 (not_1_out, out_2);
  Button \u_继续运行  (.out(Go));
  LED led_1 (.in(W1));
  LED led_2 (.in(W2));
  LED led_3 (.in(W3));
  Register #(.width(32)) register_1 (.D(R2), .en(eq34), .Q(LedData), .clk(CLK));  // open: clr
  Multiplexer #(.width(32), .disabled(0), .enable("false")) multiplexer_2 (
    .in0(multiplexer_1_out), .in1({EXnextPC[31:28], Jaddr}), .out(multiplexer_2_out), .sel(EXJ[0]));
  Multiplexer #(.width(32), .disabled(0), .enable("false")) multiplexer_3 (
    .in0(multiplexer_2_out), .in1(R1), .out(multiplexer_3_out), .sel(EXJ[1]));
  // Probe on IF_PC
  Hex_Digit_Display hex_digit_display_1 (.value(LedData[31:28]));  // open: dp
  Hex_Digit_Display hex_digit_display_2 (.value(LedData[27:24]));  // open: dp
  Register #(.width(32)) PC (.D(multiplexer_3_out), .en(EN), .Q(IF_PC), .clk(CLK), .clr(RST));
  // Probe on ID_PC
  // Probe on Ins
  Hex_Digit_Display hex_digit_display_3 (.value(LedData[23:20]));  // open: dp
  Hex_Digit_Display hex_digit_display_4 (.value(LedData[19:16]));  // open: dp
  // Probe on EX_PC
  // Probe on WB_PC
  Hex_Digit_Display hex_digit_display_5 (.value(LedData[15:12]));  // open: dp
  Hex_Digit_Display hex_digit_display_6 (.value(LedData[11:8]));  // open: dp
  Adder #(.width(32)) adder_1 (.a(IF_PC), .b(32'h4), .out(adder_1_out), .cin(1'b0));  // open: cout
  // Mips_Probe mips_probe_1: pin names not known; wires that end beside it: mips_probe_1_p1
  // Probe on MEM_PC
  Hex_Digit_Display hex_digit_display_7 (.value(LedData[3:0]));  // open: dp
  Hex_Digit_Display hex_digit_display_8 (.value(LedData[7:4]));  // open: dp
  Clock clock_1 (.out(CLK));
  ROM #(.addrWidth(10), .dataWidth(32)) rom_1 (.addr(IF_PC[11:2]), .data(mips_probe_1_p1));  // open: sel
  or or_2 (or_2_out, EXJ[0], branch);
  IF_ID if_id_1 (
    .nextPC(IF_PC), .Instr(mips_probe_1_p1), .RST(or_2_out), .CLK(CLK), .EN(EN), .nextPC_2(ID_PC),
    .Instr_2(Ins));  // open: pre, pre_2
  ROM #(.addrWidth(10), .dataWidth(32)) rom_2 (.addr(WB_PC[11:2]), .data(rom_2_data));  // open: sel
  ROM #(.addrWidth(10), .dataWidth(32)) rom_3 (.addr(ID_PC[11:2]), .data(rom_3_data));  // open: sel
  // Probe on Ins[31:26]
  // Probe on \总周期数 
  // Probe on \无条件分支数 
  // Probe on \条件分支成功数 
  // Probe on \插入气泡数 
  // Probe on \LoadUse次数 
  // Probe on mem_wb_1_p15[20:16]
  assign bit_extender_1_out = {{16{Ins[15]}}, Ins[15:0]};  // Bit_Extender bit_extender_1
  // Probe on IF_PC[11:0]
  \硬布线控制器  \u_硬布线控制器_1  (
    .Func(Ins[5:0]), .OP(Ins[31:26]), .ALU_OP(\硬布线控制器_1_alu_op ), .MemToReg(\硬布线控制器_1_memtoreg ),
    .MemWrite(\硬布线控制器_1_memwrite ), .ALU_SRC(\硬布线控制器_1_alu_src ), .RegWrite(\硬布线控制器_1_regwrite ),
    .SysCALL(\硬布线控制器_1_syscall ), .SignedExt(SignedExt), .RegDst(\硬布线控制器_1_regdst ), .JR(J[1]), .JMP(J[0]),
    .Beq(\硬布线控制器_1_beq ), .JAL(J[2]), .Bne(\硬布线控制器_1_bne ), .BGTZ(BGTZ));  // open: SRLV, LBU
  Multiplexer #(.width(5), .disabled(0), .enable("false")) multiplexer_4 (
    .in0(Ins[25:21]), .in1(5'b00010), .out(RW1), .sel(\硬布线控制器_1_syscall ));
  Multiplexer #(.width(5), .disabled(0), .enable("false")) multiplexer_5 (
    .in0(Ins[20:16]), .in1(5'b00100), .out(RW2), .sel(\硬布线控制器_1_syscall ));
  // Probe on RW2
  Multiplexer #(.width(5), .disabled(0), .enable("false")) multiplexer_6 (
    .in0(mem_wb_1_p15[20:16]), .in1(mem_wb_1_p15[15:11]), .out(RW3), .sel(mem_wb_1_p19));
  assign bit_extender_2_out = {{16{1'b0}}, Ins[15:0]};  // Bit_Extender bit_extender_2
  // Probe on EX_PC[11:0]
  // Probe on ID_PC[11:0]
  // Probe on RW1
  Multiplexer #(.width(5), .disabled(0), .enable("false")) multiplexer_7 (
    .in0(RW3), .in1({5{1'b1}}), .out(multiplexer_7_out), .sel(WBJ[2]));
  Multiplexer #(.width(32), .disabled(0), .enable("false")) multiplexer_8 (
    .in0(bit_extender_2_out), .in1(bit_extender_1_out), .out(multiplexer_8_out), .sel(SignedExt));
  // RegisterFile registerfile_1: pin names not known; wires that end beside it: din, CLK, TEN, RW3, RW1, RW2, registerfile_1_p7, registerfile_1_p8
  // Probe on MEM_PC[11:0]
  // Probe on multiplexer_9_out
  Multiplexer #(.width(32), .disabled(0), .enable("false")) multiplexer_9 (
    .in0(din), .in1(WBnextPC), .out(multiplexer_9_out), .sel(WBJ[2]));
  // Probe on registerfile_1_p7
  // Probe on registerfile_1_p8
  // Probe on RW1
  // Probe on RW2
  // Probe on RW3
  // Probe on WB_PC[11:0]
  MIPS_Regifile mips_regifile_1 (
    .Din(multiplexer_9_out), .Clk(CLK), .R1(mips_regifile_1_r1), .R2(mips_regifile_1_r2), .WE(TEN),
    .W_num(multiplexer_7_out), .R1_num(RW1), .R2_num(RW2));
  // Probe on mips_regifile_1_r1
  // Probe on mips_regifile_1_r2
  // Probe on multiplexer_8_out
  // Probe on din
  or or_3 (or_3_out, EXJ[0], branch);
  Counter #(.width(16), .max('hffff)) counter_1 (.count(EN), .Q(\总周期数 ), .clk(CLK), .clr(RST));  // open: load, D, carry
  ID_EX id_ex_1 (
    .nextPC(ID_PC), .ALU_SRC(\硬布线控制器_1_alu_src ), .R1(mips_regifile_1_r1), .MemToReg(\硬布线控制器_1_memtoreg ),
    .R2(mips_regifile_1_r2), .MemWrite(\硬布线控制器_1_memwrite ), .IMM(multiplexer_8_out),
    .SysCALL(\硬布线控制器_1_syscall ), .ALU_OP(\硬布线控制器_1_alu_op ), .nextPC_2(EX_PC),
    .ALU_SRC_2(id_ex_1_alu_src_2), .R1_2(R1), .MemToReg_2(id_ex_1_memtoreg_2), .R2_2(R2),
    .MemWrite_2(id_ex_1_memwrite_2), .IMM_2(id_ex_1_imm_2), .SysCALL_2(id_ex_1_syscall_2),
    .ALU_OP_2(id_ex_1_alu_op_2), .EN(EN), .IR(Ins), .IR_2(id_ex_1_ir_2), .RST(or_3_out), .CLK(CLK),
    .RegDst(\硬布线控制器_1_regdst ), .RegDst_2(id_ex_1_regdst_2), .Reg_Write(\硬布线控制器_1_regwrite ),
    .Reg_Write_2(id_ex_1_reg_write_2), .BNE(\硬布线控制器_1_bne ), .BNE_2(EXBNE), .BEQ(\硬布线控制器_1_beq ),
    .BEQ_2(EXBEQ), .J(J), .J_2(EXJ), .BGTZ(BGTZ), .BGTZ_2(EXBGTZ));  // open: fwd1, fwd1_2, fwd2, fwd2_2, eq34, eq34_2, SRLV, SRLV_2, LBU, LBU_2, Pre, Pre_2, simm, simm_2
  // Probe on id_ex_1_imm_2
  Adder #(.width(32)) adder_2 (.a(EX_PC), .b(32'h4), .out(EXnextPC), .cin(1'b0));  // open: cout
  Shifter #(.width(32)) shifter_1 (.in(id_ex_1_imm_2), .\dist (5'b00010), .out(shifter_1_out));
  Comparator #(.width(32)) comparator_1 (.a(32'h22), .b(R1), .eq(eq34));  // open: gt, lt
  Multiplexer #(.width(32), .disabled(0), .enable("false")) multiplexer_10 (
    .in0(R2), .in1(id_ex_1_imm_2), .out(multiplexer_10_out), .sel(id_ex_1_alu_src_2));
  Adder #(.width(32)) adder_3 (.a(shifter_1_out), .b(EXnextPC), .out(branchPC));  // open: cin, cout
  Shifter #(.width(28)) shifter_2 (.in({2'b00, id_ex_1_imm_2[25:0]}), .\dist (5'b00010), .out(Jaddr));
  Counter #(.width(16), .max('hffff)) counter_2 (
    .count(EXJ[0]), .Q(\无条件分支数 ), .clk(CLK), .clr(RST));  // open: load, D, carry
  MIPS_ALU mips_alu_1 (
    .X(R1), .Y(multiplexer_10_out), .AluOP(id_ex_1_alu_op_2), .Equal(EXEQ),
    .Result({mips_alu_1_result, EXles}), .shamt(id_ex_1_ir_2[10:6]));  // open: Result_2
  // Probe on {mips_alu_1_result, EXles}
  // EX_MEM ex_mem_1: pin names not known; wires that end beside it: EX_PC, id_ex_1_ir_2, EXBEQ, EXJ, EXBNE, id_ex_1_memtoreg_2, EXBGTZ, id_ex_1_memwrite_2, id_ex_1_reg_write_2, id_ex_1_regdst_2, id_ex_1_syscall_2, eq34, {mips_alu_1_result, EXles}, R2, CLK, EN, RST, MEM_PC, ex_mem_1_p19, ex_mem_1_p20, ex_mem_1_p21, ex_mem_1_p22, ex_mem_1_p23, ex_mem_1_p24, ex_mem_1_p25, ex_mem_1_p26, ex_mem_1_p27, ex_mem_1_p28, ex_mem_1_p29, ex_mem_1_p30, ex_mem_1_p31
  and and_1 (and_1_out, ~EXEQ, ~EXles);  // AND_Gate
  // Probe on ex_mem_1_p31
  and and_2 (and_2_out, EXBGTZ, and_1_out);
  and and_3 (and_3_out, EXEQ, EXBEQ);
  and and_4 (and_4_out, ~EXEQ, EXBNE);  // AND_Gate
  // MIPS_RAM mips_ram_1: pin names not known; wires that end beside it: ex_mem_1_p20, ex_mem_1_p30[21:2], ex_mem_1_p31, ex_mem_1_p24, ex_mem_1_p22, ex_mem_1_p25, CLK, ex_mem_1_p23, RST, mips_ram_1_p10
  or or_4 (branch, and_3_out, and_2_out, and_4_out);
  // MEM_WB mem_wb_1: pin names not known; wires that end beside it: MEM_PC, ex_mem_1_p19, ex_mem_1_p21, ex_mem_1_p23, ex_mem_1_p26, ex_mem_1_p27, ex_mem_1_p28, ex_mem_1_p29, ex_mem_1_p30, mips_ram_1_p10, CLK, EN, RST, WB_PC, mem_wb_1_p15, WBJ, mem_wb_1_p17, TEN, mem_wb_1_p19, out_2, out_1, mem_wb_1_p22, mem_wb_1_p23
  Counter #(.width(16), .max('hffff)) counter_3 (
    .count(branch), .Q(\条件分支成功数 ), .clk(CLK), .clr(RST));  // open: load, D, carry
  Multiplexer #(.width(32), .disabled(0), .enable("false")) multiplexer_11 (
    .in0(mem_wb_1_p22), .in1(mem_wb_1_p23), .out(din), .sel(mem_wb_1_p17));
  // Probe on din
  Adder #(.width(32)) adder_4 (.a(WB_PC), .b(32'h4), .out(WBnextPC), .cin(1'b0));  // open: cout

  // Other names for the same wires on the sheet: EXJMP = EXJ[0]; EXJR = EXJ[1]; EXJAL = EXJ[2]; JMP = J[0]; JR = J[1];
  //   JAL = J[2]; Jaddr[31:28] = EXnextPC[31:28]; WBJMP = WBJ[0]; WBJR = WBJ[1]; WBJAL = WBJ[2]

  // Notes on the sheet:
  //   中断源
  //   中断等待指示
  //   数码管输出
  //   指令存储器
  //   contents of rom_1 (hex, n*v repeats v):
  //   20110001 8000c05 20110001 20120002 20130003 8000c09 20110001 20120002 20130003 8000c0d 20110001
  //   20120002 20130003 8000c11 20110001 20120002 20130003 c000cb8 20100001 20110001 118fc0 112020
  //   20020022 c 118882 12200001 8000c15 112020 20020022 c 20110001 118880 112020 20020022 c 12200001
  //   8000c1f 20110001 118fc0 112020 20020022 c 1188c3 112020 20020022 c 118903 112020 20020022 c 118903
  //   112020 20020022 c 118903 112020 20020022 c 118903 112020 20020022 c 118903 112020 20020022 c 118903
  //   112020 20020022 c 118903 112020 20020022 c 20100001 109fc0 139fc3 8021 2012000c 24160003 26100001
  //   3210000f 20080008 20090001 139900 2709825 132020 20020022 c 1094022 1500fff9 22100001 2018000f
  //   2188024 108700 20080008 20090001 139902 2709825 132021 20020022 c 1094022 1500fff9 108702 2c9b022
  //   12c00001 8000c50 4020 1084027 84400 3508ffff 82021 20020022 c 2010ffff 20110000 ae300000 22100001
  //   22310004 ae300000 22100001 22310004 ae300000 22100001 22310004 ae300000 22100001 22310004 ae300000
  //   22100001 22310004 ae300000 22100001 22310004 ae300000 22100001 22310004 ae300000 22100001 22310004
  //   ae300000 22100001 22310004 ae300000 22100001 22310004 ae300000 22100001 22310004 ae300000 22100001
  //   22310004 ae300000 22100001 22310004 ae300000 22100001 22310004 ae300000 22100001 22310004 ae300000
  //   22100001 22310004 22100001 8020 2011003c 8e130000 8e340000 274402a 11000002 ae330000 ae140000
  //   2231fffc 1611fff8 102020 20020022 c 22100004 2011003c 1611fff2 20020032 c 20100000 22100001 102020
  //   20020022 c 22100002 102020 20020022 c 22100003 102020 20020022 c 22100004 102020 20020022 c 22100005
  //   102020 20020022 c 22100006 102020 20020022 c 22100007 102020 20020022 c 22100008 102020 20020022
  //   20020022 c 3e00008
  //   contents of rom_2 (hex, n*v repeats v):
  //   20110020 20020022 8000c06 20110004 20120005 20130006 10000003 20110007 20120008 20130009 14110003
  //   2011000a 2012000b 2013000c c000c14 2002000a 0 0 0 c 2231ffff 0 0 0 112020 0 0 0 c 1620fff6 3e00008
  //   contents of rom_3 (hex, n*v repeats v):
  //   20110020 20020022 8000c06 20110004 20120005 20130006 10000003 20110007 20120008 20130009 14110003
  //   2011000a 2012000b 2013000c c000c14 2002000a 0 0 0 c 2231ffff 0 0 0 112020 0 0 0 c 1620fff6 3e00008
  //   rs
  //   rt
  //   rd
  //   OP
  //   Func
  //   MemToReg
  //   MemWrite
  //   AluOP
  //   AluSrcB
  //   RegWrite
  //   RegDst
  //   Syscall
  //   流水调试日志用
endmodule

module \重定向流水线  (
  output out_1,
  output out_2
);

  wire and_1_out, and_2_out, and_3_out, and_4_out, and_5_out, and_6_out, BGTZ, branch, CLK, comparator_1_eq,
       Drelate, EN, EX_Mem2Reg, ex_mem_1_beq_2, ex_mem_1_bne_2, ex_mem_1_eq34_2, ex_mem_1_exbgtz,
       ex_mem_1_lbu_2, ex_mem_1_memwrite_2, ex_mem_1_syscall_2, EX_RegWrite, EX_SRLV, EXBEQ, EXBGTZ, EXBNE,
       EXDst, EXEQ, EXles, Go, id_ex_1_alu_src_2, id_ex_1_lbu_2, id_ex_1_memwrite_2, id_ex_1_syscall_2, IR1,
       IR2, IR3, LBU, loaduse, MEM_Mem2Reg, Mem_RegWrite, mem_wb_1_memtoreg_2, mem_wb_1_regdst_2, MemDst,
       not_1_out, or_2_out, or_3_out, or_4_out, registerfile_1_p7, registerfile_1_p8, RST, SignedExt, SRLV,
       TEN, W1, W2, W3, WB_LBU, \硬布线控制器_1_alu_src , \硬布线控制器_1_beq , \硬布线控制器_1_bne , \硬布线控制器_1_memtoreg ,
       \硬布线控制器_1_memwrite , \硬布线控制器_1_regdst , \硬布线控制器_1_regwrite , \硬布线控制器_1_syscall ;
  wire [1:0] Fwd1, Fwd2, id_ex_1_fwd1_2, id_ex_1_fwd2_2;
  wire [2:0] EXJ, J, MemJ, WBJ;
  wire [3:0] id_ex_1_alu_op_2, \硬布线控制器_1_alu_op ;
  wire [4:0] multiplexer_6_out, multiplexer_11_out, multiplexer_12_out, multiplexer_13_out,
       multiplexer_14_out, multiplexer_15_out, multiplexer_16_out, multiplexer_17_out, multiplexer_18_out,
       multiplexer_22_out, RW1, RW2, RW3;
  wire [5:0] Func;
  wire [7:0] ByteEx, multiplexer_23_out, multiplexer_23_out_2, multiplexer_23_out_3, multiplexer_23_out_4;
  wire [15:0] \LoadUse次数 , \总周期数 , \插入气泡数 , \无条件分支数 , \条件分支成功数 ;
  wire [27:2] Jaddr;
  wire [31:0] adder_1_out, bit_extender_1_out, bit_extender_2_out, branchPC, din, ex_mem_1_alu_2,
       ex_mem_1_r1_2, ex_mem_1_r2_2, EX_PC, EXI, EXnextPC, id_ex_1_r1_2, id_ex_1_r2_2, ID_PC, IF_PC, LedData,
       MEM_PC, mem_wb_1_alu_2, mem_wb_1_dm_2, mem_wb_1_ir_2, mem_wb_1_leddata_2, MemI, mips_probe_1_p1,
       mips_ram_1_p10, mips_regifile_1_r1, mips_regifile_1_r2, multiplexer_1_out, multiplexer_2_out,
       multiplexer_3_out, multiplexer_8_out, multiplexer_10_out, multiplexer_20_out, multiplexer_24_out, R1,
       R2, rom_2_data, rom_3_data, shifter_1_out, WB_PC, WBnextPC;
  wire [31:1] mips_alu_1_result;
  wire [31:6] Ins;
  wire [31:26] id_ex_1_imm_2;

  // Probe on multiplexer_3_out
  Button \u_总复位  (.out(RST));
  Button _1 (.out(IR1));
  Button _2 (.out(IR2));
  Button _3 (.out(IR3));
  Multiplexer #(.width(32), .disabled(0), .enable("false")) multiplexer_1 (
    .in0(adder_1_out), .in1(branchPC), .out(multiplexer_1_out), .sel(branch));
  or or_1 (EN, out_1, Go, not_1_out);
  not not_1 (not_1_out, out_2);
  Button \u_继续运行  (.out(Go));
  LED led_1 (.in(W1));
  LED led_2 (.in(W2));
  LED led_3 (.in(W3));
  Multiplexer #(.width(32), .disabled(0), .enable("false")) multiplexer_2 (
    .in0(multiplexer_1_out), .in1({EX_PC[31:28], Jaddr, 2'b00}), .out(multiplexer_2_out), .sel(EXJ[0]));
  Multiplexer #(.width(32), .disabled(0), .enable("false")) multiplexer_3 (
    .in0(multiplexer_2_out), .in1(R1), .out(multiplexer_3_out), .sel(EXJ[1]));
  and and_1 (and_1_out, EN, ~loaduse);  // AND_Gate
  Hex_Digit_Display hex_digit_display_1 (.value(LedData[31:28]));  // open: dp
  Hex_Digit_Display hex_digit_display_2 (.value(LedData[27:24]));  // open: dp
  Register #(.width(32)) PC (.D(multiplexer_3_out), .en(and_1_out), .Q(IF_PC), .clk(CLK), .clr(RST));
  Hex_Digit_Display hex_digit_display_3 (.value(LedData[19:16]));  // open: dp
  Hex_Digit_Display hex_digit_display_4 (.value(LedData[23:20]));  // open: dp
  Hex_Digit_Display hex_digit_display_5 (.value(LedData[11:8]));  // open: dp
  Hex_Digit_Display hex_digit_display_6 (.value(LedData[15:12]));  // open: dp
  Adder #(.width(32)) adder_1 (.a(IF_PC), .b(32'h4), .out(adder_1_out), .cin(1'b0));  // open: cout
  // Mips_Probe mips_probe_1: pin names not known; wires that end beside it: mips_probe_1_p1
  Hex_Digit_Display hex_digit_display_7 (.value(LedData[3:0]));  // open: dp
  Hex_Digit_Display hex_digit_display_8 (.value(LedData[7:4]));  // open: dp
  Clock clock_1 (.out(CLK));
  or or_2 (or_2_out, EXJ[0], 1'b0, branch);
  ROM #(.addrWidth(10), .dataWidth(32)) rom_1 (.addr(IF_PC[11:2]), .data(mips_probe_1_p1));  // open: sel
  or or_3 (or_3_out, EXJ[0], branch);
  and and_2 (and_2_out, EN, ~loaduse);  // AND_Gate
  Counter #(.width(16), .max('hffff)) counter_1 (
    .count(or_2_out), .Q(\插入气泡数 ), .clk(CLK), .clr(RST));  // open: load, D, carry
  IF_ID if_id_1 (
    .nextPC(IF_PC), .Instr(mips_probe_1_p1), .RST(or_3_out), .CLK(CLK), .EN(and_2_out), .nextPC_2(ID_PC),
    .Instr_2({Ins, Func}));  // open: pre, pre_2
  ROM #(.addrWidth(10), .dataWidth(32)) rom_2 (.addr(WB_PC[11:2]), .data(rom_2_data));  // open: sel
  ROM #(.addrWidth(10), .dataWidth(32)) rom_3 (.addr(ID_PC[11:2]), .data(rom_3_data));  // open: sel
  // Probe on \总周期数 
  // Probe on \无条件分支数 
  // Probe on \条件分支成功数 
  // Probe on \插入气泡数 
  // Probe on \LoadUse次数 
  // Probe on mem_wb_1_ir_2[20:16]
  assign bit_extender_1_out = {{16{Ins[15]}}, {Ins[15:6], Func}};  // Bit_Extender bit_extender_1
  // Probe on IF_PC[11:0]
  \硬布线控制器  \u_硬布线控制器_1  (
    .Func(Func), .OP(Ins[31:26]), .ALU_OP(\硬布线控制器_1_alu_op ), .MemToReg(\硬布线控制器_1_memtoreg ),
    .MemWrite(\硬布线控制器_1_memwrite ), .ALU_SRC(\硬布线控制器_1_alu_src ), .RegWrite(\硬布线控制器_1_regwrite ),
    .SysCALL(\硬布线控制器_1_syscall ), .SignedExt(SignedExt), .RegDst(\硬布线控制器_1_regdst ), .JR(J[1]), .JMP(J[0]),
    .Beq(\硬布线控制器_1_beq ), .JAL(J[2]), .Bne(\硬布线控制器_1_bne ), .SRLV(SRLV), .LBU(LBU), .BGTZ(BGTZ));
  Multiplexer #(.width(5), .disabled(0), .enable("false")) multiplexer_4 (
    .in0(Ins[25:21]), .in1(5'b00010), .out(RW1), .sel(\硬布线控制器_1_syscall ));
  Multiplexer #(.width(5), .disabled(0), .enable("false")) multiplexer_5 (
    .in0(Ins[20:16]), .in1(5'b00100), .out(RW2), .sel(\硬布线控制器_1_syscall ));
  // Probe on RW2
  Multiplexer #(.width(5), .disabled(0), .enable("false")) multiplexer_6 (
    .in0(mem_wb_1_ir_2[20:16]), .in1(mem_wb_1_ir_2[15:11]), .out(multiplexer_6_out), .sel(mem_wb_1_regdst_2));
  assign bit_extender_2_out = {{16{1'b0}}, {Ins[15:6], Func}};  // Bit_Extender bit_extender_2
  // Probe on ID_PC[11:0]
  // Probe on EX_PC[11:0]
  Multiplexer #(.width(5), .disabled(0), .enable("false")) multiplexer_7 (
    .in0(multiplexer_6_out), .in1({5{1'b1}}), .out(RW3), .sel(WBJ[2]));
  Multiplexer #(.width(32), .disabled(0), .enable("false")) multiplexer_8 (
    .in0(bit_extender_2_out), .in1(bit_extender_1_out), .out(multiplexer_8_out), .sel(SignedExt));
  // RegisterFile registerfile_1: pin names not known; wires that end beside it: din, CLK, TEN, RW3, RW1, RW2, registerfile_1_p7, registerfile_1_p8, EXI[15:11]
  // Probe on MEM_PC[11:0]
  // Probe on din
  Multiplexer #(.width(32), .disabled(0), .enable("false")) multiplexer_9 (
    .in0(multiplexer_10_out), .in1({{24{1'b0}}, ByteEx}), .out(din), .sel(WB_LBU));
  Multiplexer #(.width(32), .disabled(0), .enable("false")) multiplexer_10 (
    .in0({multiplexer_23_out_4, multiplexer_23_out_3, multiplexer_23_out_2, multiplexer_23_out}),
    .in1(WBnextPC), .out(multiplexer_10_out), .sel(WBJ[2]));
  // Probe on registerfile_1_p7
  // Probe on registerfile_1_p8
  // Probe on RW1
  // Probe on RW2
  // Probe on RW3
  // Probe on WB_PC[11:0]
  MIPS_Regifile mips_regifile_1 (
    .Din(din), .Clk(CLK), .R1(mips_regifile_1_r1), .R2(mips_regifile_1_r2), .WE(TEN), .W_num(RW3),
    .R1_num(RW1), .R2_num(RW2));
  // Probe on EXI[15:11]
  // Probe on MemI
  // Probe on mips_regifile_1_r2
  // Probe on multiplexer_8_out
  // Probe on din
  // Probe on MemI
  or or_4 (or_4_out, EXJ[0], loaduse, branch);
  Multiplexer #(.width(5), .disabled(0), .enable("false")) multiplexer_11 (
    .in0(EXI[20:16]), .in1(EXI[15:11]), .out(multiplexer_11_out), .sel(EXDst));
  Multiplexer #(.width(5), .disabled(0), .enable("false")) multiplexer_12 (
    .in0(multiplexer_11_out), .in1({5{1'b1}}), .out(multiplexer_12_out), .sel(EXJ[2]));
  Multiplexer #(.width(5), .disabled(0), .enable("false")) multiplexer_13 (
    .in0(MemI[20:16]), .in1(MemI[15:11]), .out(multiplexer_13_out), .sel(MemDst));
  // Probe on multiplexer_17_out
  Counter #(.width(16), .max('hffff)) counter_2 (.count(EN), .Q(\总周期数 ), .clk(CLK), .clr(RST));  // open: load, D, carry
  Counter #(.width(16), .max('hffff)) counter_3 (
    .count(loaduse), .Q(\LoadUse次数 ), .clk(CLK), .clr(RST));  // open: load, D, carry
  ID_EX id_ex_1 (
    .nextPC(ID_PC), .ALU_SRC(\硬布线控制器_1_alu_src ), .R1(mips_regifile_1_r1), .MemToReg(\硬布线控制器_1_memtoreg ),
    .R2(mips_regifile_1_r2), .MemWrite(\硬布线控制器_1_memwrite ), .IMM(multiplexer_8_out),
    .SysCALL(\硬布线控制器_1_syscall ), .ALU_OP(\硬布线控制器_1_alu_op ), .nextPC_2(EX_PC),
    .ALU_SRC_2(id_ex_1_alu_src_2), .R1_2(id_ex_1_r1_2), .MemToReg_2(EX_Mem2Reg), .R2_2(id_ex_1_r2_2),
    .MemWrite_2(id_ex_1_memwrite_2), .IMM_2({id_ex_1_imm_2, Jaddr}), .SysCALL_2(id_ex_1_syscall_2),
    .ALU_OP_2(id_ex_1_alu_op_2), .EN(EN), .IR({Ins, Func}), .IR_2(EXI), .RST(or_4_out), .CLK(CLK),
    .RegDst(\硬布线控制器_1_regdst ), .RegDst_2(EXDst), .Reg_Write(\硬布线控制器_1_regwrite ), .Reg_Write_2(EX_RegWrite),
    .BNE(\硬布线控制器_1_bne ), .BNE_2(EXBNE), .BEQ(\硬布线控制器_1_beq ), .BEQ_2(EXBEQ), .J(J), .J_2(EXJ), .BGTZ(BGTZ),
    .BGTZ_2(EXBGTZ), .fwd1(Fwd1), .fwd1_2(id_ex_1_fwd1_2), .fwd2(Fwd2), .fwd2_2(id_ex_1_fwd2_2), .SRLV(SRLV),
    .SRLV_2(EX_SRLV), .LBU(LBU), .LBU_2(id_ex_1_lbu_2));  // open: eq34, eq34_2, Pre, Pre_2, simm, simm_2
  Multiplexer #(.width(5), .disabled(0), .enable("false")) multiplexer_14 (
    .in0(EXI[20:16]), .in1(EXI[15:11]), .out(multiplexer_14_out), .sel(EXDst));
  Multiplexer #(.width(5), .disabled(0), .enable("false")) multiplexer_15 (
    .in0(multiplexer_14_out), .in1({5{1'b1}}), .out(multiplexer_15_out), .sel(EXJ[2]));
  Multiplexer #(.width(5), .disabled(0), .enable("false")) multiplexer_16 (
    .in0(MemI[20:16]), .in1(MemI[15:11]), .out(multiplexer_16_out), .sel(MemDst));
  Multiplexer #(.width(5), .disabled(0), .enable("false")) multiplexer_17 (
    .in0(multiplexer_13_out), .in1({5{1'b1}}), .out(multiplexer_17_out), .sel(MemJ[2]));
  Multiplexer #(.width(5), .disabled(0), .enable("false")) multiplexer_18 (
    .in0(multiplexer_16_out), .in1({5{1'b1}}), .out(multiplexer_18_out), .sel(MemJ[2]));
  Multiplexer #(.select(2), .width(32), .disabled(0), .enable("false")) multiplexer_19 (
    .in0(id_ex_1_r1_2), .in1(multiplexer_24_out), .in2(mem_wb_1_alu_2), .in3(ex_mem_1_alu_2), .out(R1),
    .sel(id_ex_1_fwd1_2));
  Adder #(.width(32)) adder_2 (.a(EX_PC), .b(32'h4), .out(EXnextPC), .cin(1'b0));  // open: cout
  Shifter #(.width(32)) shifter_1 (.in({id_ex_1_imm_2, Jaddr}), .\dist (5'b00010), .out(shifter_1_out));
  Comparator #(.width(32)) comparator_1 (.a(32'h22), .b(R1), .eq(comparator_1_eq));  // open: gt, lt
  Multiplexer #(.width(32), .disabled(0), .enable("false")) multiplexer_20 (
    .in0(R2), .in1({id_ex_1_imm_2, Jaddr}), .out(multiplexer_20_out), .sel(id_ex_1_alu_src_2));
  Multiplexer #(.select(2), .width(32), .disabled(0), .enable("false")) multiplexer_21 (
    .in0(id_ex_1_r2_2), .in1(multiplexer_24_out), .in2(mem_wb_1_alu_2), .in3(ex_mem_1_alu_2), .out(R2),
    .sel(id_ex_1_fwd2_2));
  Adder #(.width(32)) adder_3 (.a(shifter_1_out), .b(EXnextPC), .out(branchPC));  // open: cin, cout
  \重定向fwd  \u_重定向fwd_1  (
    .OP(Ins[31:26]), .EX_WriteReg_num(multiplexer_12_out), .EX_RegWrite(EX_RegWrite),
    .MEM_WriteReg_num(multiplexer_17_out), .MEM_RegWrite(Mem_RegWrite), .Func(Func), .ID_R1_num(RW1),
    .ID_R2_num(RW2), .MEM_Mem2Reg(MEM_Mem2Reg), .Fwd1(Fwd1), .Fwd2(Fwd2), .loaduse(loaduse),
    .EX_Mem2Reg(EX_Mem2Reg));
  Counter #(.width(16), .max('hffff)) counter_4 (
    .count(EXJ[0]), .Q(\无条件分支数 ), .clk(CLK), .clr(RST));  // open: load, D, carry
  MIPS_ALU mips_alu_1 (
    .X(R1), .Y(multiplexer_20_out), .AluOP(id_ex_1_alu_op_2), .Equal(EXEQ),
    .Result({mips_alu_1_result, EXles}), .shamt(multiplexer_22_out));  // open: Result_2
  \数据相关检测  \u_数据相关检测_1  (
    .OP(Ins[31:26]), .EX_WriteReg_num(multiplexer_15_out), .EX_RegWrite(EX_RegWrite),
    .MEM_WriteReg_num(multiplexer_18_out), .MEM_RegWrite(Mem_RegWrite), .\数据相关 (Drelate), .Func(Func),
    .ID_R1_num(RW1), .ID_R2_num(RW2));
  EX_MEM ex_mem_1 (
    .nextPC(EX_PC), .Reg_Write(EX_RegWrite), .MemToReg(EX_Mem2Reg), .R2(R2), .MemWrite(id_ex_1_memwrite_2),
    .RegDst(EXDst), .ALU({mips_alu_1_result, EXles}), .RST(RST), .CLK(CLK), .IR(EXI),
    .SysCALL(id_ex_1_syscall_2), .nextPC_2(MEM_PC), .Reg_Write_2(Mem_RegWrite), .MemToReg_2(MEM_Mem2Reg),
    .R2_2(ex_mem_1_r2_2), .MemWrite_2(ex_mem_1_memwrite_2), .RegDst_2(MemDst), .ALU_2(ex_mem_1_alu_2),
    .IR_2(MemI), .SysCALL_2(ex_mem_1_syscall_2), .EN(EN), .BNE(EXBNE), .BNE_2(ex_mem_1_bne_2), .BEQ(EXBEQ),
    .BEQ_2(ex_mem_1_beq_2), .J(EXJ), .EXJ(MemJ), .BGTZ(EXBGTZ), .EXBGTZ(ex_mem_1_exbgtz),
    .eq34(comparator_1_eq), .eq34_2(ex_mem_1_eq34_2), .R1(R2), .R1_2(ex_mem_1_r1_2), .LBU(id_ex_1_lbu_2),
    .LBU_2(ex_mem_1_lbu_2));
  Multiplexer #(.width(5), .disabled(0), .enable("false")) multiplexer_22 (
    .in0(EXI[10:6]), .in1(R1[4:0]), .out(multiplexer_22_out), .sel(EX_SRLV));
  and and_3 (and_3_out, ~EXEQ, ~EXles);  // AND_Gate
  // Probe on ex_mem_1_r2_2
  and and_4 (and_4_out, EXBGTZ, and_3_out);
  and and_5 (and_5_out, EXEQ, EXBEQ);
  and and_6 (and_6_out, ~EXEQ, EXBNE);  // AND_Gate
  // MIPS_RAM mips_ram_1: pin names not known; wires that end beside it: ex_mem_1_beq_2, ex_mem_1_bne_2, ex_mem_1_exbgtz, ex_mem_1_alu_2[21:2], ex_mem_1_r2_2, ex_mem_1_memwrite_2, CLK, MEM_Mem2Reg, RST, mips_ram_1_p10
  or or_5 (branch, and_5_out, and_4_out, and_6_out);
  MEM_WB mem_wb_1 (
    .nextPC(MEM_PC), .Reg_Write(Mem_RegWrite), .MemToReg(MEM_Mem2Reg), .DM(mips_ram_1_p10), .RegDst(MemDst),
    .ALU(ex_mem_1_alu_2), .RST(RST), .CLK(CLK), .IR(MemI), .SysCALL(ex_mem_1_syscall_2), .nextPC_2(WB_PC),
    .Reg_Write_2(TEN), .MemToReg_2(mem_wb_1_memtoreg_2), .DM_2(mem_wb_1_dm_2), .RegDst_2(mem_wb_1_regdst_2),
    .ALU_2(mem_wb_1_alu_2), .IR_2(mem_wb_1_ir_2), .SysCALL_2(out_2), .EN(EN), .EXJ(MemJ), .WBJ(WBJ),
    .LedData(ex_mem_1_r1_2), .LedData_2(mem_wb_1_leddata_2), .eq34(ex_mem_1_eq34_2), .eq34_2(out_1),
    .LBU(ex_mem_1_lbu_2), .WB_LBU(WB_LBU));  // open: R1_2, R1
  Counter #(.width(16), .max('hffff)) counter_5 (
    .count(branch), .Q(\条件分支成功数 ), .clk(CLK), .clr(RST));  // open: load, D, carry
  Multiplexer #(.width(32), .disabled(0), .enable("false")) multiplexer_23 (
    .in0(mem_wb_1_alu_2), .in1(mem_wb_1_dm_2),
    .out({multiplexer_23_out_4, multiplexer_23_out_3, multiplexer_23_out_2, multiplexer_23_out}),
    .sel(mem_wb_1_memtoreg_2));
  // Probe on {multiplexer_23_out_4, multiplexer_23_out_3, multiplexer_23_out_2, multiplexer_23_out}
  Adder #(.width(32)) adder_4 (.a(WB_PC), .b(32'h4), .out(WBnextPC), .cin(1'b0));  // open: cout
  Register #(.width(32)) register_1 (.D(mem_wb_1_leddata_2), .en(out_1), .Q(LedData), .clk(CLK));  // open: clr
  Multiplexer #(.width(32), .disabled(0), .enable("false")) multiplexer_24 (
    .in0(mem_wb_1_dm_2), .in1({{24{1'b0}}, ByteEx}), .out(multiplexer_24_out), .sel(WB_LBU));
  Multiplexer #(.select(2), .width(8), .disabled(0), .enable("false")) multiplexer_25 (
    .in0(multiplexer_23_out), .in1(multiplexer_23_out_2), .in2(multiplexer_23_out_3),
    .in3(multiplexer_23_out_4), .out(ByteEx), .sel(mem_wb_1_alu_2[1:0]));

  // Other names for the same wires on the sheet: EXJMP = EXJ[0]; EXJR = EXJ[1]; EXJAL = EXJ[2]; Ins[5:0] = Func;
  //   OP[5:0] = Ins[31:26]; JMP = J[0]; JR = J[1]; JAL = J[2]; Jaddr[31:28] = EX_PC[31:28]; MemJMP = MemJ[0];
  //   MemJR = MemJ[1]; MemJAL = MemJ[2]; WBJMP = WBJ[0]; WBJR = WBJ[1]; WBJAL = WBJ[2]

  // Notes on the sheet:
  //   中断源
  //   中断等待指示
  //   数码管输出
  //   指令存储器
  //   contents of rom_1 (hex, n*v repeats v):
  //   20110005 8000c06 20110001 20120002 20130003 20140004 8000c0b 20110001 20120002 20130003 20140004
  //   8000c10 20110001 20120002 20130003 20140004 8000c15 20110001 20120002 20130003 20140004 8000c1a
  //   20110001 20120002 20130003 20140004 8000c1f 20110001 20120002 20130003 20140004 8000c24 20110001
  //   20120002 20130003 20140004 8000c29 20110001 20120002 20130003 20140004 2231ffff 1620ffe0 20100001
  //   201200ff 20110001 20130003 12120005 12100004 20110001 20120002 20130003 20140004 16310004 16320003
  //   20110001 20120002 20130003 c000c3d 2002000a c 20100000 22100001 102020 20020022 c 3e00008
  //   contents of rom_2 (hex, n*v repeats v):
  //   20110020 20020022 8000c06 20110004 20120005 20130006 10000003 20110007 20120008 20130009 14110003
  //   2011000a 2012000b 2013000c c000c14 2002000a 0 0 0 c 2231ffff 0 0 0 112020 0 0 0 c 1620fff6 3e00008
  //   contents of rom_3 (hex, n*v repeats v):
  //   20110020 20020022 8000c06 20110004 20120005 20130006 10000003 20110007 20120008 20130009 14110003
  //   2011000a 2012000b 2013000c c000c14 2002000a 0 0 0 c 2231ffff 0 0 0 112020 0 0 0 c 1620fff6 3e00008
  //   rs
  //   rt
  //   rd
  //   OP
  //   Func
  //   MemToReg
  //   MemWrite
  //   AluOP
  //   AluSrcB
  //   RegWrite
  //   RegDst
  //   Syscall
  //   流水调试日志用
endmodule

module \气泡流水线  (
  output out_1,
  output out_2
);

  wire and_1_out, and_2_out, and_3_out, and_4_out, and_5_out, and_6_out, BGTZ, branch, CLK, Drelate, EN,
       eq34, ex_mem_1_p20, ex_mem_1_p22, ex_mem_1_p23, ex_mem_1_p24, ex_mem_1_p25, ex_mem_1_p28,
       ex_mem_1_p29, ex_mem_1_p31, EX_RegWrite, EXBEQ, EXBGTZ, EXBNE, EXDst, EXEQ, EXles, Go,
       id_ex_1_alu_src_2, id_ex_1_memtoreg_2, id_ex_1_memwrite_2, id_ex_1_syscall_2, IR1, IR2, IR3,
       Mem_RegWrite, mem_wb_1_p17, mem_wb_1_p19, MemDst, mips_ram_1_p10, not_1_out, or_2_out, or_3_out,
       registerfile_1_p7, registerfile_1_p8, RST, SignedExt, TEN, W1, W2, W3, \硬布线控制器_1_alu_src ,
       \硬布线控制器_1_beq , \硬布线控制器_1_bne , \硬布线控制器_1_memtoreg , \硬布线控制器_1_memwrite , \硬布线控制器_1_regdst ,
       \硬布线控制器_1_regwrite , \硬布线控制器_1_syscall ;
  wire [2:0] EXJ, J, MemJ, WBJ;
  wire [3:0] id_ex_1_alu_op_2, \硬布线控制器_1_alu_op ;
  wire [4:0] multiplexer_6_out, multiplexer_11_out, multiplexer_12_out, multiplexer_13_out,
       multiplexer_14_out, RW1, RW2, RW3;
  wire [5:0] Func;
  wire [15:0] \LoadUse次数 , \总周期数 , \插入气泡数 , \无条件分支数 , \条件分支成功数 ;
  wire [27:2] Jaddr;
  wire [31:0] adder_1_out, bit_extender_1_out, bit_extender_2_out, branchPC, din, ex_mem_1_p30, EX_PC, EXI,
       EXnextPC, ID_PC, IF_PC, LedData, MEM_PC, mem_wb_1_p15, mem_wb_1_p22, mem_wb_1_p23, MemI,
       mips_probe_1_p1, mips_regifile_1_r1, mips_regifile_1_r2, multiplexer_1_out, multiplexer_2_out,
       multiplexer_3_out, multiplexer_9_out, multiplexer_10_out, multiplexer_15_out, R1, R2, rom_2_data,
       rom_3_data, shifter_1_out, WB_PC, WBnextPC;
  wire [31:1] mips_alu_1_result;
  wire [31:6] Ins;
  wire [31:26] id_ex_1_imm_2;

  Button \u_总复位  (.out(RST));
  Button _1 (.out(IR1));
  Button _2 (.out(IR2));
  Button _3 (.out(IR3));
  Multiplexer #(.width(32), .disabled(0), .enable("false")) multiplexer_1 (
    .in0(adder_1_out), .in1(branchPC), .out(multiplexer_1_out), .sel(branch));
  or or_1 (EN, out_1, not_1_out);
  not not_1 (not_1_out, out_2);
  Button \u_继续运行  (.out(Go));
  LED led_1 (.in(W1));
  LED led_2 (.in(W2));
  LED led_3 (.in(W3));
  Register #(.width(32)) register_1 (.D(R2), .en(eq34), .Q(LedData), .clk(CLK));  // open: clr
  Multiplexer #(.width(32), .disabled(0), .enable("false")) multiplexer_2 (
    .in0(multiplexer_1_out), .in1({EX_PC[31:28], Jaddr, 2'b00}), .out(multiplexer_2_out), .sel(EXJ[0]));
  Multiplexer #(.width(32), .disabled(0), .enable("false")) multiplexer_3 (
    .in0(multiplexer_2_out), .in1(R1), .out(multiplexer_3_out), .sel(EXJ[1]));
  and and_1 (and_1_out, EN, ~Drelate);  // AND_Gate
  Hex_Digit_Display hex_digit_display_1 (.value(LedData[31:28]));  // open: dp
  Hex_Digit_Display hex_digit_display_2 (.value(LedData[27:24]));  // open: dp
  Register #(.width(32)) PC (.D(multiplexer_3_out), .en(and_1_out), .Q(IF_PC), .clk(CLK), .clr(RST));
  Hex_Digit_Display hex_digit_display_3 (.value(LedData[23:20]));  // open: dp
  Hex_Digit_Display hex_digit_display_4 (.value(LedData[19:16]));  // open: dp
  Hex_Digit_Display hex_digit_display_5 (.value(LedData[15:12]));  // open: dp
  Hex_Digit_Display hex_digit_display_6 (.value(LedData[11:8]));  // open: dp
  Adder #(.width(32)) adder_1 (.a(IF_PC), .b(32'h4), .out(adder_1_out), .cin(1'b0));  // open: cout
  // Mips_Probe mips_probe_1: pin names not known; wires that end beside it: mips_probe_1_p1
  Hex_Digit_Display hex_digit_display_7 (.value(LedData[3:0]));  // open: dp
  Hex_Digit_Display hex_digit_display_8 (.value(LedData[7:4]));  // open: dp
  Clock clock_1 (.out(CLK));
  ROM #(.addrWidth(10), .dataWidth(32)) rom_1 (.addr(IF_PC[11:2]), .data(mips_probe_1_p1));  // open: sel
  or or_2 (or_2_out, EXJ[0], branch);
  and and_2 (and_2_out, EN, ~Drelate);  // AND_Gate
  IF_ID if_id_1 (
    .nextPC(IF_PC), .Instr(mips_probe_1_p1), .RST(or_2_out), .CLK(CLK), .EN(and_2_out), .nextPC_2(ID_PC),
    .Instr_2({Ins, Func}));  // open: pre, pre_2
  ROM #(.addrWidth(10), .dataWidth(32)) rom_2 (.addr(WB_PC[11:2]), .data(rom_2_data));  // open: sel
  ROM #(.addrWidth(10), .dataWidth(32)) rom_3 (.addr(ID_PC[11:2]), .data(rom_3_data));  // open: sel
  // Probe on \总周期数 
  // Probe on \无条件分支数 
  // Probe on \条件分支成功数 
  // Probe on \插入气泡数 
  // Probe on \LoadUse次数 
  // Probe on mem_wb_1_p15[20:16]
  assign bit_extender_1_out = {{16{Ins[15]}}, {Ins[15:6], Func}};  // Bit_Extender bit_extender_1
  // Probe on IF_PC[11:0]
  \硬布线控制器  \u_硬布线控制器_1  (
    .Func(Func), .OP(Ins[31:26]), .ALU_OP(\硬布线控制器_1_alu_op ), .MemToReg(\硬布线控制器_1_memtoreg ),
    .MemWrite(\硬布线控制器_1_memwrite ), .ALU_SRC(\硬布线控制器_1_alu_src ), .RegWrite(\硬布线控制器_1_regwrite ),
    .SysCALL(\硬布线控制器_1_syscall ), .SignedExt(SignedExt), .RegDst(\硬布线控制器_1_regdst ), .JR(J[1]), .JMP(J[0]),
    .Beq(\硬布线控制器_1_beq ), .JAL(J[2]), .Bne(\硬布线控制器_1_bne ), .BGTZ(BGTZ));  // open: SRLV, LBU
  Multiplexer #(.width(5), .disabled(0), .enable("false")) multiplexer_4 (
    .in0(Ins[25:21]), .in1(5'b00010), .out(RW1), .sel(\硬布线控制器_1_syscall ));
  Multiplexer #(.width(5), .disabled(0), .enable("false")) multiplexer_5 (
    .in0(Ins[20:16]), .in1(5'b00100), .out(RW2), .sel(\硬布线控制器_1_syscall ));
  // Probe on RW2
  Multiplexer #(.width(5), .disabled(0), .enable("false")) multiplexer_6 (
    .in0(mem_wb_1_p15[20:16]), .in1(mem_wb_1_p15[15:11]), .out(multiplexer_6_out), .sel(mem_wb_1_p19));
  assign bit_extender_2_out = {{16{1'b0}}, {Ins[15:6], Func}};  // Bit_Extender bit_extender_2
  Multiplexer #(.select(2), .width(32), .enable("false")) multiplexer_7 ();  // open: in0, in1, in2, in3, out, sel
  // Probe on ID_PC[11:0]
  // Probe on EX_PC[11:0]
  // Probe on RW2
  Multiplexer #(.width(5), .disabled(0), .enable("false")) multiplexer_8 (
    .in0(multiplexer_6_out), .in1({5{1'b1}}), .out(RW3), .sel(WBJ[2]));
  Multiplexer #(.width(32), .disabled(0), .enable("false")) multiplexer_9 (
    .in0(bit_extender_2_out), .in1(bit_extender_1_out), .out(multiplexer_9_out), .sel(SignedExt));
  // RegisterFile registerfile_1: pin names not known; wires that end beside it: din, CLK, TEN, RW3, RW1, RW2, registerfile_1_p7, registerfile_1_p8
  // Probe on MEM_PC[11:0]
  // Probe on multiplexer_10_out
  Multiplexer #(.width(32), .disabled(0), .enable("false")) multiplexer_10 (
    .in0(din), .in1(WBnextPC), .out(multiplexer_10_out), .sel(WBJ[2]));
  // Probe on registerfile_1_p7
  // Probe on registerfile_1_p8
  // Probe on RW1
  // Probe on RW2
  // Probe on RW3
  // Probe on WB_PC[11:0]
  MIPS_Regifile mips_regifile_1 (
    .Din(multiplexer_10_out), .Clk(CLK), .R1(mips_regifile_1_r1), .R2(mips_regifile_1_r2), .WE(TEN),
    .W_num(RW3), .R1_num(RW1), .R2_num(RW2));
  // Probe on mips_regifile_1_r1
  // Probe on mips_regifile_1_r2
  // Probe on multiplexer_9_out
  // Probe on din
  // Probe on MemI
  or or_3 (or_3_out, EXJ[0], Drelate, branch);
  Counter #(.width(16), .max('hffff)) counter_1 (.count(EN), .Q(\总周期数 ), .clk(CLK), .clr(RST));  // open: load, D, carry
  ID_EX id_ex_1 (
    .nextPC(ID_PC), .ALU_SRC(\硬布线控制器_1_alu_src ), .R1(mips_regifile_1_r1), .MemToReg(\硬布线控制器_1_memtoreg ),
    .R2(mips_regifile_1_r2), .MemWrite(\硬布线控制器_1_memwrite ), .IMM(multiplexer_9_out),
    .SysCALL(\硬布线控制器_1_syscall ), .ALU_OP(\硬布线控制器_1_alu_op ), .nextPC_2(EX_PC),
    .ALU_SRC_2(id_ex_1_alu_src_2), .R1_2(R1), .MemToReg_2(id_ex_1_memtoreg_2), .R2_2(R2),
    .MemWrite_2(id_ex_1_memwrite_2), .IMM_2({id_ex_1_imm_2, Jaddr}), .SysCALL_2(id_ex_1_syscall_2),
    .ALU_OP_2(id_ex_1_alu_op_2), .EN(EN), .IR({Ins, Func}), .IR_2(EXI), .RST(or_3_out), .CLK(CLK),
    .RegDst(\硬布线控制器_1_regdst ), .RegDst_2(EXDst), .Reg_Write(\硬布线控制器_1_regwrite ), .Reg_Write_2(EX_RegWrite),
    .BNE(\硬布线控制器_1_bne ), .BNE_2(EXBNE), .BEQ(\硬布线控制器_1_beq ), .BEQ_2(EXBEQ), .J(J), .J_2(EXJ), .BGTZ(BGTZ),
    .BGTZ_2(EXBGTZ));  // open: fwd1, fwd1_2, fwd2, fwd2_2, eq34, eq34_2, SRLV, SRLV_2, LBU, LBU_2, Pre, Pre_2, simm, simm_2
  Multiplexer #(.width(5), .disabled(0), .enable("false")) multiplexer_11 (
    .in0(EXI[20:16]), .in1(EXI[15:11]), .out(multiplexer_11_out), .sel(EXDst));
  Multiplexer #(.width(5), .disabled(0), .enable("false")) multiplexer_12 (
    .in0(multiplexer_11_out), .in1({5{1'b1}}), .out(multiplexer_12_out), .sel(EXJ[2]));
  Multiplexer #(.width(5), .disabled(0), .enable("false")) multiplexer_13 (
    .in0(MemI[20:16]), .in1(MemI[15:11]), .out(multiplexer_13_out), .sel(MemDst));
  Counter #(.width(16), .max('hffff)) counter_2 (
    .count(Drelate), .Q(\插入气泡数 ), .clk(CLK), .clr(RST));  // open: load, D, carry
  Multiplexer #(.width(5), .disabled(0), .enable("false")) multiplexer_14 (
    .in0(multiplexer_13_out), .in1({5{1'b1}}), .out(multiplexer_14_out), .sel(MemJ[2]));
  Adder #(.width(32)) adder_2 (.a(EX_PC), .b(32'h4), .out(EXnextPC), .cin(1'b0));  // open: cout
  Shifter #(.width(32)) shifter_1 (.in({id_ex_1_imm_2, Jaddr}), .\dist (5'b00010), .out(shifter_1_out));
  Comparator #(.width(32)) comparator_1 (.a(32'h22), .b(R1), .eq(eq34));  // open: gt, lt
  Multiplexer #(.width(32), .disabled(0), .enable("false")) multiplexer_15 (
    .in0(R2), .in1({id_ex_1_imm_2, Jaddr}), .out(multiplexer_15_out), .sel(id_ex_1_alu_src_2));
  Adder #(.width(32)) adder_3 (.a(shifter_1_out), .b(EXnextPC), .out(branchPC));  // open: cin, cout
  Counter #(.width(16), .max('hffff)) counter_3 (
    .count(EXJ[0]), .Q(\无条件分支数 ), .clk(CLK), .clr(RST));  // open: load, D, carry
  MIPS_ALU mips_alu_1 (
    .X(R1), .Y(multiplexer_15_out), .AluOP(id_ex_1_alu_op_2), .Equal(EXEQ),
    .Result({mips_alu_1_result, EXles}), .shamt(EXI[10:6]));  // open: Result_2
  // Probe on {EX_PC[31:28], Jaddr, 2'b00}
  \数据相关检测  \u_数据相关检测_1  (
    .OP(Ins[31:26]), .EX_WriteReg_num(multiplexer_12_out), .EX_RegWrite(EX_RegWrite),
    .MEM_WriteReg_num(multiplexer_14_out), .MEM_RegWrite(Mem_RegWrite), .\数据相关 (Drelate), .Func(Func),
    .ID_R1_num(RW1), .ID_R2_num(RW2));
  // EX_MEM ex_mem_1: pin names not known; wires that end beside it: EX_PC, EXI, EXBEQ, EXJ, EXBNE, id_ex_1_memtoreg_2, EXBGTZ, id_ex_1_memwrite_2, EX_RegWrite, EXDst, id_ex_1_syscall_2, eq34, {mips_alu_1_result, EXles}, R2, CLK, EN, RST, MEM_PC, MemI, ex_mem_1_p20, MemJ, ex_mem_1_p22, ex_mem_1_p23, ex_mem_1_p24, ex_mem_1_p25, Mem_RegWrite, MemDst, ex_mem_1_p28, ex_mem_1_p29, ex_mem_1_p30, ex_mem_1_p31
  and and_3 (and_3_out, ~EXEQ, ~EXles);  // AND_Gate
  // Probe on ex_mem_1_p31
  and and_4 (and_4_out, EXBGTZ, and_3_out);
  and and_5 (and_5_out, EXEQ, EXBEQ);
  and and_6 (and_6_out, ~EXEQ, EXBNE);  // AND_Gate
  // MIPS_RAM mips_ram_1: pin names not known; wires that end beside it: ex_mem_1_p20, ex_mem_1_p22, ex_mem_1_p24, ex_mem_1_p30[21:2], ex_mem_1_p31, ex_mem_1_p25, CLK, ex_mem_1_p23, RST, mips_ram_1_p10
  or or_4 (branch, and_5_out, and_4_out, and_6_out);
  // MEM_WB mem_wb_1: pin names not known; wires that end beside it: MEM_PC, MemI, MemJ, ex_mem_1_p23, Mem_RegWrite, MemDst, ex_mem_1_p28, ex_mem_1_p29, ex_mem_1_p30, mips_ram_1_p10, CLK, EN, RST, WB_PC, mem_wb_1_p15, WBJ, mem_wb_1_p17, TEN, mem_wb_1_p19, out_2, out_1, mem_wb_1_p22, mem_wb_1_p23
  Counter #(.width(16), .max('hffff)) counter_4 (
    .count(branch), .Q(\条件分支成功数 ), .clk(CLK), .clr(RST));  // open: load, D, carry
  Multiplexer #(.width(32), .disabled(0), .enable("false")) multiplexer_16 (
    .in0(mem_wb_1_p22), .in1(mem_wb_1_p23), .out(din), .sel(mem_wb_1_p17));
  // Probe on din
  Adder #(.width(32)) adder_4 (.a(WB_PC), .b(32'h4), .out(WBnextPC), .cin(1'b0));  // open: cout

  // Other names for the same wires on the sheet: EXJMP = EXJ[0]; EXJR = EXJ[1]; EXJAL = EXJ[2]; Ins[5:0] = Func;
  //   OP[5:0] = Ins[31:26]; JMP = J[0]; JR = J[1]; JAL = J[2]; Jaddr[31:28] = EX_PC[31:28]; MemJMP = MemJ[0];
  //   MemJR = MemJ[1]; MemJAL = MemJ[2]; WBJMP = WBJ[0]; WBJR = WBJ[1]; WBJAL = WBJ[2]

  // Notes on the sheet:
  //   中断源
  //   中断等待指示
  //   数码管输出
  //   指令存储器
  //   contents of rom_1 (hex, n*v repeats v):
  //   20110001 8000c05 20110001 20120002 20130003 8000c09 20110001 20120002 20130003 8000c0d 20110001
  //   20120002 20130003 8000c11 20110001 20120002 20130003 c000cbb 20100001 20110001 118fc0 112020
  //   20020022 c 118882 12200001 8000c15 112020 20020022 c 20110001 118880 112020 20020022 c 12200001
  //   8000c1f 20110001 118fc0 112020 20020022 c 1188c3 112020 20020022 c 118903 112020 20020022 c 118903
  //   112020 20020022 c 118903 112020 20020022 c 118903 112020 20020022 c 118903 112020 20020022 c 118903
  //   112020 20020022 c 118903 112020 20020022 c 20100001 109fc0 139fc3 8021 2012000c 24160003 26100001
  //   3210000f 20080008 20090001 139900 2709825 132020 20020022 c 1094022 1500fff9 22100001 2018000f
  //   2188024 108700 20080008 20090001 139902 2709825 132021 20020022 c 1094022 1500fff9 108702 2c9b022
  //   12c00001 8000c50 4020 1084027 84400 3508ffff 82021 20020022 c 2010ffff 20110000 ae300000 22100001
  //   22310004 ae300000 22100001 22310004 ae300000 22100001 22310004 ae300000 22100001 22310004 ae300000
  //   22100001 22310004 ae300000 22100001 22310004 ae300000 22100001 22310004 ae300000 22100001 22310004
  //   ae300000 22100001 22310004 ae300000 22100001 22310004 ae300000 22100001 22310004 ae300000 22100001
  //   22310004 ae300000 22100001 22310004 ae300000 22100001 22310004 ae300000 22100001 22310004 ae300000
  //   22100001 22310004 22100001 8020 2011003c 8e130000 8e340000 274402a 11000002 ae330000 ae140000
  //   2231fffc 1611fff8 102020 20020022 c 22100004 2011003c 1611fff2 20020032 c 8000c00 2002000a c
  //   20100000 22100001 102020 20020022 c 22100002 102020 20020022 c 22100003 102020 20020022 c 22100004
  //   102020 20020022 c 22100005 102020 20020022 c 22100006 102020 20020022 c 22100007 102020 20020022 c
  //   22100008 102020 20020022 20020022 c 3e00008
  //   contents of rom_2 (hex, n*v repeats v):
  //   20110020 20020022 8000c06 20110004 20120005 20130006 10000003 20110007 20120008 20130009 14110003
  //   2011000a 2012000b 2013000c c000c14 2002000a 0 0 0 c 2231ffff 0 0 0 112020 0 0 0 c 1620fff6 3e00008
  //   contents of rom_3 (hex, n*v repeats v):
  //   20110020 20020022 8000c06 20110004 20120005 20130006 10000003 20110007 20120008 20130009 14110003
  //   2011000a 2012000b 2013000c c000c14 2002000a 0 0 0 c 2231ffff 0 0 0 112020 0 0 0 c 1620fff6 3e00008
  //   rs
  //   rt
  //   rd
  //   OP
  //   Func
  //   MemToReg
  //   MemWrite
  //   AluOP
  //   AluSrcB
  //   RegWrite
  //   RegDst
  //   Syscall
  //   流水调试日志用
endmodule

module \控制信号生成2  (
  input  OP0,
  input  OP1,
  input  OP2,
  input  OP3,
  input  OP4,
  input  OP5,
  input  F0,
  input  F1,
  input  F2,
  input  F3,
  input  F4,
  input  F5,
  output SRLV,
  output LBU,
  output BGTZ
);

  wire not_1_out, not_2_out, not_3_out, not_4_out, not_5_out, not_6_out, not_7_out, not_8_out, not_9_out,
       not_10_out, not_11_out, not_12_out, not_13_out, not_14_out, not_15_out, not_16_out, not_17_out;

  not not_1 (not_1_out, OP5);
  not not_2 (not_2_out, OP4);
  not not_3 (not_3_out, OP3);
  not not_4 (not_4_out, OP2);
  not not_5 (not_5_out, OP1);
  not not_6 (not_6_out, OP0);
  not not_7 (not_7_out, F5);
  not not_8 (not_8_out, F4);
  not not_9 (not_9_out, F3);
  not not_10 (not_10_out, F0);
  not not_11 (not_11_out, OP4);
  not not_12 (not_12_out, OP3);
  not not_13 (not_13_out, OP1);
  not not_14 (not_14_out, OP0);
  not not_15 (not_15_out, OP5);
  not not_16 (not_16_out, OP4);
  not not_17 (not_17_out, OP3);
  and and_1 (SRLV, not_1_out, not_2_out, not_3_out, not_4_out, not_5_out, not_6_out, not_7_out, not_8_out, not_9_out, F2, F1, not_10_out);
  and and_2 (LBU, OP5, not_11_out, not_12_out, OP2, not_13_out, not_14_out);
  and and_3 (BGTZ, not_15_out, not_16_out, not_17_out, OP2, OP1, OP0);
endmodule

module \重定向fwd  (
  input  [5:0] OP,
  input  [4:0] EX_WriteReg_num,
  input  EX_RegWrite,
  input  [4:0] MEM_WriteReg_num,
  input  MEM_RegWrite,
  input  [5:0] Func,
  input  [4:0] ID_R1_num,
  input  [4:0] ID_R2_num,
  input  MEM_Mem2Reg,
  input  EX_Mem2Reg,
  output loaduse,
  output [1:0] Fwd1,
  output [1:0] Fwd2
);

  wire and_1_out, and_2_out, and_3_out, and_4_out, and_5_out, and_6_out, and_7_out, and_8_out,
       comparator_1_eq, comparator_2_eq, comparator_3_eq, comparator_4_eq, comparator_5_eq, comparator_6_eq,
       not_1_out, not_2_out, or_1_out, \源寄存器使用情况_1_r1_used , \源寄存器使用情况_1_r2_used ;

  // Probe on MEM_WriteReg_num
  \源寄存器使用情况  \u_源寄存器使用情况_1  (
    .OP0(OP[0]), .OP1(OP[1]), .OP2(OP[2]), .OP3(OP[3]), .OP4(OP[4]), .OP5(OP[5]), .F0(Func[0]), .F1(Func[1]),
    .F2(Func[2]), .F3(Func[3]), .F4(Func[4]), .F5(Func[5]), .R1_Used(\源寄存器使用情况_1_r1_used ),
    .R2_Used(\源寄存器使用情况_1_r2_used ));
  Comparator #(.width(5)) comparator_1 (.a(ID_R1_num), .b({5{1'b0}}), .eq(comparator_1_eq));  // open: gt, lt
  // Probe on EX_WriteReg_num
  Comparator #(.width(5)) comparator_2 (.a(ID_R2_num), .b({5{1'b0}}), .eq(comparator_2_eq));  // open: gt, lt
  Comparator #(.width(5)) comparator_3 (.a(ID_R1_num), .b(MEM_WriteReg_num), .eq(comparator_3_eq));  // open: gt, lt
  Comparator #(.width(5)) comparator_4 (.a(ID_R2_num), .b(MEM_WriteReg_num), .eq(comparator_4_eq));  // open: gt, lt
  not not_1 (not_1_out, comparator_1_eq);
  Comparator #(.width(5)) comparator_5 (.a(ID_R2_num), .b(EX_WriteReg_num), .eq(comparator_5_eq));  // open: gt, lt
  Comparator #(.width(5)) comparator_6 (.a(ID_R1_num), .b(EX_WriteReg_num), .eq(comparator_6_eq));  // open: gt, lt
  not not_2 (not_2_out, comparator_2_eq);
  and and_1 (and_1_out, \源寄存器使用情况_1_r2_used , comparator_5_eq, not_2_out);
  and and_2 (and_2_out, \源寄存器使用情况_1_r1_used , comparator_6_eq, not_1_out);
  and and_3 (and_3_out, \源寄存器使用情况_1_r1_used , comparator_3_eq, not_1_out);
  and and_4 (and_4_out, not_2_out, comparator_4_eq, \源寄存器使用情况_1_r2_used );
  and and_5 (and_5_out, EX_RegWrite, and_1_out);
  and and_6 (and_6_out, EX_RegWrite, and_2_out);
  and and_7 (and_7_out, MEM_RegWrite, and_3_out);
  and and_8 (and_8_out, MEM_RegWrite, and_4_out);
  or or_1 (or_1_out, and_1_out, and_2_out);
  vfwd vfwd_1 (.Memread(1'b0), .ALU1(and_7_out), .ALU2(and_6_out), .High(Fwd1[1]), .Low(Fwd1[0]));
  vfwd vfwd_2 (.Memread(MEM_Mem2Reg), .ALU1(and_8_out), .ALU2(and_5_out), .High(Fwd2[1]), .Low(Fwd2[0]));
  and and_9 (loaduse, EX_Mem2Reg, or_1_out);

  // Other names for the same wires on the sheet: OP_CODE[5:0] = OP
endmodule

module vfwd (
  input  Memread,
  input  ALU1,
  input  ALU2,
  output High,
  output Low
);

  wire and_1_out, not_1_out;

  not not_1 (not_1_out, Memread);
  or or_1 (Low, ALU2, Memread);
  and and_1 (and_1_out, not_1_out, ALU1);
  or or_2 (High, ALU2, and_1_out);
endmodule

module \分支预测  (
  output out_1,
  output out_2
);

  wire A, and_1_out, and_5_out, and_6_out, and_7_out, and_8_out, and_9_out, and_10_out, B, BGTZ, branch, CLK,
       comparator_2_eq, Drelate, EN, EX_Mem2Reg, ex_mem_1_beq_2, ex_mem_1_bne_2, ex_mem_1_eq34_2,
       ex_mem_1_exbgtz, ex_mem_1_lbu_2, ex_mem_1_memwrite_2, ex_mem_1_syscall_2, EX_RegWrite, EX_SRLV, EXBEQ,
       EXBGTZ, EXBNE, EXBranch, EXDst, EXEQ, EXles, EXPre, Go, id_ex_1_alu_src_2, id_ex_1_lbu_2,
       id_ex_1_memwrite_2, id_ex_1_syscall_2, if_id_1_pre_2, IR1, IR2, IR3, LBU, loaduse, MEM_Mem2Reg,
       Mem_RegWrite, mem_wb_1_memtoreg_2, mem_wb_1_regdst_2, MemDst, miss, not_1_out, not_2_out, or_2_out,
       or_3_out, or_4_out, pre, registerfile_1_p7, registerfile_1_p8, RST, SignedExt, SRLV, suc, TEN, W1, W2,
       W3, WB_LBU, \硬布线控制器_1_alu_src , \硬布线控制器_1_beq , \硬布线控制器_1_bne , \硬布线控制器_1_memtoreg ,
       \硬布线控制器_1_memwrite , \硬布线控制器_1_regdst , \硬布线控制器_1_regwrite , \硬布线控制器_1_syscall , \跳转指令判断器_1_ifbra ;
  wire [1:0] Fwd1, Fwd2, id_ex_1_fwd1_2, id_ex_1_fwd2_2;
  wire [2:0] EXJ, J, MemJ, WBJ;
  wire [3:0] id_ex_1_alu_op_2, \硬布线控制器_1_alu_op ;
  wire [4:0] multiplexer_9_out, multiplexer_14_out, multiplexer_15_out, multiplexer_16_out,
       multiplexer_17_out, multiplexer_18_out, multiplexer_19_out, multiplexer_20_out, multiplexer_22_out,
       multiplexer_25_out, RW1, RW2, RW3;
  wire [5:0] Func;
  wire [7:0] ByteEx;
  wire [15:0] \LoadUse次数 , \总周期数 , \插入气泡数 , \无条件分支数 , \条件分支成功数 , \预测失败数 , \预测数 ;
  wire [27:2] Jaddr;
  wire [31:0] adder_1_out, bit_extender_1_out, bit_extender_2_out, branchPC, din, Dout, ex_mem_1_alu_2,
       ex_mem_1_r1_2, ex_mem_1_r2_2, EX_PC, EXI, EXnextPC, id_ex_1_r1_2, id_ex_1_r2_2, id_ex_1_simm_2, ID_PC,
       IF_PC, IF_PCout, LedData, MEM_PC, mem_wb_1_alu_2, mem_wb_1_dm_2, mem_wb_1_ir_2, mem_wb_1_leddata_2,
       MemI, mips_ram_1_p10, mips_regifile_1_r1, mips_regifile_1_r2, multiplexer_1_out, multiplexer_2_out,
       multiplexer_3_out, multiplexer_4_out, multiplexer_5_out, multiplexer_10_out, multiplexer_13_out,
       multiplexer_23_out, multiplexer_26_out, multiplexer_27_out, PC_4, PC_truebra, R1, R2, rom_2_data,
       rom_3_data, shifter_1_out, WB_PC, WBnextPC;
  wire [31:1] mips_alu_1_result;
  wire [31:6] Ins;
  wire [31:26] id_ex_1_imm_2;

  and and_1 (and_1_out, suc, EXBranch);
  \跳转指令判断器  \u_跳转指令判断器_1  (.IR(IF_PCout), .IFbra(\跳转指令判断器_1_ifbra ));
  and and_2 (pre, \跳转指令判断器_1_ifbra , not_1_out);
  and and_3 (A, EXBranch, ~suc);  // AND_Gate
  and and_4 (B, EXPre, ~and_1_out);  // AND_Gate
  not not_1 (not_1_out, miss);
  Multiplexer #(.width(32)) multiplexer_1 (.in0(PC_4), .in1(Dout), .out(multiplexer_1_out), .sel(pre));  // open: en
  Multiplexer #(.width(32)) multiplexer_2 (
    .in0(multiplexer_1_out), .in1(PC_truebra), .out(multiplexer_2_out), .sel(A));  // open: en
  Adder #(.width(32)) adder_1 (.a(EX_PC), .b(32'h4), .out(adder_1_out));  // open: cin, cout
  Button \u_总复位  (.out(RST));
  Button _1 (.out(IR1));
  Button _2 (.out(IR2));
  Button _3 (.out(IR3));
  Multiplexer #(.width(32)) multiplexer_3 (
    .in0(multiplexer_2_out), .in1(adder_1_out), .out(multiplexer_3_out), .sel(B));  // open: en
  or or_1 (EN, out_1, Go, not_2_out);
  not not_2 (not_2_out, out_2);
  Button \u_继续运行  (.out(Go));
  LED led_1 (.in(W1));
  LED led_2 (.in(W2));
  LED led_3 (.in(W3));
  and and_5 (and_5_out, EN, ~loaduse);  // AND_Gate
  Hex_Digit_Display hex_digit_display_1 (.value(LedData[31:28]));  // open: dp
  Hex_Digit_Display hex_digit_display_2 (.value(LedData[27:24]));  // open: dp
  \预测器  \u_预测器_1  (
    .IF_PCAddr(IF_PC), .EX_PCAddr(EX_PC), .BlockDataIn(PC_truebra), .BlkDataReady(or_2_out), .CLK(CLK),
    .Miss(miss), .DataOut(Dout));  // open: out_8
  Register #(.width(32)) PC (.D(multiplexer_3_out), .en(and_5_out), .Q(IF_PC), .clk(CLK), .clr(RST));
  Hex_Digit_Display hex_digit_display_3 (.value(LedData[19:16]));  // open: dp
  Hex_Digit_Display hex_digit_display_4 (.value(LedData[23:20]));  // open: dp
  or or_2 (or_2_out, branch, EXJ[0]);
  Multiplexer #(.width(32), .disabled(0), .enable("false")) multiplexer_4 (
    .in0(PC_4), .in1(branchPC), .out(multiplexer_4_out), .sel(branch));
  Hex_Digit_Display hex_digit_display_5 (.value(LedData[11:8]));  // open: dp
  Hex_Digit_Display hex_digit_display_6 (.value(LedData[15:12]));  // open: dp
  Clock clock_1 (.out(CLK));
  Counter #(.width(16), .max('hffff)) counter_1 (
    .count(EXPre), .Q(\预测数 ), .clk(CLK), .clr(RST));  // open: load, D, carry
  Adder #(.width(32)) adder_2 (.a(IF_PC), .b(32'h4), .out(PC_4), .cin(1'b0));  // open: cout
  // Mips_Probe mips_probe_1: pin names not known; wires that end beside it: IF_PCout
  Multiplexer #(.width(32), .disabled(0), .enable("false")) multiplexer_5 (
    .in0(multiplexer_4_out), .in1({EX_PC[31:28], Jaddr, 2'b00}), .out(multiplexer_5_out), .sel(EXJ[0]));
  Multiplexer #(.width(32), .disabled(0), .enable("false")) multiplexer_6 (
    .in0(multiplexer_5_out), .in1(R1), .out(PC_truebra), .sel(EXJ[1]));
  Hex_Digit_Display hex_digit_display_7 (.value(LedData[7:4]));  // open: dp
  Hex_Digit_Display hex_digit_display_8 (.value(LedData[3:0]));  // open: dp
  ROM #(.addrWidth(10), .dataWidth(32)) rom_1 (.addr(IF_PC[11:2]), .data(IF_PCout));  // open: sel
  or or_3 (or_3_out, A, B);
  and and_6 (and_6_out, EN, ~loaduse);  // AND_Gate
  // Probe on \预测失败数 
  IF_ID if_id_1 (
    .nextPC(IF_PC), .Instr(IF_PCout), .RST(or_3_out), .CLK(CLK), .EN(and_6_out), .nextPC_2(ID_PC),
    .Instr_2({Ins, Func}), .pre(pre), .pre_2(if_id_1_pre_2));
  ROM #(.addrWidth(10), .dataWidth(32)) rom_2 (.addr(WB_PC[11:2]), .data(rom_2_data));  // open: sel
  ROM #(.addrWidth(10), .dataWidth(32)) rom_3 (.addr(ID_PC[11:2]), .data(rom_3_data));  // open: sel
  // Probe on \预测数 
  // Probe on \总周期数 
  // Probe on \无条件分支数 
  // Probe on \条件分支成功数 
  // Probe on \插入气泡数 
  // Probe on \LoadUse次数 
  // Probe on mem_wb_1_ir_2[20:16]
  assign bit_extender_1_out = {{16{Ins[15]}}, {Ins[15:6], Func}};  // Bit_Extender bit_extender_1
  Comparator #(.width(32)) comparator_1 (.a(ID_PC), .b(PC_truebra), .eq(suc));  // open: gt, lt
  // Probe on IF_PC[11:0]
  // Probe on ID_PC[11:0]
  \硬布线控制器  \u_硬布线控制器_1  (
    .Func(Func), .OP(Ins[31:26]), .ALU_OP(\硬布线控制器_1_alu_op ), .MemToReg(\硬布线控制器_1_memtoreg ),
    .MemWrite(\硬布线控制器_1_memwrite ), .ALU_SRC(\硬布线控制器_1_alu_src ), .RegWrite(\硬布线控制器_1_regwrite ),
    .SysCALL(\硬布线控制器_1_syscall ), .SignedExt(SignedExt), .RegDst(\硬布线控制器_1_regdst ), .JR(J[1]), .JMP(J[0]),
    .Beq(\硬布线控制器_1_beq ), .JAL(J[2]), .Bne(\硬布线控制器_1_bne ), .SRLV(SRLV), .LBU(LBU), .BGTZ(BGTZ));
  Multiplexer #(.width(5), .disabled(0), .enable("false")) multiplexer_7 (
    .in0(Ins[25:21]), .in1(5'b00010), .out(RW1), .sel(\硬布线控制器_1_syscall ));
  Multiplexer #(.width(5), .disabled(0), .enable("false")) multiplexer_8 (
    .in0(Ins[20:16]), .in1(5'b00100), .out(RW2), .sel(\硬布线控制器_1_syscall ));
  // Probe on RW2
  Multiplexer #(.width(5), .disabled(0), .enable("false")) multiplexer_9 (
    .in0(mem_wb_1_ir_2[20:16]), .in1(mem_wb_1_ir_2[15:11]), .out(multiplexer_9_out), .sel(mem_wb_1_regdst_2));
  assign bit_extender_2_out = {{16{1'b0}}, {Ins[15:6], Func}};  // Bit_Extender bit_extender_2
  Multiplexer #(.width(32), .disabled(0), .enable("false")) multiplexer_10 (
    .in0(bit_extender_2_out), .in1(bit_extender_1_out), .out(multiplexer_10_out), .sel(SignedExt));
  // Probe on EX_PC[11:0]
  Multiplexer #(.width(5), .disabled(0), .enable("false")) multiplexer_11 (
    .in0(multiplexer_9_out), .in1({5{1'b1}}), .out(RW3), .sel(WBJ[2]));
  Multiplexer #(.width(32), .disabled(0), .enable("false")) multiplexer_12 (
    .in0(multiplexer_13_out), .in1({{24{1'b0}}, ByteEx}), .out(din), .sel(WB_LBU));
  Multiplexer #(.width(32), .disabled(0), .enable("false")) multiplexer_13 (
    .in0(multiplexer_26_out), .in1(WBnextPC), .out(multiplexer_13_out), .sel(WBJ[2]));
  // Probe on registerfile_1_p7
  // RegisterFile registerfile_1: pin names not known; wires that end beside it: din, CLK, TEN, RW3, RW1, RW2, registerfile_1_p7, registerfile_1_p8, EXI[15:11]
  // Probe on registerfile_1_p8
  // Probe on RW1
  // Probe on MEM_PC[11:0]
  // Probe on WB_PC[11:0]
  // Probe on RW2
  // Probe on RW3
  MIPS_Regifile mips_regifile_1 (
    .Din(din), .Clk(CLK), .R1(mips_regifile_1_r1), .R2(mips_regifile_1_r2), .WE(TEN), .W_num(RW3),
    .R1_num(RW1), .R2_num(RW2));
  // Probe on multiplexer_10_out
  // Probe on EXI[15:11]
  // Probe on MemI
  // Probe on mips_regifile_1_r2
  // Probe on din
  // Probe on MemI
  // Probe on multiplexer_20_out
  or or_4 (or_4_out, A, loaduse, B);
  Multiplexer #(.width(5), .disabled(0), .enable("false")) multiplexer_14 (
    .in0(EXI[20:16]), .in1(EXI[15:11]), .out(multiplexer_14_out), .sel(EXDst));
  Multiplexer #(.width(5), .disabled(0), .enable("false")) multiplexer_15 (
    .in0(multiplexer_14_out), .in1({5{1'b1}}), .out(multiplexer_15_out), .sel(EXJ[2]));
  Multiplexer #(.width(5), .disabled(0), .enable("false")) multiplexer_16 (
    .in0(MemI[20:16]), .in1(MemI[15:11]), .out(multiplexer_16_out), .sel(MemDst));
  Counter #(.width(16), .max('hffff)) counter_2 (.count(EN), .Q(\总周期数 ), .clk(CLK), .clr(RST));  // open: load, D, carry
  Counter #(.width(16), .max('hffff)) counter_3 (
    .count(loaduse), .Q(\LoadUse次数 ), .clk(CLK), .clr(RST));  // open: load, D, carry
  ID_EX id_ex_1 (
    .nextPC(ID_PC), .ALU_SRC(\硬布线控制器_1_alu_src ), .R1(mips_regifile_1_r1), .MemToReg(\硬布线控制器_1_memtoreg ),
    .R2(mips_regifile_1_r2), .MemWrite(\硬布线控制器_1_memwrite ), .IMM(multiplexer_10_out),
    .SysCALL(\硬布线控制器_1_syscall ), .ALU_OP(\硬布线控制器_1_alu_op ), .nextPC_2(EX_PC),
    .ALU_SRC_2(id_ex_1_alu_src_2), .R1_2(id_ex_1_r1_2), .MemToReg_2(EX_Mem2Reg), .R2_2(id_ex_1_r2_2),
    .MemWrite_2(id_ex_1_memwrite_2), .IMM_2({id_ex_1_imm_2, Jaddr}), .SysCALL_2(id_ex_1_syscall_2),
    .ALU_OP_2(id_ex_1_alu_op_2), .EN(EN), .IR({Ins, Func}), .IR_2(EXI), .RST(or_4_out), .CLK(CLK),
    .RegDst(\硬布线控制器_1_regdst ), .RegDst_2(EXDst), .Reg_Write(\硬布线控制器_1_regwrite ), .Reg_Write_2(EX_RegWrite),
    .BNE(\硬布线控制器_1_bne ), .BNE_2(EXBNE), .BEQ(\硬布线控制器_1_beq ), .BEQ_2(EXBEQ), .J(J), .J_2(EXJ), .BGTZ(BGTZ),
    .BGTZ_2(EXBGTZ), .fwd1(Fwd1), .fwd1_2(id_ex_1_fwd1_2), .fwd2(Fwd2), .fwd2_2(id_ex_1_fwd2_2), .SRLV(SRLV),
    .SRLV_2(EX_SRLV), .LBU(LBU), .LBU_2(id_ex_1_lbu_2), .Pre(if_id_1_pre_2), .Pre_2(EXPre),
    .simm(bit_extender_1_out), .simm_2(id_ex_1_simm_2));  // open: eq34, eq34_2
  Multiplexer #(.width(5), .disabled(0), .enable("false")) multiplexer_17 (
    .in0(EXI[20:16]), .in1(EXI[15:11]), .out(multiplexer_17_out), .sel(EXDst));
  Multiplexer #(.width(5), .disabled(0), .enable("false")) multiplexer_18 (
    .in0(multiplexer_17_out), .in1({5{1'b1}}), .out(multiplexer_18_out), .sel(EXJ[2]));
  Multiplexer #(.width(5), .disabled(0), .enable("false")) multiplexer_19 (
    .in0(MemI[20:16]), .in1(MemI[15:11]), .out(multiplexer_19_out), .sel(MemDst));
  Multiplexer #(.width(5), .disabled(0), .enable("false")) multiplexer_20 (
    .in0(multiplexer_16_out), .in1({5{1'b1}}), .out(multiplexer_20_out), .sel(MemJ[2]));
  Multiplexer #(.select(2), .width(32), .disabled(0), .enable("false")) multiplexer_21 (
    .in0(id_ex_1_r1_2), .in1(multiplexer_27_out), .in2(mem_wb_1_alu_2), .in3(ex_mem_1_alu_2), .out(R1),
    .sel(id_ex_1_fwd1_2));
  Multiplexer #(.width(5), .disabled(0), .enable("false")) multiplexer_22 (
    .in0(multiplexer_19_out), .in1({5{1'b1}}), .out(multiplexer_22_out), .sel(MemJ[2]));
  Adder #(.width(32)) adder_3 (.a(EX_PC), .b(32'h4), .out(EXnextPC), .cin(1'b0));  // open: cout
  Shifter #(.width(32)) shifter_1 (.in(id_ex_1_simm_2), .\dist (5'b00010), .out(shifter_1_out));
  Comparator #(.width(32)) comparator_2 (.a(32'h22), .b(R1), .eq(comparator_2_eq));  // open: gt, lt
  Multiplexer #(.width(32), .disabled(0), .enable("false")) multiplexer_23 (
    .in0(R2), .in1({id_ex_1_imm_2, Jaddr}), .out(multiplexer_23_out), .sel(id_ex_1_alu_src_2));
  Multiplexer #(.select(2), .width(32), .disabled(0), .enable("false")) multiplexer_24 (
    .in0(id_ex_1_r2_2), .in1(multiplexer_27_out), .in2(mem_wb_1_alu_2), .in3(ex_mem_1_alu_2), .out(R2),
    .sel(id_ex_1_fwd2_2));
  Adder #(.width(32)) adder_4 (.a(shifter_1_out), .b(EXnextPC), .out(branchPC));  // open: cin, cout
  \重定向fwd  \u_重定向fwd_1  (
    .OP(Ins[31:26]), .EX_WriteReg_num(multiplexer_15_out), .EX_RegWrite(EX_RegWrite),
    .MEM_WriteReg_num(multiplexer_20_out), .MEM_RegWrite(Mem_RegWrite), .Func(Func), .ID_R1_num(RW1),
    .ID_R2_num(RW2), .MEM_Mem2Reg(MEM_Mem2Reg), .Fwd1(Fwd1), .Fwd2(Fwd2), .loaduse(loaduse),
    .EX_Mem2Reg(EX_Mem2Reg));
  Counter #(.width(16), .max('hffff)) counter_4 (
    .count(EXJ[0]), .Q(\无条件分支数 ), .clk(CLK), .clr(RST));  // open: load, D, carry
  MIPS_ALU mips_alu_1 (
    .X(R1), .Y(multiplexer_23_out), .AluOP(id_ex_1_alu_op_2), .Equal(EXEQ),
    .Result({mips_alu_1_result, EXles}), .shamt(multiplexer_25_out));  // open: Result_2
  Multiplexer #(.width(5), .disabled(0), .enable("false")) multiplexer_25 (
    .in0(EXI[10:6]), .in1(R1[4:0]), .out(multiplexer_25_out), .sel(EX_SRLV));
  \数据相关检测  \u_数据相关检测_1  (
    .OP(Ins[31:26]), .EX_WriteReg_num(multiplexer_18_out), .EX_RegWrite(EX_RegWrite),
    .MEM_WriteReg_num(multiplexer_22_out), .MEM_RegWrite(Mem_RegWrite), .\数据相关 (Drelate), .Func(Func),
    .ID_R1_num(RW1), .ID_R2_num(RW2));
  Counter #(.width(16), .max('hffff)) counter_5 (.count(B), .Q(\预测失败数 ), .clk(CLK), .clr(RST));  // open: load, D, carry
  EX_MEM ex_mem_1 (
    .nextPC(EX_PC), .Reg_Write(EX_RegWrite), .MemToReg(EX_Mem2Reg), .R2(R2), .MemWrite(id_ex_1_memwrite_2),
    .RegDst(EXDst), .ALU({mips_alu_1_result, EXles}), .RST(RST), .CLK(CLK), .IR(EXI),
    .SysCALL(id_ex_1_syscall_2), .nextPC_2(MEM_PC), .Reg_Write_2(Mem_RegWrite), .MemToReg_2(MEM_Mem2Reg),
    .R2_2(ex_mem_1_r2_2), .MemWrite_2(ex_mem_1_memwrite_2), .RegDst_2(MemDst), .ALU_2(ex_mem_1_alu_2),
    .IR_2(MemI), .SysCALL_2(ex_mem_1_syscall_2), .EN(EN), .BNE(EXBNE), .BNE_2(ex_mem_1_bne_2), .BEQ(EXBEQ),
    .BEQ_2(ex_mem_1_beq_2), .J(EXJ), .EXJ(MemJ), .BGTZ(EXBGTZ), .EXBGTZ(ex_mem_1_exbgtz),
    .eq34(comparator_2_eq), .eq34_2(ex_mem_1_eq34_2), .R1(R2), .R1_2(ex_mem_1_r1_2), .LBU(id_ex_1_lbu_2),
    .LBU_2(ex_mem_1_lbu_2));
  and and_7 (and_7_out, ~EXEQ, ~EXles);  // AND_Gate
  or or_5 (EXBranch, EXJ[0], branch);
  // Probe on ex_mem_1_r2_2
  and and_8 (and_8_out, EXBGTZ, and_7_out);
  Counter #(.width(16), .max('hffff)) counter_6 (
    .count(EXBranch), .Q(\插入气泡数 ), .clk(CLK), .clr(RST));  // open: load, D, carry
  // MIPS_RAM mips_ram_1: pin names not known; wires that end beside it: ex_mem_1_beq_2, ex_mem_1_bne_2, ex_mem_1_exbgtz, ex_mem_1_alu_2[21:2], ex_mem_1_r2_2, ex_mem_1_memwrite_2, CLK, MEM_Mem2Reg, RST, mips_ram_1_p10
  and and_9 (and_9_out, EXEQ, EXBEQ);
  and and_10 (and_10_out, ~EXEQ, EXBNE);  // AND_Gate
  or or_6 (branch, and_9_out, and_8_out, and_10_out);
  MEM_WB mem_wb_1 (
    .nextPC(MEM_PC), .Reg_Write(Mem_RegWrite), .MemToReg(MEM_Mem2Reg), .DM(mips_ram_1_p10), .RegDst(MemDst),
    .ALU(ex_mem_1_alu_2), .RST(RST), .CLK(CLK), .IR(MemI), .SysCALL(ex_mem_1_syscall_2), .nextPC_2(WB_PC),
    .Reg_Write_2(TEN), .MemToReg_2(mem_wb_1_memtoreg_2), .DM_2(mem_wb_1_dm_2), .RegDst_2(mem_wb_1_regdst_2),
    .ALU_2(mem_wb_1_alu_2), .IR_2(mem_wb_1_ir_2), .SysCALL_2(out_2), .EN(EN), .EXJ(MemJ), .WBJ(WBJ),
    .LedData(ex_mem_1_r1_2), .LedData_2(mem_wb_1_leddata_2), .eq34(ex_mem_1_eq34_2), .eq34_2(out_1),
    .LBU(ex_mem_1_lbu_2), .WB_LBU(WB_LBU));  // open: R1_2, R1
  Counter #(.width(16), .max('hffff)) counter_7 (
    .count(branch), .Q(\条件分支成功数 ), .clk(CLK), .clr(RST));  // open: load, D, carry
  Multiplexer #(.width(32), .disabled(0), .enable("false")) multiplexer_26 (
    .in0(mem_wb_1_alu_2), .in1(mem_wb_1_dm_2), .out(multiplexer_26_out), .sel(mem_wb_1_memtoreg_2));
  // Probe on multiplexer_26_out
  Multiplexer #(.width(32), .disabled(0), .enable("false")) multiplexer_27 (
    .in0(mem_wb_1_dm_2), .in1({{24{1'b0}}, ByteEx}), .out(multiplexer_27_out), .sel(WB_LBU));
  Adder #(.width(32)) adder_5 (.a(WB_PC), .b(32'h4), .out(WBnextPC), .cin(1'b0));  // open: cout
  Register #(.width(32)) register_1 (.D(mem_wb_1_leddata_2), .en(out_1), .Q(LedData), .clk(CLK));  // open: clr
  Multiplexer #(.select(2), .width(8), .disabled(0), .enable("false")) multiplexer_28 (
    .in0(multiplexer_26_out[7:0]), .in1(multiplexer_26_out[15:8]), .in2(multiplexer_26_out[23:16]),
    .in3(multiplexer_26_out[31:24]), .out(ByteEx), .sel(mem_wb_1_alu_2[1:0]));

  // Other names for the same wires on the sheet: EXJMP = EXJ[0]; EXJR = EXJ[1]; EXJAL = EXJ[2]; Ins[5:0] = Func;
  //   OP[5:0] = Ins[31:26]; JMP = J[0]; JR = J[1]; JAL = J[2]; Jaddr[31:28] = EX_PC[31:28]; MemJMP = MemJ[0];
  //   MemJR = MemJ[1]; MemJAL = MemJ[2]; WBJMP = WBJ[0]; WBJR = WBJ[1]; WBJAL = WBJ[2]

  // Notes on the sheet:
  //   中断源
  //   中断等待指示
  //   数码管输出
  //   指令存储器
  //   contents of rom_1 (hex, n*v repeats v):
  //   20110001 8000c05 20110001 20120002 20130003 8000c09 20110001 20120002 20130003 8000c0d 20110001
  //   20120002 20130003 8000c11 20110001 20120002 20130003 c000cb8 20100001 20110001 118fc0 112020
  //   20020022 c 118882 12200001 8000c15 112020 20020022 c 20110001 118880 112020 20020022 c 12200001
  //   8000c1f 20110001 118fc0 112020 20020022 c 1188c3 112020 20020022 c 118903 112020 20020022 c 118903
  //   112020 20020022 c 118903 112020 20020022 c 118903 112020 20020022 c 118903 112020 20020022 c 118903
  //   112020 20020022 c 118903 112020 20020022 c 20100001 109fc0 139fc3 8021 2012000c 24160003 26100001
  //   3210000f 20080008 20090001 139900 2709825 132020 20020022 c 1094022 1500fff9 22100001 2018000f
  //   2188024 108700 20080008 20090001 139902 2709825 132021 20020022 c 1094022 1500fff9 108702 2c9b022
  //   12c00001 8000c50 4020 1084027 84400 3508ffff 82021 20020022 c 2010ffff 20110000 ae300000 22100001
  //   22310004 ae300000 22100001 22310004 ae300000 22100001 22310004 ae300000 22100001 22310004 ae300000
  //   22100001 22310004 ae300000 22100001 22310004 ae300000 22100001 22310004 ae300000 22100001 22310004
  //   ae300000 22100001 22310004 ae300000 22100001 22310004 ae300000 22100001 22310004 ae300000 22100001
  //   22310004 ae300000 22100001 22310004 ae300000 22100001 22310004 ae300000 22100001 22310004 ae300000
  //   22100001 22310004 22100001 8020 2011003c 8e130000 8e340000 274402a 11000002 ae330000 ae140000
  //   2231fffc 1611fff8 102020 20020022 c 22100004 2011003c 1611fff2 20020032 c 20100000 22100001 102020
  //   20020022 c 22100002 102020 20020022 c 22100003 102020 20020022 c 22100004 102020 20020022 c 22100005
  //   102020 20020022 c 22100006 102020 20020022 c 22100007 102020 20020022 c 22100008 102020 20020022
  //   20020022 c 3e00008
  //   contents of rom_2 (hex, n*v repeats v):
  //   20110020 20020022 8000c06 20110004 20120005 20130006 10000003 20110007 20120008 20130009 14110003
  //   2011000a 2012000b 2013000c c000c14 2002000a 0 0 0 c 2231ffff 0 0 0 112020 0 0 0 c 1620fff6 3e00008
  //   contents of rom_3 (hex, n*v repeats v):
  //   20110020 20020022 8000c06 20110004 20120005 20130006 10000003 20110007 20120008 20130009 14110003
  //   2011000a 2012000b 2013000c c000c14 2002000a 0 0 0 c 2231ffff 0 0 0 112020 0 0 0 c 1620fff6 3e00008
  //   rs
  //   rt
  //   rd
  //   OP
  //   Func
  //   MemToReg
  //   MemWrite
  //   AluOP
  //   AluSrcB
  //   RegWrite
  //   RegDst
  //   Syscall
  //   流水调试日志用
endmodule

module \预测器  (
  input  [31:0] IF_PCAddr,
  input  [31:0] EX_PCAddr,
  input  [31:0] BlockDataIn,
  input  BlkDataReady,
  input  CLK,
  output Miss,
  output [31:0] DataOut,
  output out_8
);

  wire adder_1_cout, adder_2_cout, adder_3_cout, adder_4_cout, adder_5_cout, adder_6_cout, adder_7_cout,
       adder_8_cout, and_1_out, and_2_out, and_3_out, and_4_out, and_5_out, and_6_out, and_7_out, and_8_out,
       and_9_out, and_10_out, and_11_out, and_12_out, and_13_out, and_14_out, and_15_out, and_16_out,
       and_17_out, and_26_out, comparator_1_eq, comparator_2_eq, comparator_3_eq, comparator_4_eq,
       comparator_5_eq, comparator_6_eq, comparator_7_eq, comparator_8_eq, comparator_9_eq, comparator_10_eq,
       comparator_11_eq, comparator_12_eq, comparator_13_eq, comparator_14_eq, comparator_15_eq,
       comparator_16_eq, Hit, Hit0, Hit1, Hit2, Hit3, Hit4, Hit5, Hit6, Hit7, or_1_out, Rd0, Rd1, Rd2, Rd3,
       Rd4, Rd5, Rd6, Rd7, Set0, Set1, Set2, Set3, Set4, Set5, Set6, Set7, V0, V1, V2, V3, V4, V5, V6, V7,
       Write, WriteHit;
  wire [2:0] delline, max3_1_max_num, max3_2_max_num, max3_3_max_num, max3_4_max_num, max3_5_max_num,
       max3_6_max_num;
  wire [7:0] demultiplexer_1_out0, multiplexer_17_out, multiplexer_18_out, multiplexer_20_out,
       multiplexer_21_out, prisetcache_1_st0, ser_1_s0, undriven, WriteSet;
  wire [15:0] adder_1_out, adder_2_out, adder_3_out, adder_4_out, adder_5_out, adder_6_out, adder_7_out,
       adder_8_out, C0, C1, C2, C3, C4, C5, C6, C7, max3_1_max, max3_2_max, max3_3_max, max3_4_max,
       max3_5_max, max3_6_max, multiplexer_9_out, multiplexer_10_out, multiplexer_11_out, multiplexer_12_out,
       multiplexer_13_out, multiplexer_14_out, multiplexer_15_out, multiplexer_16_out, NC0, NC1, NC2, NC3,
       NC4, NC5, NC6, NC7;
  wire [31:0] SlotData, Tag0, Tag1, Tag2, Tag3, Tag4, Tag5, Tag6, Tag7, \数据块副本_2_q , \数据块副本_3_q ,
       \数据块副本_4_q , \数据块副本_5_q , \数据块副本_6_q , \数据块副本_7_q , \数据块副本_8_q , \数据块副本_q ;

  and and_1 (and_1_out, Set0, BlkDataReady);
  and and_2 (and_2_out, Set1, BlkDataReady);
  and and_3 (and_3_out, Set2, BlkDataReady);
  and and_4 (and_4_out, Set3, BlkDataReady);
  and and_5 (and_5_out, Set4, BlkDataReady);
  and and_6 (and_6_out, Set5, BlkDataReady);
  and and_7 (and_7_out, Set6, BlkDataReady);
  and and_8 (and_8_out, Set7, BlkDataReady);
  Register #(.width(1)) VALID (.D(1'b1), .en(and_1_out), .Q(V0), .clk(CLK));  // open: clr
  Register #(.width(1)) VALID_2 (.D(1'b1), .en(and_2_out), .Q(V1), .clk(CLK));  // open: clr
  Register #(.width(1)) VALID_3 (.D(1'b1), .en(and_3_out), .Q(V2), .clk(CLK));  // open: clr
  Register #(.width(1)) VALID_4 (.D(1'b1), .en(and_4_out), .Q(V3), .clk(CLK));  // open: clr
  Register #(.width(1)) VALID_5 (.D(1'b1), .en(and_5_out), .Q(V4), .clk(CLK));  // open: clr
  Register #(.width(1)) VALID_6 (.D(1'b1), .en(and_6_out), .Q(V5), .clk(CLK));  // open: clr
  Register #(.width(1)) VALID_7 (.D(1'b1), .en(and_7_out), .Q(V6), .clk(CLK));  // open: clr
  Register #(.width(1)) VALID_8 (.D(1'b1), .en(and_8_out), .Q(V7), .clk(CLK));  // open: clr
  Adder #(.width(16)) adder_1 (.a(C0), .b(16'h1), .out(adder_1_out), .cout(adder_1_cout));  // open: cin
  and and_9 (and_9_out, ~adder_1_cout, V0);  // AND_Gate
  Adder #(.width(16)) adder_2 (.a(C1), .b(16'h1), .out(adder_2_out), .cout(adder_2_cout));  // open: cin
  and and_10 (and_10_out, ~adder_2_cout, V1);  // AND_Gate
  Adder #(.width(16)) adder_3 (.a(C2), .b(16'h1), .out(adder_3_out), .cout(adder_3_cout));  // open: cin
  and and_11 (and_11_out, ~adder_3_cout, V2);  // AND_Gate
  Adder #(.width(16)) adder_4 (.a(C3), .b(16'h1), .out(adder_4_out), .cout(adder_4_cout));  // open: cin
  and and_12 (and_12_out, ~adder_4_cout, V3);  // AND_Gate
  Adder #(.width(16)) adder_5 (.a(C4), .b(16'h1), .out(adder_5_out), .cout(adder_5_cout));  // open: cin
  and and_13 (and_13_out, ~adder_5_cout, V4);  // AND_Gate
  Adder #(.width(16)) adder_6 (.a(C5), .b(16'h1), .out(adder_6_out), .cout(adder_6_cout));  // open: cin
  and and_14 (and_14_out, ~adder_6_cout, V5);  // AND_Gate
  Adder #(.width(16)) adder_7 (.a(C6), .b(16'h1), .out(adder_7_out), .cout(adder_7_cout));  // open: cin
  and and_15 (and_15_out, ~adder_7_cout, V6);  // AND_Gate
  Adder #(.width(16)) adder_8 (.a(C7), .b(16'h1), .out(adder_8_out), .cout(adder_8_cout));  // open: cin
  and and_16 (and_16_out, ~adder_8_cout, V7);  // AND_Gate
  Multiplexer #(.width(16)) multiplexer_1 (.in0(C0), .in1(adder_1_out), .out(NC0), .sel(and_9_out));  // open: en
  Multiplexer #(.width(16)) multiplexer_2 (.in0(C1), .in1(adder_2_out), .out(NC1), .sel(and_10_out));  // open: en
  Multiplexer #(.width(16)) multiplexer_3 (.in0(C2), .in1(adder_3_out), .out(NC2), .sel(and_11_out));  // open: en
  Multiplexer #(.width(16)) multiplexer_4 (.in0(C3), .in1(adder_4_out), .out(NC3), .sel(and_12_out));  // open: en
  Multiplexer #(.width(16)) multiplexer_5 (.in0(C4), .in1(adder_5_out), .out(NC4), .sel(and_13_out));  // open: en
  Multiplexer #(.width(16)) multiplexer_6 (.in0(C5), .in1(adder_6_out), .out(NC5), .sel(and_14_out));  // open: en
  Multiplexer #(.width(16)) multiplexer_7 (.in0(C6), .in1(adder_7_out), .out(NC6), .sel(and_15_out));  // open: en
  Multiplexer #(.width(16)) multiplexer_8 (.in0(C7), .in1(adder_8_out), .out(NC7), .sel(and_16_out));  // open: en
  Register #(.width(32)) \u_标记位  (.D(EX_PCAddr), .en(and_1_out), .Q(Tag0), .clk(CLK));  // open: clr
  Register #(.width(32)) \u_标记位_2  (.D(EX_PCAddr), .en(and_2_out), .Q(Tag1), .clk(CLK));  // open: clr
  Register #(.width(32)) \u_标记位_3  (.D(EX_PCAddr), .en(and_3_out), .Q(Tag2), .clk(CLK));  // open: clr
  Register #(.width(32)) \u_标记位_4  (.D(EX_PCAddr), .en(and_4_out), .Q(Tag3), .clk(CLK));  // open: clr
  Register #(.width(32)) \u_标记位_5  (.D(EX_PCAddr), .en(and_5_out), .Q(Tag4), .clk(CLK));  // open: clr
  Register #(.width(32)) \u_标记位_6  (.D(EX_PCAddr), .en(and_6_out), .Q(Tag5), .clk(CLK));  // open: clr
  Register #(.width(32)) \u_标记位_7  (.D(EX_PCAddr), .en(and_7_out), .Q(Tag6), .clk(CLK));  // open: clr
  Register #(.width(32)) \u_标记位_8  (.D(EX_PCAddr), .en(and_8_out), .Q(Tag7), .clk(CLK));  // open: clr
  Multiplexer #(.width(16)) multiplexer_9 (
    .in0(NC0), .in1({16{1'b0}}), .out(multiplexer_9_out), .sel(Hit0));  // open: en
  Multiplexer #(.width(16)) multiplexer_10 (
    .in0(NC1), .in1({16{1'b0}}), .out(multiplexer_10_out), .sel(Hit1));  // open: en
  Multiplexer #(.width(16)) multiplexer_11 (
    .in0(NC2), .in1({16{1'b0}}), .out(multiplexer_11_out), .sel(Hit2));  // open: en
  Multiplexer #(.width(16)) multiplexer_12 (
    .in0(NC3), .in1({16{1'b0}}), .out(multiplexer_12_out), .sel(Hit3));  // open: en
  Multiplexer #(.width(16)) multiplexer_13 (
    .in0(NC4), .in1({16{1'b0}}), .out(multiplexer_13_out), .sel(Hit4));  // open: en
  Multiplexer #(.width(16)) multiplexer_14 (
    .in0(NC5), .in1({16{1'b0}}), .out(multiplexer_14_out), .sel(Hit5));  // open: en
  Multiplexer #(.width(16)) multiplexer_15 (
    .in0(NC6), .in1({16{1'b0}}), .out(multiplexer_15_out), .sel(Hit6));  // open: en
  Multiplexer #(.width(16)) multiplexer_16 (
    .in0(NC7), .in1({16{1'b0}}), .out(multiplexer_16_out), .sel(Hit7));  // open: en
  assign DataOut = 1'b1 ? SlotData : 32'bz;  // Controlled_Buffer controlled_buffer_1
  Register #(.width(16)) \u_淘汰标志位  (.D(multiplexer_9_out), .Q(C0), .clk(CLK));  // open: en, clr
  Register #(.width(16)) \u_淘汰标志位_2  (.D(multiplexer_10_out), .Q(C1), .clk(CLK));  // open: en, clr
  Register #(.width(16)) \u_淘汰标志位_3  (.D(multiplexer_11_out), .Q(C2), .clk(CLK));  // open: en, clr
  Register #(.width(16)) \u_淘汰标志位_4  (.D(multiplexer_12_out), .Q(C3), .clk(CLK));  // open: en, clr
  Register #(.width(16)) \u_淘汰标志位_5  (.D(multiplexer_13_out), .Q(C4), .clk(CLK));  // open: en, clr
  Register #(.width(16)) \u_淘汰标志位_6  (.D(multiplexer_14_out), .Q(C5), .clk(CLK));  // open: en, clr
  Register #(.width(16)) \u_淘汰标志位_7  (.D(multiplexer_15_out), .Q(C6), .clk(CLK));  // open: en, clr
  Register #(.width(16)) \u_淘汰标志位_8  (.D(multiplexer_16_out), .Q(C7), .clk(CLK));  // open: en, clr
  Register #(.width(32)) \u_数据块副本  (.D(BlockDataIn), .en(and_1_out), .Q(\数据块副本_q ), .clk(CLK));  // open: clr
  Register #(.width(32)) \u_数据块副本_2  (.D(BlockDataIn), .en(and_2_out), .Q(\数据块副本_2_q ), .clk(CLK));  // open: clr
  Register #(.width(32)) \u_数据块副本_3  (.D(BlockDataIn), .en(and_3_out), .Q(\数据块副本_3_q ), .clk(CLK));  // open: clr
  Register #(.width(32)) \u_数据块副本_4  (.D(BlockDataIn), .en(and_4_out), .Q(\数据块副本_4_q ), .clk(CLK));  // open: clr
  Register #(.width(32)) \u_数据块副本_5  (.D(BlockDataIn), .en(and_5_out), .Q(\数据块副本_5_q ), .clk(CLK));  // open: clr
  Register #(.width(32)) \u_数据块副本_6  (.D(BlockDataIn), .en(and_6_out), .Q(\数据块副本_6_q ), .clk(CLK));  // open: clr
  Register #(.width(32)) \u_数据块副本_7  (.D(BlockDataIn), .en(and_7_out), .Q(\数据块副本_7_q ), .clk(CLK));  // open: clr
  Register #(.width(32)) \u_数据块副本_8  (.D(BlockDataIn), .en(and_8_out), .Q(\数据块副本_8_q ), .clk(CLK));  // open: clr
  PriSetCache prisetcache_1 (
    .V0(V0), .V1(V1), .V2(V2), .V3(V3), .V4(V4), .V5(V5), .V6(V6), .V7(V7), .st0(prisetcache_1_st0[0]),
    .st1(prisetcache_1_st0[1]), .st2(prisetcache_1_st0[2]), .st3(prisetcache_1_st0[3]),
    .st4(prisetcache_1_st0[4]), .st5(prisetcache_1_st0[5]), .st6(prisetcache_1_st0[6]),
    .st7(prisetcache_1_st0[7]));
  Multiplexer #(.select(3), .width(8)) multiplexer_17 (
    .in0(8'h1), .in1(8'h2), .in2(8'h4), .in3(8'h8), .in4(8'h10), .in5(8'h20), .in6(8'h40), .in7(8'h80),
    .out(multiplexer_17_out), .sel(delline));  // open: en
  and and_17 (and_17_out, V0, V1, V2, V3, V4, V5, V6, V7);
  assign SlotData = Rd0 ? \数据块副本_q  : 32'bz;  // Controlled_Buffer controlled_buffer_2
  assign SlotData = Rd1 ? \数据块副本_2_q  : 32'bz;  // Controlled_Buffer controlled_buffer_3
  assign SlotData = Rd2 ? \数据块副本_3_q  : 32'bz;  // Controlled_Buffer controlled_buffer_4
  assign SlotData = Rd3 ? \数据块副本_4_q  : 32'bz;  // Controlled_Buffer controlled_buffer_5
  assign SlotData = Rd4 ? \数据块副本_5_q  : 32'bz;  // Controlled_Buffer controlled_buffer_6
  assign SlotData = Rd5 ? \数据块副本_6_q  : 32'bz;  // Controlled_Buffer controlled_buffer_7
  assign SlotData = Rd6 ? \数据块副本_7_q  : 32'bz;  // Controlled_Buffer controlled_buffer_8
  assign SlotData = Rd7 ? \数据块副本_8_q  : 32'bz;  // Controlled_Buffer controlled_buffer_9
  Multiplexer #(.width(8)) multiplexer_18 (
    .in0(prisetcache_1_st0), .in1(multiplexer_17_out), .out(multiplexer_18_out), .sel(and_17_out));  // open: en
  Multiplexer #(.width(8)) multiplexer_19 (
    .in0(multiplexer_18_out), .in1(WriteSet), .out({Set7, Set6, Set5, Set4, Set3, Set2, Set1, Set0}),
    .sel(WriteHit));  // open: en
  Max3 max3_1 (.Y(C1), .X(C0), .Y_num(3'b001), .X_num(3'b000), .MAX(max3_1_max), .Max_num(max3_1_max_num));
  Max3 max3_2 (.Y(C3), .X(C2), .Y_num(3'b011), .X_num(3'b010), .MAX(max3_2_max), .Max_num(max3_2_max_num));
  Max3 max3_3 (.Y(C5), .X(C4), .Y_num(3'b101), .X_num(3'b100), .MAX(max3_3_max), .Max_num(max3_3_max_num));
  Max3 max3_4 (.Y(C7), .X(C6), .Y_num(3'b111), .X_num(3'b110), .MAX(max3_4_max), .Max_num(max3_4_max_num));
  Demultiplexer #(.select(3)) demultiplexer_1 (
    .out0(demultiplexer_1_out0[0]), .out1(demultiplexer_1_out0[1]), .out2(demultiplexer_1_out0[2]),
    .out3(demultiplexer_1_out0[3]), .out4(demultiplexer_1_out0[4]), .out5(demultiplexer_1_out0[5]),
    .out6(demultiplexer_1_out0[6]), .out7(demultiplexer_1_out0[7]), .in(1'b1), .sel(delline));  // open: en
  Comparator #(.width(32)) comparator_1 (.a(Tag0), .b(IF_PCAddr), .eq(comparator_1_eq));  // open: gt, lt
  Comparator #(.width(32)) comparator_2 (.a(Tag1), .b(IF_PCAddr), .eq(comparator_2_eq));  // open: gt, lt
  Comparator #(.width(32)) comparator_3 (.a(Tag2), .b(IF_PCAddr), .eq(comparator_3_eq));  // open: gt, lt
  Comparator #(.width(32)) comparator_4 (.a(Tag3), .b(IF_PCAddr), .eq(comparator_4_eq));  // open: gt, lt
  Comparator #(.width(32)) comparator_5 (.a(Tag4), .b(IF_PCAddr), .eq(comparator_5_eq));  // open: gt, lt
  Comparator #(.width(32)) comparator_6 (.a(Tag5), .b(IF_PCAddr), .eq(comparator_6_eq));  // open: gt, lt
  Comparator #(.width(32)) comparator_7 (.a(Tag6), .b(IF_PCAddr), .eq(comparator_7_eq));  // open: gt, lt
  Comparator #(.width(32)) comparator_8 (.a(Tag7), .b(IF_PCAddr), .eq(comparator_8_eq));  // open: gt, lt
  Max3 max3_5 (
    .Y(max3_2_max), .X(max3_1_max), .Y_num(max3_2_max_num), .X_num(max3_1_max_num), .MAX(max3_5_max),
    .Max_num(max3_5_max_num));
  Max3 max3_6 (
    .Y(max3_4_max), .X(max3_3_max), .Y_num(max3_4_max_num), .X_num(max3_3_max_num), .MAX(max3_6_max),
    .Max_num(max3_6_max_num));
  and and_18 (Rd0, comparator_1_eq, V0);
  and and_19 (Rd1, comparator_2_eq, V1);
  and and_20 (Rd2, comparator_3_eq, V2);
  and and_21 (Rd3, comparator_4_eq, V3);
  and and_22 (Rd4, comparator_5_eq, V4);
  and and_23 (Rd5, comparator_6_eq, V5);
  and and_24 (Rd6, comparator_7_eq, V6);
  and and_25 (Rd7, comparator_8_eq, V7);
  Max3 max3_7 (
    .Y(max3_6_max), .X(max3_5_max), .Y_num(max3_6_max_num), .X_num(max3_5_max_num), .Max_num(delline));  // open: MAX
  Ser ser_1 (
    .V0(V0), .V1(V1), .V2(V2), .V3(V3), .V4(V4), .V5(V5), .V6(V6), .V7(V7), .S0(ser_1_s0[0]),
    .S1(ser_1_s0[1]), .S2(ser_1_s0[2]), .S3(ser_1_s0[3]), .S4(ser_1_s0[4]), .S5(ser_1_s0[5]),
    .S6(ser_1_s0[6]), .S7(ser_1_s0[7]));
  and and_26 (and_26_out, V0, V1, V2, V3, V4, V5, V6, V7);
  or or_1 (or_1_out, Rd0, Rd1, Rd2, Rd3, Rd4, Rd5, Rd6, Rd7);
  Multiplexer #(.width(8), .enable("false")) multiplexer_20 (
    .in0(ser_1_s0), .in1(demultiplexer_1_out0), .out(multiplexer_20_out), .sel(and_26_out));
  Multiplexer #(.width(8), .enable("false")) multiplexer_21 (
    .in0(multiplexer_20_out), .in1(undriven), .out(multiplexer_21_out), .sel(Write));
  not not_1 (Miss, or_1_out);
  Comparator #(.width(32)) comparator_9 (.a(Tag0), .b(EX_PCAddr), .eq(comparator_9_eq));  // open: gt, lt
  Comparator #(.width(32)) comparator_10 (.a(Tag1), .b(EX_PCAddr), .eq(comparator_10_eq));  // open: gt, lt
  Comparator #(.width(32)) comparator_11 (.a(Tag2), .b(EX_PCAddr), .eq(comparator_11_eq));  // open: gt, lt
  Comparator #(.width(32)) comparator_12 (.a(Tag3), .b(EX_PCAddr), .eq(comparator_12_eq));  // open: gt, lt
  Comparator #(.width(32)) comparator_13 (.a(Tag4), .b(EX_PCAddr), .eq(comparator_13_eq));  // open: gt, lt
  Comparator #(.width(32)) comparator_14 (.a(Tag5), .b(EX_PCAddr), .eq(comparator_14_eq));  // open: gt, lt
  Comparator #(.width(32)) comparator_15 (.a(Tag6), .b(EX_PCAddr), .eq(comparator_15_eq));  // open: gt, lt
  Comparator #(.width(32)) comparator_16 (.a(Tag7), .b(EX_PCAddr), .eq(comparator_16_eq));  // open: gt, lt
  and and_27 (WriteSet[0], comparator_9_eq, V0);
  and and_28 (WriteSet[1], comparator_10_eq, V1);
  and and_29 (WriteSet[2], comparator_11_eq, V2);
  and and_30 (WriteSet[3], comparator_12_eq, V3);
  and and_31 (WriteSet[4], comparator_13_eq, V4);
  and and_32 (WriteSet[5], comparator_14_eq, V5);
  and and_33 (WriteSet[6], comparator_15_eq, V6);
  and and_34 (WriteSet[7], comparator_16_eq, V7);
  or or_2 (Hit0, WriteSet[0], Rd0);
  or or_3 (Hit1, WriteSet[1], Rd1);
  or or_4 (Hit2, WriteSet[2], Rd2);
  or or_5 (Hit3, WriteSet[3], Rd3);
  or or_6 (Hit4, WriteSet[4], Rd4);
  or or_7 (Hit5, WriteSet[5], Rd5);
  or or_8 (Hit6, WriteSet[6], Rd6);
  or or_9 (Hit7, WriteSet[7], Rd7);
  or or_10 (WriteHit, WriteSet[0], WriteSet[1], WriteSet[2], WriteSet[3], WriteSet[4], WriteSet[5], WriteSet[6], WriteSet[7]);
  or or_11 (Hit, WriteHit, or_1_out);

  assign out_8 = Miss;

  // Other names for the same wires on the sheet: BlkReady = BlkDataReady; NextPC[31:0] = BlockDataIn;
  //   TagRead[31:0] = IF_PCAddr; TagWrite[31:0] = EX_PCAddr

  // Notes on the sheet:
  //   输入引脚区
  //   请勿增改引脚，请勿修改子电路封装
  //   电路功能：利用上面给定的隧道构建8行的Cache，cache映射方式自选
  //   请在下方利用上方输入输出引脚的隧道信号构建电路，ctrl+d复制选择部件
  //   输出引脚区
endmodule

module Max3 (
  input  [15:0] Y,
  input  [15:0] X,
  input  [2:0] Y_num,
  input  [2:0] X_num,
  output [15:0] MAX,
  output [2:0] Max_num
);

  wire comparator_1_eq, comparator_1_gt, or_1_out;

  Multiplexer #(.width(16), .enable("false")) multiplexer_1 (.in0(Y), .in1(X), .out(MAX), .sel(or_1_out));
  Comparator #(.width(16), .mode("unsigned")) comparator_1 (
    .a(X), .b(Y), .gt(comparator_1_gt), .eq(comparator_1_eq));  // open: lt
  or or_1 (or_1_out, comparator_1_gt, comparator_1_eq);
  Multiplexer #(.width(3), .enable("false")) multiplexer_2 (.in0(Y_num), .in1(X_num), .out(Max_num), .sel(or_1_out));

  // Notes on the sheet:
  //   输出两个输入中的较大值，并输出较大值的3位编号
endmodule
module FSM (
  input  success,
  input  pre_high,
  input  pre_low,
  output after_high,
  output after_low
);

  wire and_1_out, and_2_out, and_3_out, and_4_out, not_1_out, not_2_out, not_3_out, not_4_out, not_5_out;

  not not_1 (not_1_out, pre_low);
  not not_2 (not_2_out, success);
  not not_3 (not_3_out, pre_low);
  not not_4 (not_4_out, pre_high);
  not not_5 (not_5_out, pre_low);
  and and_1 (and_1_out, pre_high, not_1_out);
  and and_2 (and_2_out, success, pre_low);
  and and_3 (and_3_out, not_2_out, pre_high, not_3_out);
  and and_4 (and_4_out, success, not_4_out, not_5_out);
  or or_1 (after_high, and_1_out, and_2_out);
  or or_2 (after_low, and_3_out, and_4_out);
endmodule

module Ser (
  input  V0,
  input  V1,
  input  V2,
  input  V3,
  input  V4,
  input  V5,
  input  V6,
  input  V7,
  output S0,
  output S1,
  output S2,
  output S3,
  output S4,
  output S5,
  output S6,
  output S7
);

  wire not_2_out, not_3_out, not_4_out, not_5_out, not_6_out, not_7_out, not_8_out;

  not not_1 (S0, V0);
  and and_1 (S1, V0, not_2_out);
  not not_2 (not_2_out, V1);
  and and_2 (S2, V0, V1, not_3_out);
  not not_3 (not_3_out, V2);
  not not_4 (not_4_out, V3);
  not not_5 (not_5_out, V4);
  not not_6 (not_6_out, V5);
  not not_7 (not_7_out, V6);
  not not_8 (not_8_out, V7);
  and and_3 (S3, V0, V1, V2, not_4_out);
  and and_4 (S4, V0, V1, V2, V3, not_5_out);
  and and_5 (S5, V0, V1, V2, V3, V4, not_6_out);
  and and_6 (S6, V0, V1, V2, V3, V4, V5, not_7_out);
  and and_7 (S7, V0, V1, V2, V3, V4, V5, V6, not_8_out);
endmodule

module \跳转指令判断器  (
  input  [31:0] IR,
  output IFbra
);

  wire and_1_out, comparator_1_eq, comparator_2_eq, comparator_3_eq, comparator_4_eq, comparator_5_eq,
       comparator_6_eq;

  Comparator #(.width(6)) comparator_1 (.a(IR[31:26]), .b(6'b000100), .eq(comparator_1_eq));  // open: gt, lt
  Comparator #(.width(6)) comparator_2 (.a(IR[31:26]), .b(6'b000101), .eq(comparator_2_eq));  // open: gt, lt
  Comparator #(.width(6)) comparator_3 (.a(IR[31:26]), .b(6'b000010), .eq(comparator_3_eq));  // open: gt, lt
  Comparator #(.width(6)) comparator_4 (.a(IR[31:26]), .b(6'b000011), .eq(comparator_4_eq));  // open: gt, lt
  Comparator #(.width(6)) comparator_5 (.a(IR[31:26]), .b({6{1'b0}}), .eq(comparator_5_eq));  // open: gt, lt
  Comparator #(.width(6)) comparator_6 (.a(IR[5:0]), .b(6'b001000), .eq(comparator_6_eq));  // open: gt, lt
  and and_1 (and_1_out, comparator_5_eq, comparator_6_eq);
  or or_1 (IFbra, comparator_1_eq, comparator_2_eq, comparator_3_eq, comparator_4_eq, and_1_out);

  // Notes on the sheet:
  //   BEQ
  //   BNE
  //   J
  //   JAL
  //   JR
endmodule

module PriSetCache (
  input  V0,
  input  V1,
  input  V2,
  input  V3,
  input  V4,
  input  V5,
  input  V6,
  input  V7,
  output st0,
  output st1,
  output st2,
  output st3,
  output st4,
  output st5,
  output st6,
  output st7
);

  wire not_2_out, not_3_out, not_4_out, not_5_out, not_6_out, not_7_out;

  not not_1 (st0, V0);
  and and_1 (st1, V0, not_2_out);
  not not_2 (not_2_out, V1);
  and and_2 (st2, V1, not_3_out);
  not not_3 (not_3_out, V2);
  and and_3 (st3, V2, not_4_out);
  not not_4 (not_4_out, V3);
  and and_4 (st4, V3, not_5_out);
  not not_5 (not_5_out, V4);
  and and_5 (st5, V4, not_6_out);
  not not_6 (not_6_out, V5);
  and and_6 (st6, V5, not_7_out);
  not not_7 (not_7_out, V6);

  assign st7 = V6;
endmodule
